// Logisim project ALU.circ as structural Verilog: 17 circuits, main circuit 1位全加器
// FA
module \_1位全加器  (
  input  X,
  input  Y,
  input  Cin,
  output Cout,
  output S
);

  wire and_1_out, and_2_out, and_3_out;

  and and_1 (and_1_out, X, Y);
  or or_1 (Cout, and_1_out, and_2_out, and_3_out);
  and and_2 (and_2_out, Y, Cin);
  and and_3 (and_3_out, X, Cin);
  xor xor_1 (S, Y, X, Cin);

  // Notes on the sheet:
  //   输入信号
  //   逻辑表达式：S=X^Y^Cin;                        //此语句中^分别为异或运算
  //   功能说明：全加器Verilog对应的描述语句：assign {Cout,S}=X+Y+Cin;//此语句中的+为算术加运算
  //   逻辑表达式：Cout=X&Y|Y&Cin|Cin&X；//此语句中&,|分别为与、或运算
  //   以上管脚名称及位置均不要移动，利用下方的隧道信号用画电路图方式设计1位全加器
  //   输出信号
endmodule

// AddSub
module \_8位可控加减法器  (
  input  sub,
  input  [7:0] X,
  input  [7:0] Y,
  output [7:0] S,
  output overflow,
  output Cout
);

  wire \n1位全加器_1_cout , \n1位全加器_2_cout , \n1位全加器_3_cout , \n1位全加器_4_cout , \n1位全加器_5_cout , \n1位全加器_6_cout ,
       \n1位全加器_7_cout , \n1位全加器_8_cout , xor_3_out, xor_4_out, xor_5_out, xor_6_out, xor_7_out, xor_8_out,
       xor_9_out, xor_10_out;

  xor xor_1 (overflow, \n1位全加器_2_cout , \n1位全加器_1_cout );
  xor xor_2 (Cout, \n1位全加器_1_cout , sub);
  // Probe on X
  // Probe on X
  \_1位全加器  \u_1位全加器_1  (.X(X[7]), .Y(xor_4_out), .Cin(\n1位全加器_2_cout ), .Cout(\n1位全加器_1_cout ), .S(S[7]));
  // Probe on Y
  // Probe on Y
  \_1位全加器  \u_1位全加器_2  (.X(X[6]), .Y(xor_3_out), .Cin(\n1位全加器_3_cout ), .Cout(\n1位全加器_2_cout ), .S(S[6]));
  xor xor_3 (xor_3_out, Y[6], sub);
  xor xor_4 (xor_4_out, Y[7], sub);
  \_1位全加器  \u_1位全加器_3  (.X(X[5]), .Y(xor_5_out), .Cin(\n1位全加器_4_cout ), .Cout(\n1位全加器_3_cout ), .S(S[5]));
  xor xor_5 (xor_5_out, Y[5], sub);
  \_1位全加器  \u_1位全加器_4  (.X(X[4]), .Y(xor_6_out), .Cin(\n1位全加器_5_cout ), .Cout(\n1位全加器_4_cout ), .S(S[4]));
  \_1位全加器  \u_1位全加器_5  (.X(X[3]), .Y(xor_7_out), .Cin(\n1位全加器_6_cout ), .Cout(\n1位全加器_5_cout ), .S(S[3]));
  xor xor_6 (xor_6_out, Y[4], sub);
  // Probe on S
  // Probe on S
  \_1位全加器  \u_1位全加器_6  (.X(X[2]), .Y(xor_8_out), .Cin(\n1位全加器_8_cout ), .Cout(\n1位全加器_6_cout ), .S(S[2]));
  xor xor_7 (xor_7_out, Y[3], sub);
  xor xor_8 (xor_8_out, Y[2], sub);
  \_1位全加器  \u_1位全加器_7  (.X(X[0]), .Y(xor_9_out), .Cin(sub), .Cout(\n1位全加器_7_cout ), .S(S[0]));
  \_1位全加器  \u_1位全加器_8  (.X(X[1]), .Y(xor_10_out), .Cin(\n1位全加器_7_cout ), .Cout(\n1位全加器_8_cout ), .S(S[1]));
  xor xor_9 (xor_9_out, Y[0], sub);
  xor xor_10 (xor_10_out, Y[1], sub);

  // Notes on the sheet:
  //   输入管脚
  //   逻辑功能：8位可控加减法器，sub=0时为加法，sub=1时为减法；overflow为有符号数溢出位，Cout为加法进位或减法借位
  //   以上管脚名称及位置均不要移动，利用下方的隧道信号用画电路图方式设计8位可控加减法器
  //   输出管脚
endmodule

module \_4位先行进位逻辑  (
  input  G3,
  input  P3,
  input  G2,
  input  P2,
  input  G1,
  input  P1,
  input  G0,
  input  P0,
  input  Cin,
  output C4,
  output C3,
  output C2,
  output C1,
  output G_star,
  output P_star
);

  wire and_2_out, and_3_out, and_4_out, and_5_out, and_6_out, and_7_out, and_8_out, and_9_out, and_10_out,
       and_11_out;

  and and_1 (P_star, P0, P1, P2, P3);
  or or_1 (G_star, and_4_out, and_3_out, and_2_out, G3);
  or or_2 (C4, G3, and_2_out, and_3_out, and_4_out, and_5_out);
  and and_2 (and_2_out, P3, G2);
  and and_3 (and_3_out, P3, P2, G1);
  and and_4 (and_4_out, P3, P2, P1, G0);
  and and_5 (and_5_out, P3, P2, P1, P0, Cin);
  or or_3 (C3, G2, and_6_out, and_8_out, and_7_out);
  and and_6 (and_6_out, P2, G1);
  and and_7 (and_7_out, P2, P1, P0, Cin);
  and and_8 (and_8_out, P2, P1, G0);
  or or_4 (C2, G1, and_9_out, and_10_out);
  and and_9 (and_9_out, P1, G0);
  or or_5 (C1, G0, and_11_out);
  and and_10 (and_10_out, P1, P0, Cin);
  and and_11 (and_11_out, P0, Cin);

  // Notes on the sheet:
  //   逻辑功能：
  //   4先行进位传递公式为：C1=G0+P0·Cin
  //   输入管脚
  //   C2=G1+P1·C1=G1+P1·G0+P1·P0·Cin
  //   串行进位传递公式为：Ci+1=Xi·Yi+(Xi㈩Yi)·Ci=Gi+Pi·Ci；          //其中的·,＋,㈩分别为逻辑与、或、异或运算
  //   C3=G2+P2·C2=G2+P2·G1+P2·P1·G0+P2·P1·P0·Cin
  //   C4=G3+P3·C3=G3+P3·G2+P3·P2·G1+P3·P2·P1·G0+P3·P2·P1·P0·Cin=G*+P*·Cin
  //   以上管脚名称及位置均不要移动，利用下方的隧道信号用画电路图方式设计4位先行进位逻辑
  //   输出管脚
endmodule

module \_4位快速进位加法器  (
  input  [3:0] Y,
  input  [3:0] X,
  input  Cin,
  output C3,
  output C4,
  output [3:0] S,
  output G_star,
  output P_star
);

  wire and_1_out, and_2_out, and_3_out, and_4_out, \n4位先行进位逻辑_1_c1 , \n4位先行进位逻辑_1_c2 , xor_2_out, xor_3_out,
       xor_5_out, xor_8_out;

  // Probe on Y
  // Probe on Y
  // Probe on X
  // Probe on X
  and and_1 (and_1_out, Y[3], X[3]);
  xor xor_1 (S[3], xor_2_out, C3);
  xor xor_2 (xor_2_out, Y[3], X[3]);
  \_4位先行进位逻辑  \u_4位先行进位逻辑_1  (
    .G3(and_1_out), .P3(xor_2_out), .G2(and_2_out), .P2(xor_3_out), .G1(and_3_out), .P1(xor_5_out),
    .G0(and_4_out), .P0(xor_8_out), .Cin(Cin), .C4(C4), .C3(C3), .C2(\n4位先行进位逻辑_1_c2 ),
    .C1(\n4位先行进位逻辑_1_c1 ), .G_star(G_star), .P_star(P_star));
  and and_2 (and_2_out, Y[2], X[2]);
  xor xor_3 (xor_3_out, Y[2], X[2]);
  xor xor_4 (S[2], xor_3_out, \n4位先行进位逻辑_1_c2 );
  and and_3 (and_3_out, Y[1], X[1]);
  // Probe on S
  // Probe on S
  xor xor_5 (xor_5_out, Y[1], X[1]);
  xor xor_6 (S[1], xor_5_out, \n4位先行进位逻辑_1_c1 );
  and and_4 (and_4_out, Y[0], X[0]);
  xor xor_7 (S[0], xor_8_out, Cin);
  xor xor_8 (xor_8_out, Y[0], X[0]);

  // Notes on the sheet:
  //   逻辑功能：
  //   进位生成逻辑：P0=X0㈩Y0
  //   P1=X1㈩Y1
  //   P2=X2㈩Y2
  //   输入管脚
  //   P3=X3㈩Y3
  //   进位传递逻辑：G0=X0·Y0
  //   G1=X1·Y1
  //   G2=X2·Y2
  //   G3=X3·Y3
  //   以上管脚名称及位置均不要移动，利用下方的隧道信号用画电路图方式设计4位先行进位逻辑
  //   输出管脚
  //   加法结果：S0=P0㈩Cin
  //   S1=P1㈩C1
  //   S2=P2㈩C2
  //   S3=P3㈩C3
endmodule

module \_16位快速进位加法器  (
  input  [15:0] Y,
  input  [15:0] X,
  input  Cin,
  output C15,
  output C16,
  output [15:0] S,
  output G_star,
  output P_star
);

  wire \n4位先行进位逻辑_1_c1 , \n4位先行进位逻辑_1_c2 , \n4位先行进位逻辑_1_c3 , \n4位快速进位加法器_1_g_star , \n4位快速进位加法器_1_p_star ,
       \n4位快速进位加法器_2_g_star , \n4位快速进位加法器_2_p_star , \n4位快速进位加法器_3_g_star , \n4位快速进位加法器_3_p_star ,
       \n4位快速进位加法器_4_g_star , \n4位快速进位加法器_4_p_star ;

  // Probe on Y
  // Probe on Y
  // Probe on X
  // Probe on X
  \_4位快速进位加法器  \u_4位快速进位加法器_1  (
    .Y(X[15:12]), .X(Y[15:12]), .Cin(\n4位先行进位逻辑_1_c3 ), .S(S[15:12]), .G_star(\n4位快速进位加法器_1_g_star ),
    .P_star(\n4位快速进位加法器_1_p_star ), .C3(C15));  // open: C4
  \_4位先行进位逻辑  \u_4位先行进位逻辑_1  (
    .G3(\n4位快速进位加法器_1_g_star ), .P3(\n4位快速进位加法器_1_p_star ), .G2(\n4位快速进位加法器_2_g_star ),
    .P2(\n4位快速进位加法器_2_p_star ), .G1(\n4位快速进位加法器_3_g_star ), .P1(\n4位快速进位加法器_3_p_star ),
    .G0(\n4位快速进位加法器_4_g_star ), .P0(\n4位快速进位加法器_4_p_star ), .Cin(Cin), .C4(C16), .C3(\n4位先行进位逻辑_1_c3 ),
    .C2(\n4位先行进位逻辑_1_c2 ), .C1(\n4位先行进位逻辑_1_c1 ), .G_star(G_star), .P_star(P_star));
  \_4位快速进位加法器  \u_4位快速进位加法器_2  (
    .Y(X[11:8]), .X(Y[11:8]), .Cin(\n4位先行进位逻辑_1_c2 ), .S(S[11:8]), .G_star(\n4位快速进位加法器_2_g_star ),
    .P_star(\n4位快速进位加法器_2_p_star ));  // open: C4, C3
  \_4位快速进位加法器  \u_4位快速进位加法器_3  (
    .Y(X[7:4]), .X(Y[7:4]), .Cin(\n4位先行进位逻辑_1_c1 ), .S(S[7:4]), .G_star(\n4位快速进位加法器_3_g_star ),
    .P_star(\n4位快速进位加法器_3_p_star ));  // open: C4, C3
  \_4位快速进位加法器  \u_4位快速进位加法器_4  (
    .Y(X[3:0]), .X(Y[3:0]), .Cin(Cin), .S(S[3:0]), .G_star(\n4位快速进位加法器_4_g_star ),
    .P_star(\n4位快速进位加法器_4_p_star ));  // open: C4, C3
  // Probe on S
  // Probe on S

  // Notes on the sheet:
  //   输入管脚
  //   逻辑功能：利用4位先行进位加法器及4位先行进位信号，级联生成片内并行及片间并行进位的16位加法器
  //   以上管脚名称及位置均不要移动，利用下方的隧道信号用画电路图方式设计16位先行进位逻辑（只需连接进位信号）
  //   输出管脚
endmodule

module \_32位快速进位加法器  (
  input  [31:0] X,
  input  [31:0] Y,
  input  Cin,
  output C31,
  output C32,
  output [31:0] S
);

  wire \n4位先行进位逻辑_1_c1 , \n16位快速进位加法器_1_g_star , \n16位快速进位加法器_1_p_star , \n16位快速进位加法器_2_g_star ,
       \n16位快速进位加法器_2_p_star ;

  // Probe on X
  // Probe on X
  // Probe on Y
  // Probe on Y
  \_4位先行进位逻辑  \u_4位先行进位逻辑_1  (
    .G1(\n16位快速进位加法器_1_g_star ), .P1(\n16位快速进位加法器_1_p_star ), .G0(\n16位快速进位加法器_2_g_star ),
    .P0(\n16位快速进位加法器_2_p_star ), .Cin(Cin), .C2(C32), .C1(\n4位先行进位逻辑_1_c1 ));  // open: G3, P3, G2, P2, C4, C3, G_star, P_star
  \_16位快速进位加法器  \u_16位快速进位加法器_1  (
    .Y(Y[31:16]), .X(X[31:16]), .Cin(\n4位先行进位逻辑_1_c1 ), .S(S[31:16]), .G_star(\n16位快速进位加法器_1_g_star ),
    .P_star(\n16位快速进位加法器_1_p_star ), .C15(C31));  // open: C16
  \_16位快速进位加法器  \u_16位快速进位加法器_2  (
    .Y(Y[15:0]), .X(X[15:0]), .Cin(Cin), .S(S[15:0]), .G_star(\n16位快速进位加法器_2_g_star ),
    .P_star(\n16位快速进位加法器_2_p_star ));  // open: C16, C15
  // Probe on S
  // Probe on S

  // Notes on the sheet:
  //   输入管脚
  //   逻辑功能：利用16位先行进位加法器及4位先行进位信号，级联生成片内并行及片间并行进位的32位加法器
  //   以上管脚名称及位置均不要移动，利用下方的隧道信号用画电路图方式设计32位先行进位逻辑（只需连接进位信号）
  //   输出管脚
endmodule

// 32位逻辑右移寄存器
module \_32位逻辑右移寄存器_已设计完成  (
  input  [31:0] X,
  input  [31:0] Y,
  output [31:0] result_srl
);

  Multiplexer #(.select(5), .width(1), .disabled("Z"), .enable("false")) multiplexer_1 (
    .in0(X[0]), .in1(X[1]), .in2(X[2]), .in3(X[3]), .in4(X[4]), .in5(X[5]), .in6(X[6]), .in7(X[7]),
    .in8(X[8]), .in9(X[9]), .in10(X[10]), .in11(X[11]), .in12(X[12]), .in13(X[13]), .in14(X[14]),
    .in15(X[15]), .in16(X[16]), .in17(X[17]), .in18(X[18]), .in19(X[19]), .in20(X[20]), .in21(X[21]),
    .in22(X[22]), .in23(X[23]), .in24(X[24]), .in25(X[25]), .in26(X[26]), .in27(X[27]), .in28(X[28]),
    .in29(X[29]), .in30(X[30]), .in31(X[31]), .out(result_srl[0]), .sel(Y[4:0]));
  Multiplexer #(.select(5), .width(1), .disabled("Z"), .enable("false")) multiplexer_2 (
    .in0(X[1]), .in1(X[2]), .in2(X[3]), .in3(X[4]), .in4(X[5]), .in5(X[6]), .in6(X[7]), .in7(X[8]),
    .in8(X[9]), .in9(X[10]), .in10(X[11]), .in11(X[12]), .in12(X[13]), .in13(X[14]), .in14(X[15]),
    .in15(X[16]), .in16(X[17]), .in17(X[18]), .in18(X[19]), .in19(X[20]), .in20(X[21]), .in21(X[22]),
    .in22(X[23]), .in23(X[24]), .in24(X[25]), .in25(X[26]), .in26(X[27]), .in27(X[28]), .in28(X[29]),
    .in29(X[30]), .in30(X[31]), .in31(1'b0), .out(result_srl[1]), .sel(Y[4:0]));
  Multiplexer #(.select(5), .width(1), .disabled("Z"), .enable("false")) multiplexer_3 (
    .in0(X[2]), .in1(X[3]), .in2(X[4]), .in3(X[5]), .in4(X[6]), .in5(X[7]), .in6(X[8]), .in7(X[9]),
    .in8(X[10]), .in9(X[11]), .in10(X[12]), .in11(X[13]), .in12(X[14]), .in13(X[15]), .in14(X[16]),
    .in15(X[17]), .in16(X[18]), .in17(X[19]), .in18(X[20]), .in19(X[21]), .in20(X[22]), .in21(X[23]),
    .in22(X[24]), .in23(X[25]), .in24(X[26]), .in25(X[27]), .in26(X[28]), .in27(X[29]), .in28(X[30]),
    .in29(X[31]), .in30(1'b0), .in31(1'b0), .out(result_srl[2]), .sel(Y[4:0]));
  Multiplexer #(.select(5), .width(1), .disabled("Z"), .enable("false")) multiplexer_4 (
    .in0(X[3]), .in1(X[4]), .in2(X[5]), .in3(X[6]), .in4(X[7]), .in5(X[8]), .in6(X[9]), .in7(X[10]),
    .in8(X[11]), .in9(X[12]), .in10(X[13]), .in11(X[14]), .in12(X[15]), .in13(X[16]), .in14(X[17]),
    .in15(X[18]), .in16(X[19]), .in17(X[20]), .in18(X[21]), .in19(X[22]), .in20(X[23]), .in21(X[24]),
    .in22(X[25]), .in23(X[26]), .in24(X[27]), .in25(X[28]), .in26(X[29]), .in27(X[30]), .in28(X[31]),
    .in29(1'b0), .in30(1'b0), .in31(1'b0), .out(result_srl[3]), .sel(Y[4:0]));
  Multiplexer #(.select(5), .width(1), .disabled("Z"), .enable("false")) multiplexer_5 (
    .in0(X[4]), .in1(X[5]), .in2(X[6]), .in3(X[7]), .in4(X[8]), .in5(X[9]), .in6(X[10]), .in7(X[11]),
    .in8(X[12]), .in9(X[13]), .in10(X[14]), .in11(X[15]), .in12(X[16]), .in13(X[17]), .in14(X[18]),
    .in15(X[19]), .in16(X[20]), .in17(X[21]), .in18(X[22]), .in19(X[23]), .in20(X[24]), .in21(X[25]),
    .in22(X[26]), .in23(X[27]), .in24(X[28]), .in25(X[29]), .in26(X[30]), .in27(X[31]), .in28(1'b0),
    .in29(1'b0), .in30(1'b0), .in31(1'b0), .out(result_srl[4]), .sel(Y[4:0]));
  Multiplexer #(.select(5), .width(1), .disabled("Z"), .enable("false")) multiplexer_6 (
    .in0(X[5]), .in1(X[6]), .in2(X[7]), .in3(X[8]), .in4(X[9]), .in5(X[10]), .in6(X[11]), .in7(X[12]),
    .in8(X[13]), .in9(X[14]), .in10(X[15]), .in11(X[16]), .in12(X[17]), .in13(X[18]), .in14(X[19]),
    .in15(X[20]), .in16(X[21]), .in17(X[22]), .in18(X[23]), .in19(X[24]), .in20(X[25]), .in21(X[26]),
    .in22(X[27]), .in23(X[28]), .in24(X[29]), .in25(X[30]), .in26(X[31]), .in27(1'b0), .in28(1'b0),
    .in29(1'b0), .in30(1'b0), .in31(1'b0), .out(result_srl[5]), .sel(Y[4:0]));
  Multiplexer #(.select(5), .width(1), .disabled("Z"), .enable("false")) multiplexer_7 (
    .in0(X[6]), .in1(X[7]), .in2(X[8]), .in3(X[9]), .in4(X[10]), .in5(X[11]), .in6(X[12]), .in7(X[13]),
    .in8(X[14]), .in9(X[15]), .in10(X[16]), .in11(X[17]), .in12(X[18]), .in13(X[19]), .in14(X[20]),
    .in15(X[21]), .in16(X[22]), .in17(X[23]), .in18(X[24]), .in19(X[25]), .in20(X[26]), .in21(X[27]),
    .in22(X[28]), .in23(X[29]), .in24(X[30]), .in25(X[31]), .in26(1'b0), .in27(1'b0), .in28(1'b0),
    .in29(1'b0), .in30(1'b0), .in31(1'b0), .out(result_srl[6]), .sel(Y[4:0]));
  Multiplexer #(.select(5), .width(1), .disabled("Z"), .enable("false")) multiplexer_8 (
    .in0(X[7]), .in1(X[8]), .in2(X[9]), .in3(X[10]), .in4(X[11]), .in5(X[12]), .in6(X[13]), .in7(X[14]),
    .in8(X[15]), .in9(X[16]), .in10(X[17]), .in11(X[18]), .in12(X[19]), .in13(X[20]), .in14(X[21]),
    .in15(X[22]), .in16(X[23]), .in17(X[24]), .in18(X[25]), .in19(X[26]), .in20(X[27]), .in21(X[28]),
    .in22(X[29]), .in23(X[30]), .in24(X[31]), .in25(1'b0), .in26(1'b0), .in27(1'b0), .in28(1'b0),
    .in29(1'b0), .in30(1'b0), .in31(1'b0), .out(result_srl[7]), .sel(Y[4:0]));
  Multiplexer #(.select(5), .width(1), .disabled("Z"), .enable("false")) multiplexer_9 (
    .in0(X[8]), .in1(X[9]), .in2(X[10]), .in3(X[11]), .in4(X[12]), .in5(X[13]), .in6(X[14]), .in7(X[15]),
    .in8(X[16]), .in9(X[17]), .in10(X[18]), .in11(X[19]), .in12(X[20]), .in13(X[21]), .in14(X[22]),
    .in15(X[23]), .in16(X[24]), .in17(X[25]), .in18(X[26]), .in19(X[27]), .in20(X[28]), .in21(X[29]),
    .in22(X[30]), .in23(X[31]), .in24(1'b0), .in25(1'b0), .in26(1'b0), .in27(1'b0), .in28(1'b0), .in29(1'b0),
    .in30(1'b0), .in31(1'b0), .out(result_srl[8]), .sel(Y[4:0]));
  Multiplexer #(.select(5), .width(1), .disabled("Z"), .enable("false")) multiplexer_10 (
    .in0(X[9]), .in1(X[10]), .in2(X[11]), .in3(X[12]), .in4(X[13]), .in5(X[14]), .in6(X[15]), .in7(X[16]),
    .in8(X[17]), .in9(X[18]), .in10(X[19]), .in11(X[20]), .in12(X[21]), .in13(X[22]), .in14(X[23]),
    .in15(X[24]), .in16(X[25]), .in17(X[26]), .in18(X[27]), .in19(X[28]), .in20(X[29]), .in21(X[30]),
    .in22(X[31]), .in23(1'b0), .in24(1'b0), .in25(1'b0), .in26(1'b0), .in27(1'b0), .in28(1'b0), .in29(1'b0),
    .in30(1'b0), .in31(1'b0), .out(result_srl[9]), .sel(Y[4:0]));
  Multiplexer #(.select(5), .width(1), .disabled("Z"), .enable("false")) multiplexer_11 (
    .in0(X[10]), .in1(X[11]), .in2(X[12]), .in3(X[13]), .in4(X[14]), .in5(X[15]), .in6(X[16]), .in7(X[17]),
    .in8(X[18]), .in9(X[19]), .in10(X[20]), .in11(X[21]), .in12(X[22]), .in13(X[23]), .in14(X[24]),
    .in15(X[25]), .in16(X[26]), .in17(X[27]), .in18(X[28]), .in19(X[29]), .in20(X[30]), .in21(X[31]),
    .in22(1'b0), .in23(1'b0), .in24(1'b0), .in25(1'b0), .in26(1'b0), .in27(1'b0), .in28(1'b0), .in29(1'b0),
    .in30(1'b0), .in31(1'b0), .out(result_srl[10]), .sel(Y[4:0]));
  Multiplexer #(.select(5), .width(1), .disabled("Z"), .enable("false")) multiplexer_12 (
    .in0(X[11]), .in1(X[12]), .in2(X[13]), .in3(X[14]), .in4(X[15]), .in5(X[16]), .in6(X[17]), .in7(X[18]),
    .in8(X[19]), .in9(X[20]), .in10(X[21]), .in11(X[22]), .in12(X[23]), .in13(X[24]), .in14(X[25]),
    .in15(X[26]), .in16(X[27]), .in17(X[28]), .in18(X[29]), .in19(X[30]), .in20(X[31]), .in21(1'b0),
    .in22(1'b0), .in23(1'b0), .in24(1'b0), .in25(1'b0), .in26(1'b0), .in27(1'b0), .in28(1'b0), .in29(1'b0),
    .in30(1'b0), .in31(1'b0), .out(result_srl[11]), .sel(Y[4:0]));
  Multiplexer #(.select(5), .width(1), .disabled("Z"), .enable("false")) multiplexer_13 (
    .in0(X[12]), .in1(X[13]), .in2(X[14]), .in3(X[15]), .in4(X[16]), .in5(X[17]), .in6(X[18]), .in7(X[19]),
    .in8(X[20]), .in9(X[21]), .in10(X[22]), .in11(X[23]), .in12(X[24]), .in13(X[25]), .in14(X[26]),
    .in15(X[27]), .in16(X[28]), .in17(X[29]), .in18(X[30]), .in19(X[31]), .in20(1'b0), .in21(1'b0),
    .in22(1'b0), .in23(1'b0), .in24(1'b0), .in25(1'b0), .in26(1'b0), .in27(1'b0), .in28(1'b0), .in29(1'b0),
    .in30(1'b0), .in31(1'b0), .out(result_srl[12]), .sel(Y[4:0]));
  Multiplexer #(.select(5), .width(1), .disabled("Z"), .enable("false")) multiplexer_14 (
    .in0(X[13]), .in1(X[14]), .in2(X[15]), .in3(X[16]), .in4(X[17]), .in5(X[18]), .in6(X[19]), .in7(X[20]),
    .in8(X[21]), .in9(X[22]), .in10(X[23]), .in11(X[24]), .in12(X[25]), .in13(X[26]), .in14(X[27]),
    .in15(X[28]), .in16(X[29]), .in17(X[30]), .in18(X[31]), .in19(1'b0), .in20(1'b0), .in21(1'b0),
    .in22(1'b0), .in23(1'b0), .in24(1'b0), .in25(1'b0), .in26(1'b0), .in27(1'b0), .in28(1'b0), .in29(1'b0),
    .in30(1'b0), .in31(1'b0), .out(result_srl[13]), .sel(Y[4:0]));
  Multiplexer #(.select(5), .width(1), .disabled("Z"), .enable("false")) multiplexer_15 (
    .in0(X[14]), .in1(X[15]), .in2(X[16]), .in3(X[17]), .in4(X[18]), .in5(X[19]), .in6(X[20]), .in7(X[21]),
    .in8(X[22]), .in9(X[23]), .in10(X[24]), .in11(X[25]), .in12(X[26]), .in13(X[27]), .in14(X[28]),
    .in15(X[29]), .in16(X[30]), .in17(X[31]), .in18(1'b0), .in19(1'b0), .in20(1'b0), .in21(1'b0),
    .in22(1'b0), .in23(1'b0), .in24(1'b0), .in25(1'b0), .in26(1'b0), .in27(1'b0), .in28(1'b0), .in29(1'b0),
    .in30(1'b0), .in31(1'b0), .out(result_srl[14]), .sel(Y[4:0]));
  Multiplexer #(.select(5), .width(1), .disabled("Z"), .enable("false")) multiplexer_16 (
    .in0(X[15]), .in1(X[16]), .in2(X[17]), .in3(X[18]), .in4(X[19]), .in5(X[20]), .in6(X[21]), .in7(X[22]),
    .in8(X[23]), .in9(X[24]), .in10(X[25]), .in11(X[26]), .in12(X[27]), .in13(X[28]), .in14(X[29]),
    .in15(X[30]), .in16(X[31]), .in17(1'b0), .in18(1'b0), .in19(1'b0), .in20(1'b0), .in21(1'b0), .in22(1'b0),
    .in23(1'b0), .in24(1'b0), .in25(1'b0), .in26(1'b0), .in27(1'b0), .in28(1'b0), .in29(1'b0), .in30(1'b0),
    .in31(1'b0), .out(result_srl[15]), .sel(Y[4:0]));
  Multiplexer #(.select(5), .width(1), .disabled("Z"), .enable("false")) multiplexer_17 (
    .in0(X[16]), .in1(X[17]), .in2(X[18]), .in3(X[19]), .in4(X[20]), .in5(X[21]), .in6(X[22]), .in7(X[23]),
    .in8(X[24]), .in9(X[25]), .in10(X[26]), .in11(X[27]), .in12(X[28]), .in13(X[29]), .in14(X[30]),
    .in15(X[31]), .in16(1'b0), .in17(1'b0), .in18(1'b0), .in19(1'b0), .in20(1'b0), .in21(1'b0), .in22(1'b0),
    .in23(1'b0), .in24(1'b0), .in25(1'b0), .in26(1'b0), .in27(1'b0), .in28(1'b0), .in29(1'b0), .in30(1'b0),
    .in31(1'b0), .out(result_srl[16]), .sel(Y[4:0]));
  Multiplexer #(.select(5), .width(1), .disabled("Z"), .enable("false")) multiplexer_18 (
    .in0(X[17]), .in1(X[18]), .in2(X[19]), .in3(X[20]), .in4(X[21]), .in5(X[22]), .in6(X[23]), .in7(X[24]),
    .in8(X[25]), .in9(X[26]), .in10(X[27]), .in11(X[28]), .in12(X[29]), .in13(X[30]), .in14(X[31]),
    .in15(1'b0), .in16(1'b0), .in17(1'b0), .in18(1'b0), .in19(1'b0), .in20(1'b0), .in21(1'b0), .in22(1'b0),
    .in23(1'b0), .in24(1'b0), .in25(1'b0), .in26(1'b0), .in27(1'b0), .in28(1'b0), .in29(1'b0), .in30(1'b0),
    .in31(1'b0), .out(result_srl[17]), .sel(Y[4:0]));
  Multiplexer #(.select(5), .width(1), .disabled("Z"), .enable("false")) multiplexer_19 (
    .in0(X[18]), .in1(X[19]), .in2(X[20]), .in3(X[21]), .in4(X[22]), .in5(X[23]), .in6(X[24]), .in7(X[25]),
    .in8(X[26]), .in9(X[27]), .in10(X[28]), .in11(X[29]), .in12(X[30]), .in13(X[31]), .in14(1'b0),
    .in15(1'b0), .in16(1'b0), .in17(1'b0), .in18(1'b0), .in19(1'b0), .in20(1'b0), .in21(1'b0), .in22(1'b0),
    .in23(1'b0), .in24(1'b0), .in25(1'b0), .in26(1'b0), .in27(1'b0), .in28(1'b0), .in29(1'b0), .in30(1'b0),
    .in31(1'b0), .out(result_srl[18]), .sel(Y[4:0]));
  Multiplexer #(.select(5), .width(1), .disabled("Z"), .enable("false")) multiplexer_20 (
    .in0(X[19]), .in1(X[20]), .in2(X[21]), .in3(X[22]), .in4(X[23]), .in5(X[24]), .in6(X[25]), .in7(X[26]),
    .in8(X[27]), .in9(X[28]), .in10(X[29]), .in11(X[30]), .in12(X[31]), .in13(1'b0), .in14(1'b0),
    .in15(1'b0), .in16(1'b0), .in17(1'b0), .in18(1'b0), .in19(1'b0), .in20(1'b0), .in21(1'b0), .in22(1'b0),
    .in23(1'b0), .in24(1'b0), .in25(1'b0), .in26(1'b0), .in27(1'b0), .in28(1'b0), .in29(1'b0), .in30(1'b0),
    .in31(1'b0), .out(result_srl[19]), .sel(Y[4:0]));
  Multiplexer #(.select(5), .width(1), .disabled("Z"), .enable("false")) multiplexer_21 (
    .in0(X[20]), .in1(X[21]), .in2(X[22]), .in3(X[23]), .in4(X[24]), .in5(X[25]), .in6(X[26]), .in7(X[27]),
    .in8(X[28]), .in9(X[29]), .in10(X[30]), .in11(X[31]), .in12(1'b0), .in13(1'b0), .in14(1'b0), .in15(1'b0),
    .in16(1'b0), .in17(1'b0), .in18(1'b0), .in19(1'b0), .in20(1'b0), .in21(1'b0), .in22(1'b0), .in23(1'b0),
    .in24(1'b0), .in25(1'b0), .in26(1'b0), .in27(1'b0), .in28(1'b0), .in29(1'b0), .in30(1'b0), .in31(1'b0),
    .out(result_srl[20]), .sel(Y[4:0]));
  Multiplexer #(.select(5), .width(1), .disabled("Z"), .enable("false")) multiplexer_22 (
    .in0(X[21]), .in1(X[22]), .in2(X[23]), .in3(X[24]), .in4(X[25]), .in5(X[26]), .in6(X[27]), .in7(X[28]),
    .in8(X[29]), .in9(X[30]), .in10(X[31]), .in11(1'b0), .in12(1'b0), .in13(1'b0), .in14(1'b0), .in15(1'b0),
    .in16(1'b0), .in17(1'b0), .in18(1'b0), .in19(1'b0), .in20(1'b0), .in21(1'b0), .in22(1'b0), .in23(1'b0),
    .in24(1'b0), .in25(1'b0), .in26(1'b0), .in27(1'b0), .in28(1'b0), .in29(1'b0), .in30(1'b0), .in31(1'b0),
    .out(result_srl[21]), .sel(Y[4:0]));
  Multiplexer #(.select(5), .width(1), .disabled("Z"), .enable("false")) multiplexer_23 (
    .in0(X[22]), .in1(X[23]), .in2(X[24]), .in3(X[25]), .in4(X[26]), .in5(X[27]), .in6(X[28]), .in7(X[29]),
    .in8(X[30]), .in9(X[31]), .in10(1'b0), .in11(1'b0), .in12(1'b0), .in13(1'b0), .in14(1'b0), .in15(1'b0),
    .in16(1'b0), .in17(1'b0), .in18(1'b0), .in19(1'b0), .in20(1'b0), .in21(1'b0), .in22(1'b0), .in23(1'b0),
    .in24(1'b0), .in25(1'b0), .in26(1'b0), .in27(1'b0), .in28(1'b0), .in29(1'b0), .in30(1'b0), .in31(1'b0),
    .out(result_srl[22]), .sel(Y[4:0]));
  Multiplexer #(.select(5), .width(1), .disabled("Z"), .enable("false")) multiplexer_24 (
    .in0(X[23]), .in1(X[24]), .in2(X[25]), .in3(X[26]), .in4(X[27]), .in5(X[28]), .in6(X[29]), .in7(X[30]),
    .in8(X[31]), .in9(1'b0), .in10(1'b0), .in11(1'b0), .in12(1'b0), .in13(1'b0), .in14(1'b0), .in15(1'b0),
    .in16(1'b0), .in17(1'b0), .in18(1'b0), .in19(1'b0), .in20(1'b0), .in21(1'b0), .in22(1'b0), .in23(1'b0),
    .in24(1'b0), .in25(1'b0), .in26(1'b0), .in27(1'b0), .in28(1'b0), .in29(1'b0), .in30(1'b0), .in31(1'b0),
    .out(result_srl[23]), .sel(Y[4:0]));
  Multiplexer #(.select(5), .width(1), .disabled("Z"), .enable("false")) multiplexer_25 (
    .in0(X[24]), .in1(X[25]), .in2(X[26]), .in3(X[27]), .in4(X[28]), .in5(X[29]), .in6(X[30]), .in7(X[31]),
    .in8(1'b0), .in9(1'b0), .in10(1'b0), .in11(1'b0), .in12(1'b0), .in13(1'b0), .in14(1'b0), .in15(1'b0),
    .in16(1'b0), .in17(1'b0), .in18(1'b0), .in19(1'b0), .in20(1'b0), .in21(1'b0), .in22(1'b0), .in23(1'b0),
    .in24(1'b0), .in25(1'b0), .in26(1'b0), .in27(1'b0), .in28(1'b0), .in29(1'b0), .in30(1'b0), .in31(1'b0),
    .out(result_srl[24]), .sel(Y[4:0]));
  Multiplexer #(.select(5), .width(1), .disabled("Z"), .enable("false")) multiplexer_26 (
    .in0(X[25]), .in1(X[26]), .in2(X[27]), .in3(X[28]), .in4(X[29]), .in5(X[30]), .in6(X[31]), .in7(1'b0),
    .in8(1'b0), .in9(1'b0), .in10(1'b0), .in11(1'b0), .in12(1'b0), .in13(1'b0), .in14(1'b0), .in15(1'b0),
    .in16(1'b0), .in17(1'b0), .in18(1'b0), .in19(1'b0), .in20(1'b0), .in21(1'b0), .in22(1'b0), .in23(1'b0),
    .in24(1'b0), .in25(1'b0), .in26(1'b0), .in27(1'b0), .in28(1'b0), .in29(1'b0), .in30(1'b0), .in31(1'b0),
    .out(result_srl[25]), .sel(Y[4:0]));
  Multiplexer #(.select(5), .width(1), .disabled("Z"), .enable("false")) multiplexer_27 (
    .in0(X[26]), .in1(X[27]), .in2(X[28]), .in3(X[29]), .in4(X[30]), .in5(X[31]), .in6(1'b0), .in7(1'b0),
    .in8(1'b0), .in9(1'b0), .in10(1'b0), .in11(1'b0), .in12(1'b0), .in13(1'b0), .in14(1'b0), .in15(1'b0),
    .in16(1'b0), .in17(1'b0), .in18(1'b0), .in19(1'b0), .in20(1'b0), .in21(1'b0), .in22(1'b0), .in23(1'b0),
    .in24(1'b0), .in25(1'b0), .in26(1'b0), .in27(1'b0), .in28(1'b0), .in29(1'b0), .in30(1'b0), .in31(1'b0),
    .out(result_srl[26]), .sel(Y[4:0]));
  Multiplexer #(.select(5), .width(1), .disabled("Z"), .enable("false")) multiplexer_28 (
    .in0(X[27]), .in1(X[28]), .in2(X[29]), .in3(X[30]), .in4(X[31]), .in5(1'b0), .in6(1'b0), .in7(1'b0),
    .in8(1'b0), .in9(1'b0), .in10(1'b0), .in11(1'b0), .in12(1'b0), .in13(1'b0), .in14(1'b0), .in15(1'b0),
    .in16(1'b0), .in17(1'b0), .in18(1'b0), .in19(1'b0), .in20(1'b0), .in21(1'b0), .in22(1'b0), .in23(1'b0),
    .in24(1'b0), .in25(1'b0), .in26(1'b0), .in27(1'b0), .in28(1'b0), .in29(1'b0), .in30(1'b0), .in31(1'b0),
    .out(result_srl[27]), .sel(Y[4:0]));
  Multiplexer #(.select(5), .width(1), .disabled("Z"), .enable("false")) multiplexer_29 (
    .in0(X[28]), .in1(X[29]), .in2(X[30]), .in3(X[31]), .in4(1'b0), .in5(1'b0), .in6(1'b0), .in7(1'b0),
    .in8(1'b0), .in9(1'b0), .in10(1'b0), .in11(1'b0), .in12(1'b0), .in13(1'b0), .in14(1'b0), .in15(1'b0),
    .in16(1'b0), .in17(1'b0), .in18(1'b0), .in19(1'b0), .in20(1'b0), .in21(1'b0), .in22(1'b0), .in23(1'b0),
    .in24(1'b0), .in25(1'b0), .in26(1'b0), .in27(1'b0), .in28(1'b0), .in29(1'b0), .in30(1'b0), .in31(1'b0),
    .out(result_srl[28]), .sel(Y[4:0]));
  Multiplexer #(.select(5), .width(1), .disabled("Z"), .enable("false")) multiplexer_30 (
    .in0(X[29]), .in1(X[30]), .in2(X[31]), .in3(1'b0), .in4(1'b0), .in5(1'b0), .in6(1'b0), .in7(1'b0),
    .in8(1'b0), .in9(1'b0), .in10(1'b0), .in11(1'b0), .in12(1'b0), .in13(1'b0), .in14(1'b0), .in15(1'b0),
    .in16(1'b0), .in17(1'b0), .in18(1'b0), .in19(1'b0), .in20(1'b0), .in21(1'b0), .in22(1'b0), .in23(1'b0),
    .in24(1'b0), .in25(1'b0), .in26(1'b0), .in27(1'b0), .in28(1'b0), .in29(1'b0), .in30(1'b0), .in31(1'b0),
    .out(result_srl[29]), .sel(Y[4:0]));
  Multiplexer #(.select(5), .width(1), .disabled("Z"), .enable("false")) multiplexer_31 (
    .in0(X[30]), .in1(X[31]), .in2(1'b0), .in3(1'b0), .in4(1'b0), .in5(1'b0), .in6(1'b0), .in7(1'b0),
    .in8(1'b0), .in9(1'b0), .in10(1'b0), .in11(1'b0), .in12(1'b0), .in13(1'b0), .in14(1'b0), .in15(1'b0),
    .in16(1'b0), .in17(1'b0), .in18(1'b0), .in19(1'b0), .in20(1'b0), .in21(1'b0), .in22(1'b0), .in23(1'b0),
    .in24(1'b0), .in25(1'b0), .in26(1'b0), .in27(1'b0), .in28(1'b0), .in29(1'b0), .in30(1'b0), .in31(1'b0),
    .out(result_srl[30]), .sel(Y[4:0]));
  Multiplexer #(.select(5), .width(1), .disabled("Z"), .enable("false")) multiplexer_32 (
    .in0(X[31]), .in1(1'b0), .in2(1'b0), .in3(1'b0), .in4(1'b0), .in5(1'b0), .in6(1'b0), .in7(1'b0),
    .in8(1'b0), .in9(1'b0), .in10(1'b0), .in11(1'b0), .in12(1'b0), .in13(1'b0), .in14(1'b0), .in15(1'b0),
    .in16(1'b0), .in17(1'b0), .in18(1'b0), .in19(1'b0), .in20(1'b0), .in21(1'b0), .in22(1'b0), .in23(1'b0),
    .in24(1'b0), .in25(1'b0), .in26(1'b0), .in27(1'b0), .in28(1'b0), .in29(1'b0), .in30(1'b0), .in31(1'b0),
    .out(result_srl[31]), .sel(Y[4:0]));

  // Notes on the sheet:
  //   输入管脚
  //   逻辑功能：利用32个1位32选1多路选择器设计逻辑右移寄存器
  //   以上管脚名称及位置均不要移动，利用下方的隧道信号用画电路图方式设计32位逻辑右移寄存器（已设计完成）
  //   输出管脚
endmodule

// 32位桶型逻辑右移寄存器
module \_32位桶型逻辑右移寄存器_已设计完成  (
  input  [31:0] X,
  input  [31:0] Y,
  output [31:0] result_srl
);

  wire [31:0] multiplexer_1_out, multiplexer_2_out, multiplexer_3_out, multiplexer_4_out;

  Multiplexer #(.select(1), .width(32), .disabled("Z"), .enable("false")) multiplexer_1 (
    .in0(X), .in1({1'b0, X[31:1]}), .out(multiplexer_1_out), .sel(Y[0]));
  Multiplexer #(.select(1), .width(32), .disabled("Z"), .enable("false")) multiplexer_2 (
    .in0(multiplexer_1_out), .in1({2'b00, multiplexer_1_out[31:2]}), .out(multiplexer_2_out), .sel(Y[1]));
  Multiplexer #(.select(1), .width(32), .disabled("Z"), .enable("false")) multiplexer_3 (
    .in0(multiplexer_2_out), .in1({4'b0000, multiplexer_2_out[31:4]}), .out(multiplexer_3_out), .sel(Y[2]));
  Multiplexer #(.select(1), .width(32), .disabled("Z"), .enable("false")) multiplexer_4 (
    .in0(multiplexer_3_out), .in1({{8{1'b0}}, multiplexer_3_out[31:8]}), .out(multiplexer_4_out), .sel(Y[3]));
  Multiplexer #(.select(1), .width(32), .disabled("Z"), .enable("false")) multiplexer_5 (
    .in0(multiplexer_4_out), .in1({{16{1'b0}}, multiplexer_4_out[31:16]}), .out(result_srl), .sel(Y[4]));

  // Notes on the sheet:
  //   输入管脚
  //   逻辑功能：利用5个32位2选1多路选择器设计逻辑右移寄存器（桶型移位）
  //   以上管脚名称及位置均不要移动，利用下方的隧道信号用画电路图方式设计32位逻辑右移寄存器（已设计完成）
  //   输出管脚
endmodule

// 32位低成本移位寄存器
module \_32位低成本移位寄存器_已设计完成  (
  input  [1:0] shift_op,
  input  [31:0] X,
  input  [31:0] Y,
  output [31:0] result_sll,
  output [31:0] result_sra,
  output [31:0] result_srl
);

  wire [31:0] and_1_out, multiplexer_1_out, \n32位桶型逻辑右移寄存器_已设计完成_2_result_srl , not_1_out;

  Multiplexer #(.select(2), .width(32), .disabled("Z"), .enable("false")) multiplexer_1 (
    .in0({X[0], X[1], X[2], X[3], X[4], X[5], X[6], X[7], X[8], X[9], X[10], X[11], X[12], X[13], X[14], X[15], X[16], X[17], X[18], X[19], X[20], X[21], X[22], X[23], X[24], X[25], X[26], X[27], X[28], X[29], X[30], X[31]}),
    .in1(X), .in2(X), .in3({32{1'b0}}), .out(multiplexer_1_out), .sel(shift_op));
  \_32位桶型逻辑右移寄存器_已设计完成  \u_32位桶型逻辑右移寄存器_已设计完成_1  (
    .X(multiplexer_1_out), .Y(Y),
    .result_srl({result_sll[0], result_sll[1], result_sll[2], result_sll[3], result_sll[4], result_sll[5], result_sll[6], result_sll[7], result_sll[8], result_sll[9], result_sll[10], result_sll[11], result_sll[12], result_sll[13], result_sll[14], result_sll[15], result_sll[16], result_sll[17], result_sll[18], result_sll[19], result_sll[20], result_sll[21], result_sll[22], result_sll[23], result_sll[24], result_sll[25], result_sll[26], result_sll[27], result_sll[28], result_sll[29], result_sll[30], result_sll[31]}));
  \_32位桶型逻辑右移寄存器_已设计完成  \u_32位桶型逻辑右移寄存器_已设计完成_2  (
    .X({32{1'b1}}), .Y(Y), .result_srl(\n32位桶型逻辑右移寄存器_已设计完成_2_result_srl ));
  assign not_1_out = ~\n32位桶型逻辑右移寄存器_已设计完成_2_result_srl ;  // NOT_Gate not_1, 32 bits wide
  assign result_sra = {result_sll[0], result_sll[1], result_sll[2], result_sll[3], result_sll[4], result_sll[5], result_sll[6], result_sll[7], result_sll[8], result_sll[9], result_sll[10], result_sll[11], result_sll[12], result_sll[13], result_sll[14], result_sll[15], result_sll[16], result_sll[17], result_sll[18], result_sll[19], result_sll[20], result_sll[21], result_sll[22], result_sll[23], result_sll[24], result_sll[25], result_sll[26], result_sll[27], result_sll[28], result_sll[29], result_sll[30], result_sll[31]} | and_1_out;  // OR_Gate or_1, 32 bits wide
  assign and_1_out = not_1_out & {32{X[31]}};  // AND_Gate and_1, 32 bits wide

  assign result_srl = {result_sll[0], result_sll[1], result_sll[2], result_sll[3], result_sll[4], result_sll[5], result_sll[6], result_sll[7], result_sll[8], result_sll[9], result_sll[10], result_sll[11], result_sll[12], result_sll[13], result_sll[14], result_sll[15], result_sll[16], result_sll[17], result_sll[18], result_sll[19], result_sll[20], result_sll[21], result_sll[22], result_sll[23], result_sll[24], result_sll[25], result_sll[26], result_sll[27], result_sll[28], result_sll[29], result_sll[30], result_sll[31]};

  // Notes on the sheet:
  //   输入管脚
  //   逻辑功能：利用32位逻辑右移寄存器,增加适当电路实现逻辑左移(shift_op=00),算术右移(shift_op=01)及逻辑右移(shift_op=10)功能
  //   以上管脚名称及位置均不要移动，利用下方的隧道信号用画电路图方式设计32位移位寄存器
  //   输出管脚
endmodule

// 4位无符号比较器
module \_4位无符号比较器_已设计完成  (
  input  X3,
  input  X2,
  input  X1,
  input  X0,
  input  Y3,
  input  Y2,
  input  Y1,
  input  Y0,
  output Gt,
  output Equal,
  output Lt
);

  wire and_1_out, and_2_out, and_3_out, and_4_out, and_5_out, and_6_out, and_7_out, and_8_out, and_9_out,
       and_10_out, and_11_out, and_12_out, and_13_out, and_14_out, and_15_out, and_16_out, and_17_out,
       and_18_out, and_19_out, and_20_out, and_21_out, and_22_out, and_23_out, and_24_out, and_25_out,
       and_26_out, and_27_out, and_28_out, and_29_out, and_30_out, and_31_out, and_32_out, and_33_out,
       and_34_out, and_35_out, and_36_out, and_37_out, and_38_out, and_39_out, and_40_out, and_41_out,
       and_42_out, and_43_out, and_44_out, and_45_out, and_46_out, not_1_out, not_2_out, not_3_out,
       not_4_out, not_5_out, not_6_out, not_7_out, not_8_out, not_9_out, not_10_out, not_11_out, not_12_out,
       not_13_out, not_14_out, not_15_out, not_16_out, not_17_out, not_18_out, not_19_out, not_20_out,
       not_21_out, not_22_out, not_23_out, not_24_out, not_25_out, not_26_out, not_27_out, not_28_out,
       not_29_out, not_30_out, not_31_out, not_32_out, not_33_out, not_34_out, not_35_out, not_36_out,
       not_37_out, not_38_out, not_39_out, not_40_out, not_41_out, not_42_out, not_43_out, not_44_out,
       not_45_out, not_46_out, not_47_out, not_48_out, not_49_out, not_50_out, not_51_out, not_52_out,
       not_53_out, not_54_out, not_55_out, not_56_out, not_57_out, not_58_out, not_59_out, not_60_out,
       not_61_out, not_62_out, not_63_out, not_64_out, not_65_out, not_66_out, not_67_out, not_68_out,
       not_69_out, not_70_out, not_71_out, not_72_out, not_73_out, not_74_out, not_75_out, not_76_out,
       not_77_out, not_78_out, not_79_out, not_80_out, not_81_out, not_82_out, not_83_out, not_84_out,
       not_85_out, not_86_out, not_87_out, not_88_out, not_89_out, not_90_out, not_91_out, not_92_out,
       not_93_out, not_94_out, not_95_out, not_96_out, not_97_out, not_98_out, not_99_out, not_100_out,
       not_101_out, not_102_out, not_103_out, not_104_out, not_105_out, not_106_out, not_107_out,
       not_108_out, not_109_out, not_110_out, not_111_out, not_112_out, not_113_out, not_114_out,
       not_115_out, not_116_out, not_117_out, not_118_out, not_119_out, not_120_out, not_121_out,
       not_122_out, not_123_out, not_124_out, not_125_out, not_126_out, not_127_out, not_128_out;

  not not_1 (not_1_out, Y3);
  not not_2 (not_2_out, Y2);
  not not_3 (not_3_out, Y1);
  not not_4 (not_4_out, Y0);
  not not_5 (not_5_out, Y3);
  not not_6 (not_6_out, Y2);
  not not_7 (not_7_out, Y1);
  not not_8 (not_8_out, Y3);
  not not_9 (not_9_out, Y2);
  not not_10 (not_10_out, Y0);
  not not_11 (not_11_out, Y3);
  not not_12 (not_12_out, Y2);
  not not_13 (not_13_out, Y3);
  not not_14 (not_14_out, Y1);
  not not_15 (not_15_out, Y0);
  not not_16 (not_16_out, Y3);
  not not_17 (not_17_out, Y1);
  not not_18 (not_18_out, Y3);
  not not_19 (not_19_out, Y0);
  not not_20 (not_20_out, Y3);
  not not_21 (not_21_out, Y2);
  not not_22 (not_22_out, Y1);
  not not_23 (not_23_out, Y0);
  not not_24 (not_24_out, Y2);
  not not_25 (not_25_out, Y1);
  not not_26 (not_26_out, Y2);
  not not_27 (not_27_out, Y0);
  not not_28 (not_28_out, Y2);
  not not_29 (not_29_out, Y1);
  not not_30 (not_30_out, Y0);
  not not_31 (not_31_out, Y1);
  not not_32 (not_32_out, Y0);
  not not_33 (not_33_out, X3);
  not not_34 (not_34_out, X2);
  not not_35 (not_35_out, X1);
  not not_36 (not_36_out, X0);
  not not_37 (not_37_out, Y3);
  not not_38 (not_38_out, Y2);
  not not_39 (not_39_out, Y1);
  not not_40 (not_40_out, Y0);
  not not_41 (not_41_out, X3);
  not not_42 (not_42_out, X2);
  not not_43 (not_43_out, X1);
  not not_44 (not_44_out, Y3);
  not not_45 (not_45_out, Y2);
  not not_46 (not_46_out, Y1);
  not not_47 (not_47_out, X3);
  not not_48 (not_48_out, X2);
  not not_49 (not_49_out, X0);
  not not_50 (not_50_out, Y3);
  not not_51 (not_51_out, Y2);
  not not_52 (not_52_out, Y0);
  not not_53 (not_53_out, X3);
  not not_54 (not_54_out, X2);
  not not_55 (not_55_out, Y3);
  not not_56 (not_56_out, Y2);
  not not_57 (not_57_out, X3);
  not not_58 (not_58_out, X1);
  not not_59 (not_59_out, X0);
  not not_60 (not_60_out, Y3);
  not not_61 (not_61_out, Y1);
  not not_62 (not_62_out, Y0);
  not not_63 (not_63_out, X3);
  not not_64 (not_64_out, X1);
  not not_65 (not_65_out, Y3);
  not not_66 (not_66_out, Y1);
  not not_67 (not_67_out, X3);
  not not_68 (not_68_out, X0);
  not not_69 (not_69_out, Y3);
  not not_70 (not_70_out, Y0);
  not not_71 (not_71_out, X3);
  not not_72 (not_72_out, Y3);
  not not_73 (not_73_out, X2);
  not not_74 (not_74_out, X1);
  not not_75 (not_75_out, X0);
  not not_76 (not_76_out, Y2);
  not not_77 (not_77_out, Y1);
  not not_78 (not_78_out, Y0);
  not not_79 (not_79_out, X2);
  not not_80 (not_80_out, X1);
  not not_81 (not_81_out, Y2);
  not not_82 (not_82_out, Y1);
  not not_83 (not_83_out, X2);
  not not_84 (not_84_out, X0);
  not not_85 (not_85_out, Y2);
  not not_86 (not_86_out, Y0);
  not not_87 (not_87_out, X2);
  not not_88 (not_88_out, Y2);
  not not_89 (not_89_out, X1);
  not not_90 (not_90_out, X0);
  not not_91 (not_91_out, Y1);
  not not_92 (not_92_out, Y0);
  not not_93 (not_93_out, X1);
  not not_94 (not_94_out, Y1);
  not not_95 (not_95_out, X0);
  not not_96 (not_96_out, Y0);
  not not_97 (not_97_out, X3);
  not not_98 (not_98_out, X2);
  not not_99 (not_99_out, X1);
  not not_100 (not_100_out, X0);
  not not_101 (not_101_out, X3);
  not not_102 (not_102_out, X2);
  not not_103 (not_103_out, X1);
  not not_104 (not_104_out, X3);
  not not_105 (not_105_out, X2);
  not not_106 (not_106_out, X0);
  not not_107 (not_107_out, X3);
  not not_108 (not_108_out, X2);
  not not_109 (not_109_out, X3);
  not not_110 (not_110_out, X1);
  not not_111 (not_111_out, X0);
  not not_112 (not_112_out, X3);
  not not_113 (not_113_out, X1);
  not not_114 (not_114_out, X3);
  not not_115 (not_115_out, X0);
  not not_116 (not_116_out, X3);
  not not_117 (not_117_out, X2);
  not not_118 (not_118_out, X1);
  not not_119 (not_119_out, X0);
  not not_120 (not_120_out, X2);
  not not_121 (not_121_out, X1);
  not not_122 (not_122_out, X2);
  not not_123 (not_123_out, X0);
  not not_124 (not_124_out, X2);
  not not_125 (not_125_out, X1);
  not not_126 (not_126_out, X0);
  not not_127 (not_127_out, X1);
  not not_128 (not_128_out, X0);
  and and_1 (and_1_out, X0, not_1_out, not_2_out, not_3_out, not_4_out);
  and and_2 (and_2_out, X1, not_5_out, not_6_out, not_7_out);
  and and_3 (and_3_out, X1, X0, not_8_out, not_9_out, not_10_out);
  and and_4 (and_4_out, X2, not_11_out, not_12_out);
  and and_5 (and_5_out, X2, X0, not_13_out, not_14_out, not_15_out);
  and and_6 (and_6_out, X2, X1, not_16_out, not_17_out);
  and and_7 (and_7_out, X2, X1, X0, not_18_out, not_19_out);
  and and_8 (and_8_out, X3, not_20_out);
  and and_9 (and_9_out, X3, X0, not_21_out, not_22_out, not_23_out);
  and and_10 (and_10_out, X3, X1, not_24_out, not_25_out);
  and and_11 (and_11_out, X3, X1, X0, not_26_out, not_27_out);
  and and_12 (and_12_out, X3, X2, not_28_out);
  and and_13 (and_13_out, X3, X2, X0, not_29_out, not_30_out);
  and and_14 (and_14_out, X3, X2, X1, not_31_out);
  and and_15 (and_15_out, X3, X2, X1, X0, not_32_out);
  and and_16 (and_16_out, not_33_out, not_34_out, not_35_out, not_36_out, not_37_out, not_38_out, not_39_out, not_40_out);
  and and_17 (and_17_out, not_41_out, not_42_out, not_43_out, X0, not_44_out, not_45_out, not_46_out, Y0);
  and and_18 (and_18_out, not_47_out, not_48_out, X1, not_49_out, not_50_out, not_51_out, Y1, not_52_out);
  and and_19 (and_19_out, not_53_out, not_54_out, X1, X0, not_55_out, not_56_out, Y1, Y0);
  and and_20 (and_20_out, not_57_out, X2, not_58_out, not_59_out, not_60_out, Y2, not_61_out, not_62_out);
  and and_21 (and_21_out, not_63_out, X2, not_64_out, X0, not_65_out, Y2, not_66_out, Y0);
  and and_22 (and_22_out, not_67_out, X2, X1, not_68_out, not_69_out, Y2, Y1, not_70_out);
  and and_23 (and_23_out, not_71_out, X2, X1, X0, not_72_out, Y2, Y1, Y0);
  and and_24 (and_24_out, X3, not_73_out, not_74_out, not_75_out, Y3, not_76_out, not_77_out, not_78_out);
  and and_25 (and_25_out, X3, not_79_out, not_80_out, X0, Y3, not_81_out, not_82_out, Y0);
  and and_26 (and_26_out, X3, not_83_out, X1, not_84_out, Y3, not_85_out, Y1, not_86_out);
  and and_27 (and_27_out, X3, not_87_out, X1, X0, Y3, not_88_out, Y1, Y0);
  and and_28 (and_28_out, X3, X2, not_89_out, not_90_out, Y3, Y2, not_91_out, not_92_out);
  and and_29 (and_29_out, X3, X2, not_93_out, X0, Y3, Y2, not_94_out, Y0);
  and and_30 (and_30_out, X3, X2, X1, not_95_out, Y3, Y2, Y1, not_96_out);
  and and_31 (and_31_out, X3, X2, X1, X0, Y3, Y2, Y1, Y0);
  and and_32 (and_32_out, not_97_out, not_98_out, not_99_out, not_100_out, Y0);
  and and_33 (and_33_out, not_101_out, not_102_out, not_103_out, Y1);
  and and_34 (and_34_out, not_104_out, not_105_out, not_106_out, Y1, Y0);
  and and_35 (and_35_out, not_107_out, not_108_out, Y2);
  and and_36 (and_36_out, not_109_out, not_110_out, not_111_out, Y2, Y0);
  and and_37 (and_37_out, not_112_out, not_113_out, Y2, Y1);
  and and_38 (and_38_out, not_114_out, not_115_out, Y2, Y1, Y0);
  and and_39 (and_39_out, not_116_out, Y3);
  and and_40 (and_40_out, not_117_out, not_118_out, not_119_out, Y3, Y0);
  and and_41 (and_41_out, not_120_out, not_121_out, Y3, Y1);
  and and_42 (and_42_out, not_122_out, not_123_out, Y3, Y1, Y0);
  and and_43 (and_43_out, not_124_out, Y3, Y2);
  and and_44 (and_44_out, not_125_out, not_126_out, Y3, Y2, Y0);
  and and_45 (and_45_out, not_127_out, Y3, Y2, Y1);
  and and_46 (and_46_out, not_128_out, Y3, Y2, Y1, Y0);
  or or_1 (Gt, and_1_out, and_2_out, and_3_out, and_4_out, and_5_out, and_6_out, and_7_out, and_8_out, and_9_out, and_10_out, and_11_out, and_12_out, and_13_out, and_14_out, and_15_out);
  or or_2 (Equal, and_16_out, and_17_out, and_18_out, and_19_out, and_20_out, and_21_out, and_22_out, and_23_out, and_24_out, and_25_out, and_26_out, and_27_out, and_28_out, and_29_out, and_30_out, and_31_out);
  or or_3 (Lt, and_32_out, and_33_out, and_34_out, and_35_out, and_36_out, and_37_out, and_38_out, and_39_out, and_40_out, and_41_out, and_42_out, and_43_out, and_44_out, and_45_out, and_46_out);
endmodule

// 8位无符号比较器
module \_8位无符号比较器_已设计完成  (
  input  [7:0] X,
  input  [7:0] Y,
  output Gt,
  output Equal,
  output Lt
);

  wire and_1_out, and_2_out, \n4位无符号比较器_已设计完成_1_equal , \n4位无符号比较器_已设计完成_1_gt , \n4位无符号比较器_已设计完成_1_lt ,
       \n4位无符号比较器_已设计完成_2_equal , \n4位无符号比较器_已设计完成_2_gt , \n4位无符号比较器_已设计完成_2_lt ;

  // Probe on X
  // Probe on Y
  \_4位无符号比较器_已设计完成  \u_4位无符号比较器_已设计完成_1  (
    .X3(X[7]), .X2(X[6]), .X1(X[5]), .X0(X[4]), .Y3(Y[7]), .Y2(Y[6]), .Y1(Y[5]), .Y0(Y[4]),
    .Gt(\n4位无符号比较器_已设计完成_1_gt ), .Equal(\n4位无符号比较器_已设计完成_1_equal ), .Lt(\n4位无符号比较器_已设计完成_1_lt ));
  \_4位无符号比较器_已设计完成  \u_4位无符号比较器_已设计完成_2  (
    .X3(X[3]), .X2(X[2]), .X1(X[1]), .X0(X[0]), .Y3(Y[3]), .Y2(Y[2]), .Y1(Y[1]), .Y0(Y[0]),
    .Gt(\n4位无符号比较器_已设计完成_2_gt ), .Equal(\n4位无符号比较器_已设计完成_2_equal ), .Lt(\n4位无符号比较器_已设计完成_2_lt ));
  and and_1 (and_1_out, \n4位无符号比较器_已设计完成_1_equal , \n4位无符号比较器_已设计完成_2_gt );
  and and_2 (and_2_out, \n4位无符号比较器_已设计完成_1_equal , \n4位无符号比较器_已设计完成_2_lt );
  or or_1 (Gt, \n4位无符号比较器_已设计完成_1_gt , and_1_out);
  and and_3 (Equal, \n4位无符号比较器_已设计完成_1_equal , \n4位无符号比较器_已设计完成_2_equal );
  or or_2 (Lt, \n4位无符号比较器_已设计完成_1_lt , and_2_out);

  // Notes on the sheet:
  //   输入管脚
  //   逻辑功能：利用4位无符号比较器,增加适当电路设计8位无符号比较器
  //   以上管脚名称及位置均不要移动，利用下方的隧道信号用画电路图方式设计8位无符号比较器
  //   输出管脚
endmodule

// 32位无符号比较器
module \_32位无符号比较器_已设计完成  (
  input  [31:0] X,
  input  [31:0] Y,
  output Gt,
  output Equal,
  output Lt
);

  wire and_1_out, and_2_out, and_3_out, and_4_out, and_5_out, and_6_out, \n8位无符号比较器_已设计完成_1_equal ,
       \n8位无符号比较器_已设计完成_1_gt , \n8位无符号比较器_已设计完成_1_lt , \n8位无符号比较器_已设计完成_2_equal , \n8位无符号比较器_已设计完成_2_gt ,
       \n8位无符号比较器_已设计完成_2_lt , \n8位无符号比较器_已设计完成_3_equal , \n8位无符号比较器_已设计完成_3_gt , \n8位无符号比较器_已设计完成_3_lt ,
       \n8位无符号比较器_已设计完成_4_equal , \n8位无符号比较器_已设计完成_4_gt , \n8位无符号比较器_已设计完成_4_lt ;

  // Probe on X
  // Probe on Y
  \_8位无符号比较器_已设计完成  \u_8位无符号比较器_已设计完成_1  (
    .X(X[7:0]), .Y(Y[7:0]), .Gt(\n8位无符号比较器_已设计完成_1_gt ), .Equal(\n8位无符号比较器_已设计完成_1_equal ),
    .Lt(\n8位无符号比较器_已设计完成_1_lt ));
  \_8位无符号比较器_已设计完成  \u_8位无符号比较器_已设计完成_2  (
    .X(X[15:8]), .Y(Y[15:8]), .Gt(\n8位无符号比较器_已设计完成_2_gt ), .Equal(\n8位无符号比较器_已设计完成_2_equal ),
    .Lt(\n8位无符号比较器_已设计完成_2_lt ));
  \_8位无符号比较器_已设计完成  \u_8位无符号比较器_已设计完成_3  (
    .X(X[23:16]), .Y(Y[23:16]), .Gt(\n8位无符号比较器_已设计完成_3_gt ), .Equal(\n8位无符号比较器_已设计完成_3_equal ),
    .Lt(\n8位无符号比较器_已设计完成_3_lt ));
  \_8位无符号比较器_已设计完成  \u_8位无符号比较器_已设计完成_4  (
    .X(X[31:24]), .Y(Y[31:24]), .Gt(\n8位无符号比较器_已设计完成_4_gt ), .Equal(\n8位无符号比较器_已设计完成_4_equal ),
    .Lt(\n8位无符号比较器_已设计完成_4_lt ));
  and and_1 (and_1_out, \n8位无符号比较器_已设计完成_4_equal , \n8位无符号比较器_已设计完成_3_equal , \n8位无符号比较器_已设计完成_2_equal , \n8位无符号比较器_已设计完成_1_gt );
  and and_2 (and_2_out, \n8位无符号比较器_已设计完成_4_equal , \n8位无符号比较器_已设计完成_3_equal , \n8位无符号比较器_已设计完成_2_gt );
  and and_3 (and_3_out, \n8位无符号比较器_已设计完成_4_equal , \n8位无符号比较器_已设计完成_3_gt );
  and and_4 (and_4_out, \n8位无符号比较器_已设计完成_1_lt , \n8位无符号比较器_已设计完成_2_equal , \n8位无符号比较器_已设计完成_3_equal , \n8位无符号比较器_已设计完成_4_equal );
  and and_5 (and_5_out, \n8位无符号比较器_已设计完成_2_lt , \n8位无符号比较器_已设计完成_3_equal , \n8位无符号比较器_已设计完成_4_equal );
  and and_6 (and_6_out, \n8位无符号比较器_已设计完成_3_lt , \n8位无符号比较器_已设计完成_4_equal );
  or or_1 (Gt, and_1_out, and_2_out, and_3_out, \n8位无符号比较器_已设计完成_4_gt );
  and and_7 (Equal, \n8位无符号比较器_已设计完成_1_equal , \n8位无符号比较器_已设计完成_2_equal , \n8位无符号比较器_已设计完成_3_equal , \n8位无符号比较器_已设计完成_4_equal );
  or or_2 (Lt, and_4_out, and_5_out, and_6_out, \n8位无符号比较器_已设计完成_4_lt );

  // Notes on the sheet:
  //   输入管脚
  //   逻辑功能：利用8位无符号比较器,增加适当电路设计32位无符号比较器
  //   以上管脚名称及位置均不要移动，利用下方的隧道信号用画电路图方式设计32位无符号比较器
  //   输出管脚
endmodule

// 4位有符号比较器
module \_4位有符号比较器_已设计完成  (
  input  X3,
  input  X2,
  input  X1,
  input  X0,
  input  Y3,
  input  Y2,
  input  Y1,
  input  Y0,
  output Gt,
  output Equal,
  output Lt
);

  wire and_1_out, and_2_out, and_3_out, and_4_out, and_5_out, and_6_out, and_7_out, and_8_out, and_9_out,
       and_10_out, and_11_out, and_12_out, and_13_out, and_14_out, and_15_out, and_16_out, and_17_out,
       and_18_out, and_19_out, and_20_out, and_21_out, and_22_out, and_23_out, and_24_out, and_25_out,
       and_26_out, and_27_out, and_28_out, and_29_out, and_30_out, and_31_out, and_32_out, and_33_out,
       and_34_out, and_35_out, and_36_out, and_37_out, and_38_out, and_39_out, and_40_out, and_41_out,
       and_42_out, and_43_out, and_44_out, and_45_out, not_1_out, not_2_out, not_3_out, not_4_out, not_5_out,
       not_6_out, not_7_out, not_8_out, not_9_out, not_10_out, not_11_out, not_12_out, not_13_out,
       not_14_out, not_15_out, not_16_out, not_17_out, not_18_out, not_19_out, not_20_out, not_21_out,
       not_22_out, not_23_out, not_24_out, not_25_out, not_26_out, not_27_out, not_28_out, not_29_out,
       not_30_out, not_31_out, not_32_out, not_33_out, not_34_out, not_35_out, not_36_out, not_37_out,
       not_38_out, not_39_out, not_40_out, not_41_out, not_42_out, not_43_out, not_44_out, not_45_out,
       not_46_out, not_47_out, not_48_out, not_49_out, not_50_out, not_51_out, not_52_out, not_53_out,
       not_54_out, not_55_out, not_56_out, not_57_out, not_58_out, not_59_out, not_60_out, not_61_out,
       not_62_out, not_63_out, not_64_out, not_65_out, not_66_out, not_67_out, not_68_out, not_69_out,
       not_70_out, not_71_out, not_72_out, not_73_out, not_74_out, not_75_out, not_76_out, not_77_out,
       not_78_out, not_79_out, not_80_out, not_81_out, not_82_out, not_83_out, not_84_out, not_85_out,
       not_86_out, not_87_out, not_88_out, not_89_out, not_90_out, not_91_out, not_92_out, not_93_out,
       not_94_out, not_95_out, not_96_out, not_97_out, not_98_out, not_99_out, not_100_out, not_101_out,
       not_102_out, not_103_out, not_104_out, not_105_out, not_106_out, not_107_out, not_108_out,
       not_109_out, not_110_out, not_111_out, not_112_out, not_113_out, not_114_out, not_115_out,
       not_116_out, not_117_out, not_118_out, not_119_out, not_120_out, not_121_out, not_122_out;

  not not_1 (not_1_out, X3);
  not not_2 (not_2_out, X3);
  not not_3 (not_3_out, Y2);
  not not_4 (not_4_out, Y1);
  not not_5 (not_5_out, Y0);
  not not_6 (not_6_out, Y2);
  not not_7 (not_7_out, Y1);
  not not_8 (not_8_out, Y0);
  not not_9 (not_9_out, X3);
  not not_10 (not_10_out, Y2);
  not not_11 (not_11_out, Y1);
  not not_12 (not_12_out, Y2);
  not not_13 (not_13_out, Y1);
  not not_14 (not_14_out, X3);
  not not_15 (not_15_out, Y2);
  not not_16 (not_16_out, Y0);
  not not_17 (not_17_out, Y2);
  not not_18 (not_18_out, Y0);
  not not_19 (not_19_out, X3);
  not not_20 (not_20_out, Y2);
  not not_21 (not_21_out, Y2);
  not not_22 (not_22_out, X3);
  not not_23 (not_23_out, Y1);
  not not_24 (not_24_out, Y0);
  not not_25 (not_25_out, Y1);
  not not_26 (not_26_out, Y0);
  not not_27 (not_27_out, X3);
  not not_28 (not_28_out, Y1);
  not not_29 (not_29_out, Y1);
  not not_30 (not_30_out, X3);
  not not_31 (not_31_out, Y0);
  not not_32 (not_32_out, Y0);
  not not_33 (not_33_out, X3);
  not not_34 (not_34_out, X2);
  not not_35 (not_35_out, X1);
  not not_36 (not_36_out, X0);
  not not_37 (not_37_out, Y3);
  not not_38 (not_38_out, Y2);
  not not_39 (not_39_out, Y1);
  not not_40 (not_40_out, Y0);
  not not_41 (not_41_out, X3);
  not not_42 (not_42_out, X2);
  not not_43 (not_43_out, X1);
  not not_44 (not_44_out, Y3);
  not not_45 (not_45_out, Y2);
  not not_46 (not_46_out, Y1);
  not not_47 (not_47_out, X3);
  not not_48 (not_48_out, X2);
  not not_49 (not_49_out, X0);
  not not_50 (not_50_out, Y3);
  not not_51 (not_51_out, Y2);
  not not_52 (not_52_out, Y0);
  not not_53 (not_53_out, X3);
  not not_54 (not_54_out, X2);
  not not_55 (not_55_out, Y3);
  not not_56 (not_56_out, Y2);
  not not_57 (not_57_out, X3);
  not not_58 (not_58_out, X1);
  not not_59 (not_59_out, X0);
  not not_60 (not_60_out, Y3);
  not not_61 (not_61_out, Y1);
  not not_62 (not_62_out, Y0);
  not not_63 (not_63_out, X3);
  not not_64 (not_64_out, X1);
  not not_65 (not_65_out, Y3);
  not not_66 (not_66_out, Y1);
  not not_67 (not_67_out, X3);
  not not_68 (not_68_out, X0);
  not not_69 (not_69_out, Y3);
  not not_70 (not_70_out, Y0);
  not not_71 (not_71_out, X3);
  not not_72 (not_72_out, Y3);
  not not_73 (not_73_out, X2);
  not not_74 (not_74_out, X1);
  not not_75 (not_75_out, Y2);
  not not_76 (not_76_out, Y1);
  not not_77 (not_77_out, X2);
  not not_78 (not_78_out, X0);
  not not_79 (not_79_out, Y2);
  not not_80 (not_80_out, Y0);
  not not_81 (not_81_out, X2);
  not not_82 (not_82_out, Y2);
  not not_83 (not_83_out, X1);
  not not_84 (not_84_out, X0);
  not not_85 (not_85_out, Y1);
  not not_86 (not_86_out, Y0);
  not not_87 (not_87_out, X1);
  not not_88 (not_88_out, Y1);
  not not_89 (not_89_out, X0);
  not not_90 (not_90_out, Y0);
  not not_91 (not_91_out, X2);
  not not_92 (not_92_out, X1);
  not not_93 (not_93_out, X0);
  not not_94 (not_94_out, Y3);
  not not_95 (not_95_out, X2);
  not not_96 (not_96_out, X1);
  not not_97 (not_97_out, Y3);
  not not_98 (not_98_out, X2);
  not not_99 (not_99_out, X0);
  not not_100 (not_100_out, Y3);
  not not_101 (not_101_out, X2);
  not not_102 (not_102_out, Y3);
  not not_103 (not_103_out, X1);
  not not_104 (not_104_out, X0);
  not not_105 (not_105_out, Y3);
  not not_106 (not_106_out, X1);
  not not_107 (not_107_out, Y3);
  not not_108 (not_108_out, X0);
  not not_109 (not_109_out, Y3);
  not not_110 (not_110_out, X2);
  not not_111 (not_111_out, X1);
  not not_112 (not_112_out, X0);
  not not_113 (not_113_out, Y3);
  not not_114 (not_114_out, X2);
  not not_115 (not_115_out, X1);
  not not_116 (not_116_out, X2);
  not not_117 (not_117_out, X0);
  not not_118 (not_118_out, X2);
  not not_119 (not_119_out, X1);
  not not_120 (not_120_out, X0);
  not not_121 (not_121_out, X1);
  not not_122 (not_122_out, X0);
  and and_1 (and_1_out, not_1_out, Y3);
  and and_2 (and_2_out, not_2_out, X0, not_3_out, not_4_out, not_5_out);
  and and_3 (and_3_out, X0, Y3, not_6_out, not_7_out, not_8_out);
  and and_4 (and_4_out, not_9_out, X1, not_10_out, not_11_out);
  and and_5 (and_5_out, X1, Y3, not_12_out, not_13_out);
  and and_6 (and_6_out, not_14_out, X1, X0, not_15_out, not_16_out);
  and and_7 (and_7_out, X1, X0, Y3, not_17_out, not_18_out);
  and and_8 (and_8_out, not_19_out, X2, not_20_out);
  and and_9 (and_9_out, X2, Y3, not_21_out);
  and and_10 (and_10_out, not_22_out, X2, X0, not_23_out, not_24_out);
  and and_11 (and_11_out, X2, X0, Y3, not_25_out, not_26_out);
  and and_12 (and_12_out, not_27_out, X2, X1, not_28_out);
  and and_13 (and_13_out, X2, X1, Y3, not_29_out);
  and and_14 (and_14_out, not_30_out, X2, X1, X0, not_31_out);
  and and_15 (and_15_out, X2, X1, X0, Y3, not_32_out);
  and and_16 (and_16_out, not_33_out, not_34_out, not_35_out, not_36_out, not_37_out, not_38_out, not_39_out, not_40_out);
  and and_17 (and_17_out, not_41_out, not_42_out, not_43_out, X0, not_44_out, not_45_out, not_46_out, Y0);
  and and_18 (and_18_out, not_47_out, not_48_out, X1, not_49_out, not_50_out, not_51_out, Y1, not_52_out);
  and and_19 (and_19_out, not_53_out, not_54_out, X1, X0, not_55_out, not_56_out, Y1, Y0);
  and and_20 (and_20_out, not_57_out, X2, not_58_out, not_59_out, not_60_out, Y2, not_61_out, not_62_out);
  and and_21 (and_21_out, not_63_out, X2, not_64_out, X0, not_65_out, Y2, not_66_out, Y0);
  and and_22 (and_22_out, not_67_out, X2, X1, not_68_out, not_69_out, Y2, Y1, not_70_out);
  and and_23 (and_23_out, not_71_out, X2, X1, X0, not_72_out, Y2, Y1, Y0);
  and and_24 (and_24_out, X3, not_73_out, not_74_out, X0, Y3, not_75_out, not_76_out, Y0);
  and and_25 (and_25_out, X3, not_77_out, X1, not_78_out, Y3, not_79_out, Y1, not_80_out);
  and and_26 (and_26_out, X3, not_81_out, X1, X0, Y3, not_82_out, Y1, Y0);
  and and_27 (and_27_out, X3, X2, not_83_out, not_84_out, Y3, Y2, not_85_out, not_86_out);
  and and_28 (and_28_out, X3, X2, not_87_out, X0, Y3, Y2, not_88_out, Y0);
  and and_29 (and_29_out, X3, X2, X1, not_89_out, Y3, Y2, Y1, not_90_out);
  and and_30 (and_30_out, X3, X2, X1, X0, Y3, Y2, Y1, Y0);
  and and_31 (and_31_out, not_91_out, not_92_out, not_93_out, not_94_out, Y0);
  and and_32 (and_32_out, not_95_out, not_96_out, not_97_out, Y1);
  and and_33 (and_33_out, not_98_out, not_99_out, not_100_out, Y1, Y0);
  and and_34 (and_34_out, not_101_out, not_102_out, Y2);
  and and_35 (and_35_out, not_103_out, not_104_out, not_105_out, Y2, Y0);
  and and_36 (and_36_out, not_106_out, not_107_out, Y2, Y1);
  and and_37 (and_37_out, not_108_out, not_109_out, Y2, Y1, Y0);
  and and_38 (and_38_out, X3, not_110_out, not_111_out, not_112_out);
  and and_39 (and_39_out, X3, not_113_out);
  and and_40 (and_40_out, X3, not_114_out, not_115_out, Y1);
  and and_41 (and_41_out, X3, not_116_out, not_117_out, Y1, Y0);
  and and_42 (and_42_out, X3, not_118_out, Y2);
  and and_43 (and_43_out, X3, not_119_out, not_120_out, Y2, Y0);
  and and_44 (and_44_out, X3, not_121_out, Y2, Y1);
  and and_45 (and_45_out, X3, not_122_out, Y2, Y1, Y0);
  or or_1 (Gt, and_1_out, and_2_out, and_3_out, and_4_out, and_5_out, and_6_out, and_7_out, and_8_out, and_9_out, and_10_out, and_11_out, and_12_out, and_13_out, and_14_out, and_15_out);
  or or_2 (Equal, and_16_out, and_17_out, and_18_out, and_19_out, and_20_out, and_21_out, and_22_out, and_23_out, and_24_out, and_25_out, and_26_out, and_27_out, and_28_out, and_29_out, and_30_out);
  or or_3 (Lt, and_31_out, and_32_out, and_33_out, and_34_out, and_35_out, and_36_out, and_37_out, and_38_out, and_39_out, and_40_out, and_41_out, and_42_out, and_43_out, and_44_out, and_45_out);
endmodule

module \_8位有符号比较器  (
  input  [7:0] X,
  input  [7:0] Y,
  output Gt,
  output Equal,
  output Lt
);

  wire and_1_out, and_2_out, \n4位无符号比较器_已设计完成_1_equal , \n4位无符号比较器_已设计完成_1_gt , \n4位无符号比较器_已设计完成_1_lt ,
       \n4位有符号比较器_已设计完成_1_equal , \n4位有符号比较器_已设计完成_1_gt , \n4位有符号比较器_已设计完成_1_lt ;

  // Probe on X
  // Probe on Y
  \_4位有符号比较器_已设计完成  \u_4位有符号比较器_已设计完成_1  (
    .X3(X[7]), .X2(X[6]), .X1(X[5]), .X0(X[4]), .Y3(Y[7]), .Y2(Y[6]), .Y1(Y[5]), .Y0(Y[4]),
    .Gt(\n4位有符号比较器_已设计完成_1_gt ), .Equal(\n4位有符号比较器_已设计完成_1_equal ), .Lt(\n4位有符号比较器_已设计完成_1_lt ));
  \_4位无符号比较器_已设计完成  \u_4位无符号比较器_已设计完成_1  (
    .X3(X[3]), .X2(X[2]), .X1(X[1]), .X0(X[0]), .Y3(Y[3]), .Y2(Y[2]), .Y1(Y[1]), .Y0(Y[0]),
    .Gt(\n4位无符号比较器_已设计完成_1_gt ), .Equal(\n4位无符号比较器_已设计完成_1_equal ), .Lt(\n4位无符号比较器_已设计完成_1_lt ));
  and and_1 (and_1_out, \n4位有符号比较器_已设计完成_1_equal , \n4位无符号比较器_已设计完成_1_gt );
  and and_2 (and_2_out, \n4位有符号比较器_已设计完成_1_equal , \n4位无符号比较器_已设计完成_1_lt );
  or or_1 (Gt, \n4位有符号比较器_已设计完成_1_gt , and_1_out);
  and and_3 (Equal, \n4位有符号比较器_已设计完成_1_equal , \n4位无符号比较器_已设计完成_1_equal );
  or or_2 (Lt, \n4位有符号比较器_已设计完成_1_lt , and_2_out);

  // Notes on the sheet:
  //   输入管脚
  //   以上管脚名称及位置均不要移动，利用下方的隧道信号用画电路图方式设计8位有符号比较器
  //   逻辑功能：利用4位有符号比较器,增加适当电路设计8位有符号比较器
  //   输出管脚
endmodule

// 32位有符号比较器
module \_32位有符号比较器_已设计完成  (
  input  [31:0] X,
  input  [31:0] Y,
  output Gt,
  output Equal,
  output Lt
);

  wire and_1_out, and_2_out, and_3_out, and_4_out, and_5_out, and_6_out, \n8位无符号比较器_已设计完成_1_equal ,
       \n8位无符号比较器_已设计完成_1_gt , \n8位无符号比较器_已设计完成_1_lt , \n8位无符号比较器_已设计完成_2_equal , \n8位无符号比较器_已设计完成_2_gt ,
       \n8位无符号比较器_已设计完成_2_lt , \n8位无符号比较器_已设计完成_3_equal , \n8位无符号比较器_已设计完成_3_gt , \n8位无符号比较器_已设计完成_3_lt ,
       \n8位有符号比较器_1_equal , \n8位有符号比较器_1_gt , \n8位有符号比较器_1_lt ;

  // Probe on X
  // Probe on Y
  \_8位无符号比较器_已设计完成  \u_8位无符号比较器_已设计完成_1  (
    .X(X[7:0]), .Y(Y[7:0]), .Gt(\n8位无符号比较器_已设计完成_1_gt ), .Equal(\n8位无符号比较器_已设计完成_1_equal ),
    .Lt(\n8位无符号比较器_已设计完成_1_lt ));
  \_8位无符号比较器_已设计完成  \u_8位无符号比较器_已设计完成_2  (
    .X(X[15:8]), .Y(Y[15:8]), .Gt(\n8位无符号比较器_已设计完成_2_gt ), .Equal(\n8位无符号比较器_已设计完成_2_equal ),
    .Lt(\n8位无符号比较器_已设计完成_2_lt ));
  \_8位无符号比较器_已设计完成  \u_8位无符号比较器_已设计完成_3  (
    .X(X[23:16]), .Y(Y[23:16]), .Gt(\n8位无符号比较器_已设计完成_3_gt ), .Equal(\n8位无符号比较器_已设计完成_3_equal ),
    .Lt(\n8位无符号比较器_已设计完成_3_lt ));
  \_8位有符号比较器  \u_8位有符号比较器_1  (
    .X(X[31:24]), .Y(Y[31:24]), .Gt(\n8位有符号比较器_1_gt ), .Equal(\n8位有符号比较器_1_equal ), .Lt(\n8位有符号比较器_1_lt ));
  and and_1 (and_1_out, \n8位无符号比较器_已设计完成_1_gt , \n8位无符号比较器_已设计完成_1_equal , \n8位无符号比较器_已设计完成_3_equal , \n8位有符号比较器_1_equal );
  and and_2 (and_2_out, \n8位无符号比较器_已设计完成_2_gt , \n8位无符号比较器_已设计完成_3_equal , \n8位有符号比较器_1_equal );
  and and_3 (and_3_out, \n8位无符号比较器_已设计完成_3_gt , \n8位有符号比较器_1_equal );
  and and_4 (and_4_out, \n8位无符号比较器_已设计完成_1_lt , \n8位无符号比较器_已设计完成_2_equal , \n8位无符号比较器_已设计完成_3_equal , \n8位有符号比较器_1_equal );
  and and_5 (and_5_out, \n8位无符号比较器_已设计完成_3_equal , \n8位无符号比较器_已设计完成_2_lt , \n8位有符号比较器_1_equal );
  and and_6 (and_6_out, \n8位无符号比较器_已设计完成_3_lt , \n8位有符号比较器_1_equal );
  or or_1 (Gt, and_1_out, and_2_out, \n8位有符号比较器_1_gt , and_3_out);
  and and_7 (Equal, \n8位无符号比较器_已设计完成_1_equal , \n8位无符号比较器_已设计完成_2_equal , \n8位无符号比较器_已设计完成_3_equal , \n8位有符号比较器_1_equal );
  or or_2 (Lt, and_4_out, and_5_out, \n8位有符号比较器_1_lt , and_6_out);

  // Notes on the sheet:
  //   输入管脚
  //   逻辑功能：利用8位有符号比较器,增加适当电路设计32位有符号比较器
  //   以上管脚名称及位置均不要移动，利用下方的隧道信号用画电路图方式设计32位有符号比较器
  //   输出管脚
endmodule

// 32位有符号乘法
module \_32位有符号乘法_已设计完成  (
  input  [31:0] X,
  input  [31:0] Y,
  output [31:0] Hi,
  output [31:0] Lo
);

  wire [0:0] adder_4_cout;
  wire [31:0] multiplier_1_cout, multiplier_1_out, X_t, xor_1_out, xor_2_out, xor_4_out, xor_5_out, Y_t;
  wire [31:31] xor_3_out;

  // Probe on X
  // Probe on X_t
  // Probe on Y
  // Probe on Y_t
  assign xor_1_out = X ^ {32{X[31]}};  // XOR_Gate xor_1, 32 bits wide
  Adder #(.width(32)) adder_1 (.a(xor_1_out), .b({{31{1'b0}}, X[31]}), .out(X_t), .cin(1'b0));  // open: cout
  assign xor_2_out = Y ^ {32{Y[31]}};  // XOR_Gate xor_2, 32 bits wide
  Adder #(.width(32)) adder_2 (.a(xor_2_out), .b({{31{1'b0}}, Y[31]}), .out(Y_t), .cin(1'b0));  // open: cout
  Multiplier #(.width(32)) multiplier_1 (
    .a(X_t), .b(Y_t), .out(multiplier_1_out), .cout(multiplier_1_cout));  // open: cin
  xor xor_3 (xor_3_out[31], X[31], Y[31]);
  assign xor_4_out = multiplier_1_cout ^ {32{xor_3_out[31]}};  // XOR_Gate xor_4, 32 bits wide
  assign xor_5_out = multiplier_1_out ^ {32{xor_3_out[31]}};  // XOR_Gate xor_5, 32 bits wide
  Adder #(.width(32)) adder_3 (.a(xor_4_out), .b({{31{1'b0}}, adder_4_cout[0]}), .out(Hi), .cin(1'b0));  // open: cout
  Adder #(.width(32)) adder_4 (
    .a(xor_5_out), .b({{31{1'b0}}, xor_3_out[31]}), .out(Lo), .cin(1'b0), .cout(adder_4_cout[0]));

  // Notes on the sheet:
  //   输入管脚
  //   求X的绝对值
  //   求Y的绝对值
  //   逻辑功能：利用32位无符号乘法器添加适当电路，设计32位有符号乘法器
  //   以上管脚名称及位置均不要移动，利用下方的隧道信号用画电路图方式设计32位有符号乘法器
  //   输出管脚
  //   求X×Y的补码
endmodule

module RISC_ALU (
  input  [31:0] X,
  input  [3:0] ALUOP,
  input  [31:0] Y,
  output Signed_Overflow,
  output UnSigned_Overflow,
  output [31:0] Result2,
  output Equal,
  output [31:0] Result
);

  wire \n32位快速进位加法器_1_c31 , \n32位快速进位加法器_1_c32 , \n32位快速进位加法器_2_c31 , \n32位快速进位加法器_2_c32 ,
       \n32位无符号比较器_已设计完成_1_equal , \n32位有符号比较器_已设计完成_1_equal , not_2_out, xor_2_out, xor_3_out;
  wire [0:0] \n32位无符号比较器_已设计完成_1_lt , \n32位有符号比较器_已设计完成_1_lt ;
  wire [31:0] and_1_out, divider_1_out, divider_1_rem, multiplier_1_cout, multiplier_1_out,
       \n32位低成本移位寄存器_已设计完成_1_result_sll , \n32位低成本移位寄存器_已设计完成_1_result_sra ,
       \n32位低成本移位寄存器_已设计完成_1_result_srl , \n32位快速进位加法器_1_s , \n32位快速进位加法器_2_s , \n32位有符号乘法_已设计完成_1_hi ,
       \n32位有符号乘法_已设计完成_1_lo , nor_1_out, not_1_out, or_1_out, xor_1_out;

  // Probe on X
  // Probe on X
  // Probe on Y
  // Probe on Y
  \_32位低成本移位寄存器_已设计完成  \u_32位低成本移位寄存器_已设计完成_1  (
    .shift_op(ALUOP[1:0]), .X(Y), .Y(X), .result_srl(\n32位低成本移位寄存器_已设计完成_1_result_srl ),
    .result_sra(\n32位低成本移位寄存器_已设计完成_1_result_sra ), .result_sll(\n32位低成本移位寄存器_已设计完成_1_result_sll ));
  \_32位快速进位加法器  \u_32位快速进位加法器_1  (
    .Y(Y), .X(X), .Cin(1'b0), .C31(\n32位快速进位加法器_1_c31 ), .C32(\n32位快速进位加法器_1_c32 ), .S(\n32位快速进位加法器_1_s ));
  assign not_1_out = ~Y;  // NOT_Gate not_1, 32 bits wide
  \_32位快速进位加法器  \u_32位快速进位加法器_2  (
    .Y(not_1_out), .X(X), .Cin(1'b1), .C31(\n32位快速进位加法器_2_c31 ), .C32(\n32位快速进位加法器_2_c32 ),
    .S(\n32位快速进位加法器_2_s ));
  \_32位有符号比较器_已设计完成  \u_32位有符号比较器_已设计完成_1  (
    .Equal(\n32位有符号比较器_已设计完成_1_equal ), .Lt(\n32位有符号比较器_已设计完成_1_lt [0]), .X(X), .Y(Y));  // open: Gt
  \_32位无符号比较器_已设计完成  \u_32位无符号比较器_已设计完成_1  (
    .Equal(\n32位无符号比较器_已设计完成_1_equal ), .Lt(\n32位无符号比较器_已设计完成_1_lt [0]), .X(X), .Y(Y));  // open: Gt
  \_32位有符号乘法_已设计完成  \u_32位有符号乘法_已设计完成_1  (.X(X), .Y(Y), .Lo(\n32位有符号乘法_已设计完成_1_lo ), .Hi(\n32位有符号乘法_已设计完成_1_hi ));
  Multiplier #(.width(32)) multiplier_1 (.a(X), .b(Y), .out(multiplier_1_out), .cout(multiplier_1_cout));  // open: cin
  Divider #(.width(32)) divider_1 (.a(X), .b(Y), .out(divider_1_out), .rem(divider_1_rem));  // open: upper
  assign and_1_out = X & Y;  // AND_Gate and_1, 32 bits wide
  assign or_1_out = X | Y;  // OR_Gate or_1, 32 bits wide
  assign xor_1_out = X ^ Y;  // XOR_Gate xor_1, 32 bits wide
  assign nor_1_out = ~(X | Y);  // NOR_Gate nor_1, 32 bits wide
  // Probe on Result2
  // Probe on Result2
  // Probe on Result
  // Probe on Result
  xor xor_2 (xor_2_out, \n32位快速进位加法器_1_c32 , \n32位快速进位加法器_1_c31 );
  xor xor_3 (xor_3_out, \n32位快速进位加法器_2_c32 , \n32位快速进位加法器_2_c31 );
  not not_2 (not_2_out, \n32位快速进位加法器_2_c32 );
  Multiplexer #(.select(4), .width(32), .disabled("Z"), .enable("false")) multiplexer_1 (
    .in0(\n32位低成本移位寄存器_已设计完成_1_result_sll ), .in1(\n32位低成本移位寄存器_已设计完成_1_result_sra ),
    .in2(\n32位低成本移位寄存器_已设计完成_1_result_srl ), .in3(multiplier_1_out), .in4(divider_1_out),
    .in5(\n32位快速进位加法器_1_s ), .in6(\n32位快速进位加法器_2_s ), .in7(and_1_out), .in8(or_1_out), .in9(xor_1_out),
    .in10(nor_1_out), .in11({{31{1'b0}}, \n32位有符号比较器_已设计完成_1_lt [0]}),
    .in12({{31{1'b0}}, \n32位无符号比较器_已设计完成_1_lt [0]}), .in13(\n32位有符号乘法_已设计完成_1_lo ), .in14({32{1'b0}}),
    .in15({32{1'b0}}), .out(Result), .sel(ALUOP));
  Multiplexer #(.select(4), .width(32), .disabled("Z"), .enable("false")) multiplexer_2 (
    .in0({32{1'b0}}), .in1({32{1'b0}}), .in2({32{1'b0}}), .in3(multiplier_1_cout), .in4(divider_1_rem),
    .in5({32{1'b0}}), .in6({32{1'b0}}), .in7({32{1'b0}}), .in8({32{1'b0}}), .in9({32{1'b0}}),
    .in10({32{1'b0}}), .in11({32{1'b0}}), .in12({32{1'b0}}), .in13(\n32位有符号乘法_已设计完成_1_hi ),
    .in14({32{1'b0}}), .in15({32{1'b0}}), .out(Result2), .sel(ALUOP));
  Multiplexer #(.select(4), .width(1), .disabled("Z"), .enable("false")) multiplexer_3 (
    .in0(1'b0), .in1(1'b0), .in2(1'b0), .in3(1'b0), .in4(1'b0), .in5(xor_2_out), .in6(xor_3_out), .in7(1'b0),
    .in8(1'b0), .in9(1'b0), .in10(1'b0), .in11(1'b0), .in12(1'b0), .in13(1'b0), .in14(1'b0), .in15(1'b0),
    .out(Signed_Overflow), .sel(ALUOP));
  Multiplexer #(.select(4), .width(1), .disabled("Z"), .enable("false")) multiplexer_4 (
    .in0(1'b0), .in1(1'b0), .in2(1'b0), .in3(1'b0), .in4(1'b0), .in5(\n32位快速进位加法器_1_c32 ), .in6(not_2_out),
    .in7(1'b0), .in8(1'b0), .in9(1'b0), .in10(1'b0), .in11(1'b0), .in12(1'b0), .in13(1'b0), .in14(1'b0),
    .in15(1'b0), .out(UnSigned_Overflow), .sel(ALUOP));
  or or_2 (Equal, \n32位有符号比较器_已设计完成_1_equal , \n32位无符号比较器_已设计完成_1_equal );

  // Other names for the same wires on the sheet: OF = Signed_Overflow; UOF = UnSigned_Overflow

  // Notes on the sheet:
  //   输入管脚
  //   逻辑功能：利用16位先行进位加法器及4位先行进位信号，级联生成片内并行及片间并行进位的32位加法器
  //   以上管脚名称及位置均不要移动，利用下方的隧道信号用画电路图方式设32位先行进位逻辑
  //   输出管脚
endmodule
