// Logisim project Controller.circ as structural Verilog: 3 circuits, main circuit 硬布线控制器(CU)
module \指令译码器  (
  input  [5:0] op,
  input  [5:0] func,
  output iADD,
  output iSUB,
  output iAND,
  output iOR,
  output iXOR,
  output iSLT,
  output iSLL,
  output iSRL,
  output iSRA,
  output iJR,
  output SYSCALL,
  output R_Type,
  output iLW,
  output iLHU,
  output iLBU,
  output iSW,
  output iSH,
  output iSB,
  output iADDi,
  output iANDi,
  output iORi,
  output iLUi,
  output iBEQ,
  output iBNE,
  output iJ,
  output iJAL
);

  wire not_1_out, not_2_out, not_3_out, not_4_out, not_5_out, not_6_out, not_7_out, not_8_out, not_9_out,
       not_10_out, not_11_out, not_12_out;

  not not_1 (not_1_out, op[5]);
  not not_2 (not_2_out, op[4]);
  not not_3 (not_3_out, op[3]);
  not not_4 (not_4_out, op[2]);
  not not_5 (not_5_out, op[1]);
  not not_6 (not_6_out, op[0]);
  and and_1 (R_Type, not_1_out, not_2_out, not_3_out, not_4_out, not_5_out, not_6_out);
  not not_7 (not_7_out, func[5]);
  not not_8 (not_8_out, func[4]);
  not not_9 (not_9_out, func[3]);
  not not_10 (not_10_out, func[2]);
  not not_11 (not_11_out, func[1]);
  not not_12 (not_12_out, func[0]);
  and and_2 (iLW, op[5], not_2_out, not_3_out, not_4_out, op[1], op[0]);
  and and_3 (iADD, func[5], not_8_out, not_9_out, R_Type, not_10_out, not_11_out, not_12_out);
  and and_4 (iSW, op[5], not_2_out, op[3], not_4_out, op[1], op[0]);
  and and_5 (iSUB, func[5], not_8_out, not_9_out, not_10_out, func[1], not_12_out, R_Type);
  and and_6 (iADDi, not_1_out, not_2_out, op[3], not_4_out, not_5_out, not_6_out);
  and and_7 (iAND, R_Type, func[5], not_8_out, not_9_out, func[2], not_11_out, not_12_out);
  and and_8 (iANDi, not_1_out, not_2_out, op[3], op[2], not_5_out, not_6_out);
  and and_9 (iOR, R_Type, func[5], not_8_out, func[2], not_11_out, func[0], not_9_out);
  and and_10 (iORi, not_1_out, not_2_out, op[3], op[2], not_5_out, op[0]);
  and and_11 (iXOR, R_Type, func[5], not_8_out, not_9_out, func[2], func[1], not_12_out);
  and and_12 (iLUi, not_1_out, not_2_out, op[3], op[2], op[1], op[0]);
  and and_13 (iSLT, R_Type, func[5], not_8_out, func[3], not_10_out, func[1], not_12_out);
  and and_14 (iBEQ, not_1_out, not_2_out, not_3_out, op[2], not_5_out, not_6_out);
  and and_15 (iSLL, R_Type, not_7_out, not_8_out, not_9_out, not_10_out, not_11_out, not_12_out);
  and and_16 (iBNE, not_1_out, not_2_out, not_3_out, op[2], not_5_out, op[0]);
  and and_17 (iSRL, R_Type, not_7_out, not_8_out, not_9_out, not_10_out, func[1], not_12_out);
  and and_18 (iJ, not_1_out, not_2_out, not_3_out, not_4_out, op[1], not_6_out);
  and and_19 (iSRA, R_Type, not_7_out, not_8_out, not_9_out, not_10_out, func[1], func[0]);
  and and_20 (iJAL, not_1_out, not_2_out, not_3_out, not_4_out, op[1], op[0]);
  and and_21 (iJR, R_Type, not_7_out, not_8_out, func[3], not_10_out, not_11_out, not_12_out);
  and and_22 (iLBU, op[5], not_2_out, not_3_out, op[2], not_5_out, not_6_out);
  and and_23 (SYSCALL, R_Type, not_7_out, not_8_out, func[3], func[2], not_11_out, not_12_out);
  and and_24 (iSB, op[5], not_2_out, op[3], not_4_out, not_5_out, not_6_out);
  and and_25 (iLHU, op[5], not_2_out, not_3_out, op[2], not_5_out, op[0]);
  and and_26 (iSH, op[5], not_2_out, op[3], not_4_out, not_5_out, op[0]);

  // Notes on the sheet:
  //   指令操作码输入管脚
  //   R类指令
  //   以上管脚名称及位置均不要移动，利用下方的隧道信号用画电路图方式设计MIPS32控制器指令译码器逻辑
  //   I、J类指令译码器
  //   R类指令译码器
  //   逻辑功能：根据输入指令的OP码及Function码，采用硬布线方式生成指令系统10条指令中的4条指令（or、jr、lui、jal）所需的指令译码器
  //   6条指令：add、syscall、sw、addi、beq、j已实现
  //   译码输出管脚
  //   I类指令
  //   J类指令
endmodule

module \微命令生成电路  (
  input  Z,
  input  iADD,
  input  iSUB,
  input  iAND,
  input  iOR,
  input  iXOR,
  input  iSLT,
  input  iSLL,
  input  iSRL,
  input  iSRA,
  input  iJR,
  input  SYSCALL,
  input  R_Type,
  input  iLW,
  input  iLHU,
  input  iLBU,
  input  iSW,
  input  iSH,
  input  iSB,
  input  iADDi,
  input  iANDi,
  input  iORi,
  input  iLUi,
  input  iBEQ,
  input  iBNE,
  input  iJ,
  input  iJAL,
  output RStoPC,
  output TargettoPC,
  output MemtoReg,
  output Branch,
  output nWriteMem,
  output [3:0] ALUOP,
  output ShamttoA,
  output Lui,
  output ImmtoB,
  output Signextend,
  output nWriteReg,
  output PCtoR31,
  output RegDst,
  output Halt,
  output [1:0] Mode
);

  wire and_1_out, and_2_out, and_3_out, and_4_out, not_1_out, not_2_out, not_3_out, not_4_out, not_5_out;

  not not_1 (not_1_out, Z);
  not not_2 (not_2_out, SYSCALL);
  not not_3 (not_3_out, iJR);
  not not_4 (not_4_out, SYSCALL);
  and and_1 (and_1_out, not_4_out, not_5_out, R_Type);
  not not_5 (not_5_out, iJR);
  or or_1 (TargettoPC, iJAL, iJ);
  and and_2 (and_2_out, Z, iBEQ);
  and and_3 (and_3_out, iBNE, not_1_out);
  not not_6 (nWriteMem, iSW);
  or or_2 (ALUOP[3], iOR, iSLT);
  and and_4 (and_4_out, not_2_out, not_3_out, R_Type);
  or or_3 (RegDst, and_1_out, iSLL);
  or or_4 (Branch, and_2_out, and_3_out);
  or or_5 (ALUOP[2], iADDi, iADD, iSW, iLW);
  or or_6 (ALUOP[0], iADDi, iADD, iSLT, iSW, iLW);
  or or_7 (ImmtoB, iLUi, iSW, iADDi, iLW);
  or or_8 (Signextend, iSW, iLW, iBNE, iBEQ, iADDi);
  nor nor_1 (nWriteReg, and_4_out, iLUi, iLW, iJAL, iADDi, iSLL);

  assign ALUOP[1] = iSLT;
  assign Halt = SYSCALL;
  assign Lui = iLUi;
  assign MemtoReg = iLW;
  assign Mode = 2'b00;
  assign PCtoR31 = iJAL;
  assign RStoPC = iJR;
  assign ShamttoA = iSLL;

  // Other names for the same wires on the sheet: ALUOP_0 = ALUOP[0]; ALUOP_1 = iSLT; ALUOP_2 = ALUOP[2];
  //   ALUOP_3 = ALUOP[3]; TargertoPC = TargettoPC

  // Notes on the sheet:
  //   0标志位
  //   I、J类指令
  //   逻辑功能：根据指令译码器的译码结果，采用硬布线方式生成指令系统10条指令中的4条指令（or、jr、lui、jal）所需的微命令
  //   输入管脚
  //   6条指令：add、sw、addi、beq、j、syscall已实现
  //   以上管脚名称及位置均不要移动，利用下方的隧道信号用画电路图方式设计MIPS32控制器微命令逻辑
  //   输出管脚
  //   R类指令
endmodule

module \硬布线控制器_CU  (
  input  z,
  input  [5:0] op,
  input  [5:0] func,
  output RStoPC,
  output TargettoPC,
  output MemtoREG,
  output Branch,
  output nWriteMem,
  output [3:0] ALUOP,
  output ShamttoA,
  output Lui,
  output ImmtoB,
  output SignExtend,
  output nWriteReg,
  output PCtoR31,
  output RegDst,
  output Halt,
  output [1:0] Mode
);

  wire \指令译码器_1_iadd , \指令译码器_1_iaddi , \指令译码器_1_iand , \指令译码器_1_iandi , \指令译码器_1_ibeq , \指令译码器_1_ibne ,
       \指令译码器_1_ij , \指令译码器_1_ijal , \指令译码器_1_ijr , \指令译码器_1_ilbu , \指令译码器_1_ilhu , \指令译码器_1_ilui ,
       \指令译码器_1_ilw , \指令译码器_1_ior , \指令译码器_1_iori , \指令译码器_1_isb , \指令译码器_1_ish , \指令译码器_1_isll ,
       \指令译码器_1_islt , \指令译码器_1_isra , \指令译码器_1_isrl , \指令译码器_1_isub , \指令译码器_1_isw , \指令译码器_1_ixor ,
       \指令译码器_1_r_type , \指令译码器_1_syscall ;

  \指令译码器  \u_指令译码器_1  (
    .op(op), .func(func), .iADD(\指令译码器_1_iadd ), .iSUB(\指令译码器_1_isub ), .iAND(\指令译码器_1_iand ),
    .iOR(\指令译码器_1_ior ), .iXOR(\指令译码器_1_ixor ), .iSLT(\指令译码器_1_islt ), .iSLL(\指令译码器_1_isll ),
    .iSRL(\指令译码器_1_isrl ), .iJR(\指令译码器_1_ijr ), .SYSCALL(\指令译码器_1_syscall ), .R_Type(\指令译码器_1_r_type ),
    .iLW(\指令译码器_1_ilw ), .iLHU(\指令译码器_1_ilhu ), .iLBU(\指令译码器_1_ilbu ), .iSW(\指令译码器_1_isw ),
    .iSH(\指令译码器_1_ish ), .iSB(\指令译码器_1_isb ), .iADDi(\指令译码器_1_iaddi ), .iANDi(\指令译码器_1_iandi ),
    .iORi(\指令译码器_1_iori ), .iLUi(\指令译码器_1_ilui ), .iBEQ(\指令译码器_1_ibeq ), .iBNE(\指令译码器_1_ibne ),
    .iJ(\指令译码器_1_ij ), .iJAL(\指令译码器_1_ijal ), .iSRA(\指令译码器_1_isra ));
  \微命令生成电路  \u_微命令生成电路_1  (
    .Z(z), .iADD(\指令译码器_1_iadd ), .iSUB(\指令译码器_1_isub ), .iAND(\指令译码器_1_iand ), .iOR(\指令译码器_1_ior ),
    .iXOR(\指令译码器_1_ixor ), .iSLT(\指令译码器_1_islt ), .iSLL(\指令译码器_1_isll ), .iSRL(\指令译码器_1_isrl ),
    .iSRA(\指令译码器_1_isra ), .iJR(\指令译码器_1_ijr ), .SYSCALL(\指令译码器_1_syscall ), .R_Type(\指令译码器_1_r_type ),
    .iLW(\指令译码器_1_ilw ), .iLHU(\指令译码器_1_ilhu ), .iLBU(\指令译码器_1_ilbu ), .iSW(\指令译码器_1_isw ),
    .iSH(\指令译码器_1_ish ), .iSB(\指令译码器_1_isb ), .iADDi(\指令译码器_1_iaddi ), .iANDi(\指令译码器_1_iandi ),
    .iORi(\指令译码器_1_iori ), .iLUi(\指令译码器_1_ilui ), .iBEQ(\指令译码器_1_ibeq ), .iBNE(\指令译码器_1_ibne ),
    .iJ(\指令译码器_1_ij ), .iJAL(\指令译码器_1_ijal ), .RStoPC(RStoPC), .TargettoPC(TargettoPC), .MemtoReg(MemtoREG),
    .Branch(Branch), .nWriteMem(nWriteMem), .ALUOP(ALUOP), .ShamttoA(ShamttoA), .Lui(Lui), .ImmtoB(ImmtoB),
    .Signextend(SignExtend), .nWriteReg(nWriteReg), .PCtoR31(PCtoR31), .RegDst(RegDst), .Halt(Halt),
    .Mode(Mode));

  // Other names for the same wires on the sheet: nWritMem = nWriteMem; TargertoPC = TargettoPC

  // Notes on the sheet:
  //   输入管脚
  //   输出管脚
  //   以上管脚名称及位置均不要移动，利用下方的隧道信号用画电路图方式设计MIPS32控制器指令译码器逻辑
  //   逻辑功能：调用指令译码器和微命令产生电路设计支持10条指令的MIPS32CPU控制器
  //   10条指令：add、sll、syscall、lw、sw、sb、addi、beq、j、jal
endmodule
