// Logisim project IO.circ as structural Verilog: 3 circuits, main circuit 输入输出接口
module \输入输出接口  (
  input  nWE,
  input  [8:0] addr,
  input  [31:0] KEY,
  input  [31:0] din,
  input  [31:0] SW,
  input  clk,
  input  nrst,
  output [31:0] dout,
  output [8:0] LEDG,
  output [17:0] LEDR,
  output [7:0] LCD_DATA,
  output LCD_EN,
  output LCD_RS,
  output LCD_RW,
  output LCD_ON,
  output LCD_ON_2,
  output [6:0] HEX0,
  output [6:0] HEX1,
  output [6:0] HEX2,
  output [6:0] HEX3,
  output [6:0] HEX4,
  output [6:0] HEX5,
  output [6:0] HEX6,
  output [6:0] HEX7
);

  wire and_1_out, and_2_out, and_3_out, HEX0_E, HEX1_E, HEX2_E, HEX3_E, HEX4_E, HEX5_E, HEX6_E, HEX7_E,
       KEY_E, LCD_Command_E, LCD_Data_E, LEDG_E, LEDR_E, not_1_out, not_2_out, not_3_out, not_4_out,
       not_5_out, SW_E;
  wire [6:0] \数码管显示译码器_1_s0 ;

  and and_1 (and_1_out, LCD_Command_E, ~nWE);  // AND_Gate
  and and_2 (and_2_out, LCD_Data_E, ~nWE);  // AND_Gate
  \I_O地址译码器  \i_o地址译码器_1  (
    .nWE(nWE), .addr(addr), .SW_E(SW_E), .HEX0_E(HEX0_E), .KEY_E(KEY_E), .HEX1_E(HEX1_E), .LEDG_E(LEDG_E),
    .HEX2_E(HEX2_E), .LEDR_E(LEDR_E), .HEX3_E(HEX3_E), .HEX4_E(HEX4_E), .LCD_Command_E(LCD_Command_E),
    .HEX5_E(HEX5_E), .LCD_Data_E(LCD_Data_E), .HEX6_E(HEX6_E), .HEX7_E(HEX7_E));
  Register #(.width(3), .trigger("rising"), .Select("low")) register_1 (
    .D(din[2:0]), .en(and_1_out), .Q({LCD_EN, LCD_RS, LCD_RW}), .clk(clk), .clr(not_1_out));
  not not_1 (not_1_out, nrst);
  assign dout = and_3_out ? {{24{1'b0}}, LCD_DATA} : 32'bz;  // Controlled_Buffer controlled_buffer_1
  Register #(.width(8), .trigger("rising"), .Select("low")) register_2 (
    .D(din[7:0]), .en(and_2_out), .Q(LCD_DATA), .clk(clk), .clr(not_2_out));
  not not_2 (not_2_out, nrst);
  // Probe on {LCD_EN, LCD_RS, LCD_RW}
  and and_3 (and_3_out, LCD_RW, LCD_Data_E);
  // Probe on LCD_DATA
  // Probe on SW
  assign dout = SW_E ? SW : 32'bz;  // Controlled_Buffer controlled_buffer_2
  // Probe on KEY
  assign dout = KEY_E ? KEY : 32'bz;  // Controlled_Buffer controlled_buffer_3
  // Probe on din
  // Probe on din
  Register #(.width(9), .trigger("rising"), .Select("low")) register_3 (
    .D(din[8:0]), .en(LEDG_E), .Q(LEDG), .clk(clk), .clr(not_3_out));
  not not_3 (not_3_out, nrst);
  Register #(.width(18), .trigger("rising"), .Select("low")) register_4 (
    .D(din[17:0]), .en(LEDR_E), .Q(LEDR), .clk(clk), .clr(not_4_out));
  not not_4 (not_4_out, nrst);
  \数码管显示译码器  \u_数码管显示译码器_1  (
    .d3(din[3]), .d2(din[2]), .d1(din[1]), .d0(din[0]), .s0(\数码管显示译码器_1_s0 [0]), .s1(\数码管显示译码器_1_s0 [1]),
    .s2(\数码管显示译码器_1_s0 [2]), .s3(\数码管显示译码器_1_s0 [3]), .s4(\数码管显示译码器_1_s0 [4]), .s5(\数码管显示译码器_1_s0 [5]),
    .s6(\数码管显示译码器_1_s0 [6]));
  Register #(.width(7), .trigger("rising"), .Select("low")) register_5 (
    .D(\数码管显示译码器_1_s0 ), .en(HEX0_E), .Q(HEX0), .clk(clk), .preset(not_5_out));  // open: clr, cs
  Register #(.width(7), .trigger("rising"), .Select("low")) register_6 (
    .D(\数码管显示译码器_1_s0 ), .en(HEX1_E), .Q(HEX1), .clk(clk), .preset(not_5_out));  // open: clr, cs
  Register #(.width(7), .trigger("rising"), .Select("low")) register_7 (
    .D(\数码管显示译码器_1_s0 ), .en(HEX2_E), .Q(HEX2), .clk(clk), .preset(not_5_out));  // open: clr, cs
  Register #(.width(7), .trigger("rising"), .Select("low")) register_8 (
    .D(\数码管显示译码器_1_s0 ), .en(HEX3_E), .Q(HEX3), .clk(clk), .preset(not_5_out));  // open: clr, cs
  Register #(.width(7), .trigger("rising"), .Select("low")) register_9 (
    .D(\数码管显示译码器_1_s0 ), .en(HEX4_E), .Q(HEX4), .clk(clk), .preset(not_5_out));  // open: clr, cs
  Register #(.width(7), .trigger("rising"), .Select("low")) register_10 (
    .D(\数码管显示译码器_1_s0 ), .en(HEX5_E), .Q(HEX5), .clk(clk), .preset(not_5_out));  // open: clr, cs
  Register #(.width(7), .trigger("rising"), .Select("low")) register_11 (
    .D(\数码管显示译码器_1_s0 ), .en(HEX6_E), .Q(HEX6), .clk(clk), .preset(not_5_out));  // open: clr, cs
  Register #(.width(7), .trigger("rising"), .Select("low")) register_12 (
    .D(\数码管显示译码器_1_s0 ), .en(HEX7_E), .Q(HEX7), .clk(clk), .preset(not_5_out));  // open: clr, cs
  not not_5 (not_5_out, nrst);

  assign LCD_ON = 1'b1;
  assign LCD_ON_2 = 1'b0;

  // Notes on the sheet:
  //   I/O地址译码
  //   输入管脚
  //   LCD液晶显示器接口（输入、输出）
  //   逻辑功能：用画电路图的方式设计简单外围设备（拨动开关、按键开关、发光二极管、LCD液晶显示器等）的接口电路
  //   以上管脚名称及位置均不要移动，利用下方的隧道信号用画电路图方式设计IO接口控制逻辑
  //   拨动开关接口（输入）
  //   按键开关接口（输入）
  //   绿色LED接口（输出）
  //   红色LED接口（输出）
  //   输出管脚
  //   数码管接口（输出）
endmodule

module \I_O地址译码器  (
  input  nWE,
  input  [8:0] addr,
  output SW_E,
  output KEY_E,
  output LEDG_E,
  output LEDR_E,
  output LCD_Command_E,
  output LCD_Data_E,
  output HEX0_E,
  output HEX1_E,
  output HEX2_E,
  output HEX3_E,
  output HEX4_E,
  output HEX5_E,
  output HEX6_E,
  output HEX7_E
);

  wire and_3_out, and_4_out, and_5_out, and_6_out, and_7_out, and_8_out, and_9_out, and_10_out, and_11_out,
       and_12_out, and_13_out, not_1_out, not_2_out, not_3_out, not_4_out, not_5_out, not_6_out, not_7_out,
       not_8_out, not_9_out, not_10_out;

  not not_1 (not_1_out, addr[6]);
  not not_2 (not_2_out, addr[7]);
  not not_3 (not_3_out, addr[5]);
  not not_4 (not_4_out, addr[8]);
  not not_5 (not_5_out, addr[4]);
  not not_6 (not_6_out, addr[1]);
  not not_7 (not_7_out, addr[2]);
  not not_8 (not_8_out, addr[3]);
  not not_9 (not_9_out, addr[0]);
  not not_10 (not_10_out, nWE);
  and and_1 (SW_E, not_9_out, not_6_out, addr[2], not_8_out, not_5_out, addr[5], not_1_out, not_2_out, addr[8]);
  and and_2 (KEY_E, not_9_out, not_6_out, not_7_out, not_8_out, addr[4], addr[5], not_1_out, not_2_out, addr[8]);
  and and_3 (and_3_out, not_9_out, not_6_out, addr[2], addr[3], not_5_out, addr[5], not_1_out, not_2_out, addr[8]);
  and and_4 (and_4_out, not_9_out, not_6_out, not_7_out, addr[3], not_5_out, addr[5], not_1_out, not_2_out, addr[8]);
  and and_5 (and_5_out, not_9_out, not_6_out, not_7_out, not_8_out, not_5_out, not_3_out, not_1_out, not_2_out, addr[8]);
  and and_6 (and_6_out, not_9_out, not_6_out, addr[2], not_8_out, not_5_out, not_3_out, not_1_out, not_2_out, addr[8]);
  and and_7 (and_7_out, not_9_out, not_6_out, not_7_out, addr[3], not_5_out, not_3_out, not_1_out, not_2_out, addr[8]);
  and and_8 (and_8_out, not_9_out, not_6_out, addr[2], addr[3], not_5_out, not_3_out, not_1_out, not_2_out, addr[8]);
  and and_9 (and_9_out, not_9_out, not_6_out, not_7_out, not_8_out, addr[4], not_3_out, not_1_out, not_2_out, addr[8]);
  and and_10 (and_10_out, not_9_out, not_6_out, addr[2], not_8_out, addr[4], not_3_out, not_1_out, not_2_out, addr[8]);
  and and_11 (and_11_out, not_9_out, not_6_out, not_7_out, addr[3], addr[4], not_3_out, not_1_out, not_2_out, addr[8]);
  and and_12 (and_12_out, not_9_out, not_6_out, addr[2], addr[3], addr[4], not_3_out, not_1_out, not_2_out, addr[8]);
  and and_13 (and_13_out, not_9_out, not_6_out, not_7_out, not_8_out, not_5_out, not_3_out, addr[6], not_2_out, addr[8]);
  and and_14 (LCD_Data_E, addr[0], not_6_out, not_7_out, not_8_out, not_5_out, not_3_out, addr[6], not_2_out, addr[8]);
  and and_15 (LEDG_E, not_10_out, and_3_out);
  and and_16 (LEDR_E, not_10_out, and_4_out);
  and and_17 (HEX0_E, not_10_out, and_5_out);
  and and_18 (HEX1_E, not_10_out, and_6_out);
  and and_19 (HEX2_E, not_10_out, and_7_out);
  and and_20 (HEX3_E, not_10_out, and_8_out);
  and and_21 (HEX4_E, not_10_out, and_9_out);
  and and_22 (HEX5_E, not_10_out, and_10_out);
  and and_23 (HEX6_E, not_10_out, and_11_out);
  and and_24 (HEX7_E, not_10_out, and_12_out);
  and and_25 (LCD_Command_E, not_10_out, and_13_out);

  // Notes on the sheet:
  //   设备名称
  //   拨动开关
  //   红色LED
  //   绿色LED
  //   按键开关
  //   数码管0
  //   数码管1
  //   数码管2
  //   数码管3
  //   数码管4
  //   数码管5
  //   数码管6
  //   数码管7
  //   液晶显示器
  //   液晶显示器
  //   输入管脚
  //   使能信号名称
  //   SW_E
  //   LEDR_E
  //   LEDG_E
  //   KEY_E
  //   HEX0_E
  //   HEX1_E
  //   HEX2_E
  //   HEX3_E
  //   HEX4_E
  //   HEX5_E
  //   HEX6_E
  //   HEX7_E
  //   LCD_Command_E
  //   LCD_Data_E
  //   设备地址
  //   124H(1 0010 0100)
  //   128H(1 0010 1000)
  //   12CH(1 0010 1100)
  //   130H(1 0011 0000)
  //   100H(1 0000 0000)
  //   104H(1 0000 0100)
  //   108H(1 0000 1000)
  //   10CH(1 0000 1100)
  //   110H(1 0001 0000)
  //   114H(1 0001 0100)
  //   118H(1 0001 1000)
  //   11CH(1 0001 1100)
  //   140H(1 0100 0000)
  //   141H(1 0100 0001)
  //   逻辑功能：根据输入的IO地址码，生成IO设备的使能控制信号（实际MIPS的IO地址空间于此不同，但设计方法类似）
  //   nWE
  //   x
  //   0
  //   0
  //   x
  //   0
  //   0
  //   0
  //   0
  //   0
  //   0
  //   0
  //   0
  //   0
  //   x
  //   以上管脚名称及位置均不要移动，利用下方的隧道信号按左下表中的信息完成I/O地址译码电路设计
  //   备注
  //   需要设计
  //   需要设计
  //   需要设计
  //   需要设计
  //   输出管脚
  //   外围设备地址译码器
endmodule

module \数码管显示译码器  (
  input  d3,
  input  d2,
  input  d1,
  input  d0,
  output s0,
  output s1,
  output s2,
  output s3,
  output s4,
  output s5,
  output s6
);

  wire and_1_out, and_2_out, and_3_out, and_4_out, and_5_out, and_6_out, and_7_out, and_8_out, and_9_out,
       and_10_out, and_11_out, and_12_out, and_13_out, and_14_out, and_15_out, and_16_out, and_17_out,
       and_18_out, and_19_out, and_20_out, and_21_out, and_22_out, and_23_out, and_24_out, and_25_out,
       not_1_out, not_2_out, not_3_out, not_4_out, not_5_out, not_6_out, not_7_out, not_8_out, not_9_out,
       not_10_out, not_11_out, not_12_out, not_13_out, not_14_out, not_15_out, not_16_out, not_17_out,
       not_18_out, not_19_out, not_20_out, not_21_out, not_22_out, not_23_out, not_24_out, not_25_out,
       not_26_out, not_27_out, not_28_out, not_29_out, not_30_out, not_31_out, not_32_out, not_33_out,
       not_34_out, not_35_out, not_36_out, not_37_out, not_38_out, not_39_out, not_40_out, not_41_out;

  not not_1 (not_1_out, d3);
  not not_2 (not_2_out, d2);
  not not_3 (not_3_out, d1);
  not not_4 (not_4_out, d3);
  not not_5 (not_5_out, d1);
  not not_6 (not_6_out, d0);
  not not_7 (not_7_out, d2);
  not not_8 (not_8_out, d1);
  not not_9 (not_9_out, d3);
  not not_10 (not_10_out, d1);
  not not_11 (not_11_out, d0);
  not not_12 (not_12_out, d0);
  not not_13 (not_13_out, d3);
  not not_14 (not_14_out, d2);
  not not_15 (not_15_out, d0);
  not not_16 (not_16_out, d0);
  not not_17 (not_17_out, d3);
  not not_18 (not_18_out, d2);
  not not_19 (not_19_out, d1);
  not not_20 (not_20_out, d3);
  not not_21 (not_21_out, d1);
  not not_22 (not_22_out, d0);
  not not_23 (not_23_out, d2);
  not not_24 (not_24_out, d0);
  not not_25 (not_25_out, d3);
  and and_1 (and_1_out, not_25_out, d0);
  not not_26 (not_26_out, d2);
  and and_2 (and_2_out, not_26_out, not_27_out, d0);
  not not_27 (not_27_out, d1);
  not not_28 (not_28_out, d3);
  and and_3 (and_3_out, not_28_out, d2, not_29_out);
  not not_29 (not_29_out, d1);
  not not_30 (not_30_out, d3);
  not not_31 (not_31_out, d2);
  not not_32 (not_32_out, d3);
  not not_33 (not_33_out, d2);
  not not_34 (not_34_out, d3);
  not not_35 (not_35_out, d1);
  not not_36 (not_36_out, d3);
  not not_37 (not_37_out, d2);
  not not_38 (not_38_out, d1);
  not not_39 (not_39_out, d3);
  not not_40 (not_40_out, d1);
  not not_41 (not_41_out, d0);
  and and_4 (and_4_out, not_1_out, not_2_out, not_3_out, d0);
  and and_5 (and_5_out, not_4_out, d2, not_5_out, not_6_out);
  and and_6 (and_6_out, d3, not_7_out, d1, d0);
  and and_7 (and_7_out, d3, d2, not_8_out, d0);
  and and_8 (and_8_out, not_9_out, d2, not_10_out, d0);
  and and_9 (and_9_out, d2, d1, not_11_out);
  and and_10 (and_10_out, d3, d1, d0);
  and and_11 (and_11_out, d3, d2, not_12_out);
  and and_12 (and_12_out, not_13_out, not_14_out, d1, not_15_out);
  and and_13 (and_13_out, d3, d2, not_16_out);
  or or_1 (s2, and_12_out, and_13_out, and_14_out);
  and and_14 (and_14_out, d3, d2, d1);
  and and_15 (and_15_out, not_17_out, not_18_out, not_19_out, d0);
  and and_16 (and_16_out, not_20_out, d2, not_21_out, not_22_out);
  and and_17 (and_17_out, d2, d1, d0);
  and and_18 (and_18_out, d3, not_23_out, d1, not_24_out);
  or or_2 (s4, and_1_out, and_2_out, and_3_out);
  and and_19 (and_19_out, not_30_out, not_31_out, d0);
  and and_20 (and_20_out, not_32_out, not_33_out, d1);
  and and_21 (and_21_out, not_34_out, d1, d0);
  and and_22 (and_22_out, d3, d2, not_35_out, d0);
  and and_23 (and_23_out, not_36_out, not_37_out, not_38_out);
  or or_3 (s6, and_23_out, and_24_out, and_25_out);
  and and_24 (and_24_out, not_39_out, d2, d1, d0);
  and and_25 (and_25_out, d3, d2, not_40_out, not_41_out);
  or or_4 (s0, and_4_out, and_5_out, and_6_out, and_7_out);
  or or_5 (s1, and_8_out, and_9_out, and_10_out, and_11_out);
  or or_6 (s3, and_15_out, and_16_out, and_17_out, and_18_out);
  or or_7 (s5, and_19_out, and_20_out, and_21_out, and_22_out);
endmodule
