// Logisim project MIPS32CPU_IO.circ as structural Verilog: 7 circuits, main circuit MIPS32-CPU
// 控制器（CU）
module MIPS32_CPU (
  input  nrst,
  output [7:0] LCD_DATA,
  output LCD_EN,
  output LCD_RS,
  output LCD_RW,
  output LCD_ON,
  output LCD_BLON
);

  wire clk, not_1_out, not_2_out, not_3_out, risc_alu_1_equal, \硬布线控制器_cu_1_branch , \硬布线控制器_cu_1_halt ,
       \硬布线控制器_cu_1_immtob , \硬布线控制器_cu_1_lui , \硬布线控制器_cu_1_memtoreg , \硬布线控制器_cu_1_nwritemem ,
       \硬布线控制器_cu_1_nwritereg , \硬布线控制器_cu_1_pctor31 , \硬布线控制器_cu_1_regdst , \硬布线控制器_cu_1_rstopc ,
       \硬布线控制器_cu_1_shamttoa , \硬布线控制器_cu_1_signextend , \硬布线控制器_cu_1_targettopc ;
  wire [1:0] \硬布线控制器_cu_1_mode ;
  wire [2:0] button_3_out;
  wire [3:0] \硬布线控制器_cu_1_aluop ;
  wire [4:0] multiplexer_1_out, multiplexer_2_out, rom_1_data_3;
  wire [6:0] \输入输出接口_1_hex0 , \输入输出接口_1_hex1 , \输入输出接口_1_hex2 , \输入输出接口_1_hex3 , \输入输出接口_1_hex4 ,
       \输入输出接口_1_hex5 , \输入输出接口_1_hex6 , \输入输出接口_1_hex7 ;
  wire [8:0] \输入输出接口_1_ledg ;
  wire [15:0] rom_1_data_2;
  wire [17:0] undriven, \输入输出接口_1_ledr ;
  wire [22:0] risc_alu_1_result;
  wire [31:0] adder_1_out, adder_2_out, bit_extender_1_out, bit_extender_2_out, multiplexer_3_out,
       multiplexer_4_out, multiplexer_5_out, multiplexer_6_out, multiplexer_7_out, multiplexer_8_out,
       multiplexer_9_out, multiplexer_10_out, multiplexer_11_out, register_1_q, risc_ram2m_32bit_1_dout,
       riscregfile_1_rdata1, riscregfile_1_rdata2, shifter_1_out, \输入输出接口_1_dout ;
  wire [31:16] rom_1_data;
  wire [31:23] risc_alu_1_result_2;

  // Probe on register_1_q
  // Probe on multiplexer_10_out
  Clock #(.highDuration(1), .lowDuration(1)) u_clk (.out(clk));
  not not_1 (not_1_out, \硬布线控制器_cu_1_halt );
  not not_2 (not_2_out, nrst);
  // Probe on rom_1_data_3
  // Probe on {rom_1_data_2[15:11], rom_1_data_3, rom_1_data_2[5:0]}
  Register #(.width(32), .trigger("rising"), .Select("low")) register_1 (
    .D(multiplexer_10_out), .en(not_1_out), .Q(register_1_q), .clk(clk), .clr(not_2_out));
  // Probe on rom_1_data[31:26]
  ROM #(.addrWidth(10), .dataWidth(32), .Select("low")) rom_1 (
    .addr(register_1_q[11:2]), .data({rom_1_data, rom_1_data_2[15:11], rom_1_data_3, rom_1_data_2[5:0]}));
  // Probe on rom_1_data_2[5:0]
  // Probe on {rom_1_data[25:16], rom_1_data_2[15:11], rom_1_data_3, rom_1_data_2[5:0]}
  Adder #(.width(32)) adder_1 (.a(32'h4), .b(register_1_q), .out(adder_1_out));  // open: cin, cout
  // Probe on rom_1_data[25:21]
  // Probe on rom_1_data[20:16]
  // Probe on rom_1_data_2[15:11]
  \Controller_硬布线控制器_CU  \u_硬布线控制器_cu_1  (
    .op(rom_1_data[31:26]), .RStoPC(\硬布线控制器_cu_1_rstopc ), .TargettoPC(\硬布线控制器_cu_1_targettopc ),
    .MemtoREG(\硬布线控制器_cu_1_memtoreg ), .Branch(\硬布线控制器_cu_1_branch ), .nWriteMem(\硬布线控制器_cu_1_nwritemem ),
    .ALUOP(\硬布线控制器_cu_1_aluop ), .ShamttoA(\硬布线控制器_cu_1_shamttoa ), .Lui(\硬布线控制器_cu_1_lui ),
    .ImmtoB(\硬布线控制器_cu_1_immtob ), .SignExtend(\硬布线控制器_cu_1_signextend ),
    .nWriteReg(\硬布线控制器_cu_1_nwritereg ), .PCtoR31(\硬布线控制器_cu_1_pctor31 ), .RegDst(\硬布线控制器_cu_1_regdst ),
    .Halt(\硬布线控制器_cu_1_halt ), .Mode(\硬布线控制器_cu_1_mode ), .func(rom_1_data_2[5:0]), .z(risc_alu_1_equal));
  Multiplexer #(.select(1), .width(5), .disabled("Z"), .enable("false")) multiplexer_1 (
    .in0(rom_1_data[20:16]), .in1(rom_1_data_2[15:11]), .out(multiplexer_1_out), .sel(\硬布线控制器_cu_1_regdst ));
  assign bit_extender_1_out = {{16{1'b0}}, {rom_1_data_2[15:11], rom_1_data_3, rom_1_data_2[5:0]}};  // Bit_Extender bit_extender_1
  assign bit_extender_2_out = {{16{rom_1_data_2[15]}}, {rom_1_data_2[15:11], rom_1_data_3, rom_1_data_2[5:0]}};  // Bit_Extender bit_extender_2
  Multiplexer #(.select(1), .width(5), .disabled("Z"), .enable("false")) multiplexer_2 (
    .in0(multiplexer_1_out), .in1({5{1'b1}}), .out(multiplexer_2_out), .sel(\硬布线控制器_cu_1_pctor31 ));
  Multiplexer #(.select(1), .width(32), .disabled("Z"), .enable("false")) multiplexer_3 (
    .in0(multiplexer_11_out), .in1(adder_1_out), .out(multiplexer_3_out), .sel(\硬布线控制器_cu_1_pctor31 ));
  // Probe on multiplexer_2_out
  // Probe on multiplexer_3_out
  // DipSwitch #(.NSwitches(18)) dipswitch_1: pin names not known; wires that end beside it: undriven[17], undriven[16], undriven[15], undriven[14], undriven[13], undriven[12], undriven[11], undriven[10], undriven[9], undriven[8], undriven[7], undriven[6]
  Multiplexer #(.select(1), .width(32), .disabled("Z"), .enable("false")) multiplexer_4 (
    .in0(bit_extender_1_out), .in1(bit_extender_2_out), .out(multiplexer_4_out),
    .sel(\硬布线控制器_cu_1_signextend ));
  // Probe on {adder_1_out[31:28], rom_1_data[25:16], rom_1_data_2[15:11], rom_1_data_3, rom_1_data_2[5:0], 2'b00}
  RISCRegfile riscregfile_1 (
    .RAddr1(rom_1_data[25:21]), .RAddr2(rom_1_data[20:16]), .WAddr(multiplexer_2_out),
    .WData(multiplexer_3_out), .nWE(\硬布线控制器_cu_1_nwritereg ), .CLK(clk), .RData1(riscregfile_1_rdata1),
    .RData2(riscregfile_1_rdata2), .nrst(nrst));
  Multiplexer #(.select(1), .width(32), .disabled("Z"), .enable("false")) multiplexer_5 (
    .in0(riscregfile_1_rdata1), .in1(32'h10), .out(multiplexer_5_out), .sel(\硬布线控制器_cu_1_lui ));
  Multiplexer #(.select(1), .width(32), .disabled("Z"), .enable("false")) multiplexer_6 (
    .in0(riscregfile_1_rdata2), .in1(multiplexer_4_out), .out(multiplexer_6_out), .sel(\硬布线控制器_cu_1_immtob ));
  Shifter #(.width(32), .shift("ll")) shifter_1 (.in(multiplexer_4_out), .\dist (5'b00010), .out(shifter_1_out));
  Multiplexer #(.select(1), .width(32), .disabled("Z"), .enable("false")) multiplexer_7 (
    .in0(multiplexer_5_out), .in1({{27{1'b0}}, rom_1_data_3}), .out(multiplexer_7_out),
    .sel(\硬布线控制器_cu_1_shamttoa ));
  // Probe on multiplexer_7_out
  // Probe on multiplexer_6_out
  // Probe on {risc_alu_1_result_2, risc_alu_1_result}
  // Probe on \硬布线控制器_cu_1_aluop 
  Multiplexer #(.select(1), .width(32), .disabled("Z"), .enable("false")) multiplexer_8 (
    .in0(adder_1_out), .in1(adder_2_out), .out(multiplexer_8_out), .sel(\硬布线控制器_cu_1_branch ));
  Adder #(.width(32)) adder_2 (.a(shifter_1_out), .b(adder_1_out), .out(adder_2_out));  // open: cin, cout
  RISC_ALU risc_alu_1 (
    .Equal(risc_alu_1_equal), .X(multiplexer_7_out), .Y(multiplexer_6_out), .ALUOP(\硬布线控制器_cu_1_aluop ),
    .Result({risc_alu_1_result_2, risc_alu_1_result}));  // open: Signed_Overflow, UnSigned_Overflow, Result2
  // Probe on risc_alu_1_result[8:0]
  Button button_1 (.out(button_3_out[2]));
  Button button_2 (.out(button_3_out[1]));
  Multiplexer #(.select(1), .width(32), .disabled("Z"), .enable("false")) multiplexer_9 (
    .in0(multiplexer_8_out),
    .in1({adder_1_out[31:28], rom_1_data[25:16], rom_1_data_2[15:11], rom_1_data_3, rom_1_data_2[5:0], 2'b00}),
    .out(multiplexer_9_out), .sel(\硬布线控制器_cu_1_targettopc ));
  // Probe on risc_alu_1_result
  // Probe on riscregfile_1_rdata2
  Button button_3 (.out(button_3_out[0]));
  _7_Segment_Display #(.active("false")) u_7_segment_display_1 (
    .g(\输入输出接口_1_hex7 [6]), .f(\输入输出接口_1_hex7 [5]), .a(\输入输出接口_1_hex7 [0]), .b(\输入输出接口_1_hex7 [1]),
    .e(\输入输出接口_1_hex7 [4]), .d(\输入输出接口_1_hex7 [3]), .c(\输入输出接口_1_hex7 [2]), .dp(1'b1));
  Multiplexer #(.select(1), .width(32), .disabled("Z"), .enable("false")) multiplexer_10 (
    .in0(multiplexer_9_out), .in1(riscregfile_1_rdata1), .out(multiplexer_10_out), .sel(\硬布线控制器_cu_1_rstopc ));
  RISC_RAM2M_32bit risc_ram2m_32bit_1 (
    .Addr(risc_alu_1_result), .Din(riscregfile_1_rdata2), .Mode(\硬布线控制器_cu_1_mode ),
    .RWn(\硬布线控制器_cu_1_nwritemem ), .CLK(clk), .Dout(risc_ram2m_32bit_1_dout));
  \IO_输入输出接口  \u_输入输出接口_1  (
    .nWE(\硬布线控制器_cu_1_nwritemem ), .addr(risc_alu_1_result[8:0]), .KEY({{29{1'b0}}, button_3_out}),
    .din(riscregfile_1_rdata2), .SW({{14{1'b0}}, undriven}), .clk(clk), .nrst(nrst), .LEDG(\输入输出接口_1_ledg ),
    .LEDR(\输入输出接口_1_ledr ), .dout(\输入输出接口_1_dout ), .LCD_DATA(LCD_DATA), .LCD_RW(LCD_RW), .LCD_ON(LCD_ON),
    .LCD_ON_2(LCD_BLON), .HEX0(\输入输出接口_1_hex0 ), .HEX1(\输入输出接口_1_hex1 ), .HEX2(\输入输出接口_1_hex2 ),
    .HEX3(\输入输出接口_1_hex3 ), .HEX4(\输入输出接口_1_hex4 ), .HEX5(\输入输出接口_1_hex5 ), .HEX6(\输入输出接口_1_hex6 ),
    .HEX7(\输入输出接口_1_hex7 ), .LCD_RS(LCD_RS), .LCD_EN(LCD_EN));
  _7_Segment_Display #(.active("false")) u_7_segment_display_2 (
    .g(\输入输出接口_1_hex6 [6]), .f(\输入输出接口_1_hex6 [5]), .a(\输入输出接口_1_hex6 [0]), .b(\输入输出接口_1_hex6 [1]),
    .e(\输入输出接口_1_hex6 [4]), .d(\输入输出接口_1_hex6 [3]), .c(\输入输出接口_1_hex6 [2]), .dp(1'b1));
  not not_3 (not_3_out, risc_alu_1_result[8]);
  assign \输入输出接口_1_dout  = not_3_out ? risc_ram2m_32bit_1_dout : 32'bz;  // Controlled_Buffer controlled_buffer_1
  Multiplexer #(.select(1), .width(32), .disabled("Z"), .enable("false")) multiplexer_11 (
    .in0({risc_alu_1_result_2, risc_alu_1_result}), .in1(\输入输出接口_1_dout ), .out(multiplexer_11_out),
    .sel(\硬布线控制器_cu_1_memtoreg ));
  // Probe on \输入输出接口_1_dout 
  LED #(.active("true")) led_1 (.in(\输入输出接口_1_ledr [17]));
  _7_Segment_Display #(.active("false")) u_7_segment_display_3 (
    .g(\输入输出接口_1_hex5 [6]), .f(\输入输出接口_1_hex5 [5]), .a(\输入输出接口_1_hex5 [0]), .b(\输入输出接口_1_hex5 [1]),
    .e(\输入输出接口_1_hex5 [4]), .d(\输入输出接口_1_hex5 [3]), .c(\输入输出接口_1_hex5 [2]), .dp(1'b1));
  // Probe on \硬布线控制器_cu_1_mode 
  LED #(.active("true")) led_2 (.in(\输入输出接口_1_ledr [13]));
  LED #(.active("true")) led_3 (.in(\输入输出接口_1_ledr [15]));
  LED #(.active("true")) led_4 (.in(\输入输出接口_1_ledr [14]));
  LED #(.active("true")) led_5 (.in(\输入输出接口_1_ledr [16]));
  _7_Segment_Display #(.active("false")) u_7_segment_display_4 (
    .g(\输入输出接口_1_hex4 [6]), .f(\输入输出接口_1_hex4 [5]), .a(\输入输出接口_1_hex4 [0]), .b(\输入输出接口_1_hex4 [1]),
    .e(\输入输出接口_1_hex4 [4]), .d(\输入输出接口_1_hex4 [3]), .c(\输入输出接口_1_hex4 [2]), .dp(1'b1));
  LED #(.active("true")) led_6 (.in(\输入输出接口_1_ledr [9]));
  LED #(.active("true")) led_7 (.in(\输入输出接口_1_ledr [12]));
  LED #(.active("true")) led_8 (.in(\输入输出接口_1_ledr [10]));
  LED #(.active("true")) led_9 (.in(\输入输出接口_1_ledr [11]));
  _7_Segment_Display #(.active("false")) u_7_segment_display_5 (
    .g(\输入输出接口_1_hex3 [6]), .f(\输入输出接口_1_hex3 [5]), .a(\输入输出接口_1_hex3 [0]), .b(\输入输出接口_1_hex3 [1]),
    .e(\输入输出接口_1_hex3 [4]), .d(\输入输出接口_1_hex3 [3]), .c(\输入输出接口_1_hex3 [2]), .dp(1'b1));
  LED #(.active("true")) led_10 (.in(\输入输出接口_1_ledr [8]));
  LED #(.active("true")) led_11 (.in(\输入输出接口_1_ledr [5]));
  LED #(.active("true")) led_12 (.in(\输入输出接口_1_ledr [6]));
  LED #(.active("true")) led_13 (.in(\输入输出接口_1_ledr [7]));
  _7_Segment_Display #(.active("false")) u_7_segment_display_6 (
    .g(\输入输出接口_1_hex2 [6]), .f(\输入输出接口_1_hex2 [5]), .a(\输入输出接口_1_hex2 [0]), .b(\输入输出接口_1_hex2 [1]),
    .e(\输入输出接口_1_hex2 [4]), .d(\输入输出接口_1_hex2 [3]), .c(\输入输出接口_1_hex2 [2]), .dp(1'b1));
  LED #(.active("true")) led_14 (.in(\输入输出接口_1_ledr [2]));
  LED #(.active("true")) led_15 (.in(\输入输出接口_1_ledr [4]));
  LED #(.active("true")) led_16 (.in(\输入输出接口_1_ledr [1]));
  LED #(.active("true")) led_17 (.in(\输入输出接口_1_ledr [3]));
  LED #(.active("true")) led_18 (.in(\输入输出接口_1_ledg [7]));
  LED #(.active("true")) led_19 (.in(\输入输出接口_1_ledg [8]));
  LED #(.active("true")) led_20 (.in(\输入输出接口_1_ledr [0]));
  _7_Segment_Display #(.active("false")) u_7_segment_display_7 (
    .g(\输入输出接口_1_hex1 [6]), .f(\输入输出接口_1_hex1 [5]), .a(\输入输出接口_1_hex1 [0]), .b(\输入输出接口_1_hex1 [1]),
    .e(\输入输出接口_1_hex1 [4]), .d(\输入输出接口_1_hex1 [3]), .c(\输入输出接口_1_hex1 [2]), .dp(1'b1));
  LED #(.active("true")) led_21 (.in(\输入输出接口_1_ledg [4]));
  LED #(.active("true")) led_22 (.in(\输入输出接口_1_ledg [5]));
  LED #(.active("true")) led_23 (.in(\输入输出接口_1_ledg [3]));
  LED #(.active("true")) led_24 (.in(\输入输出接口_1_ledg [6]));
  _7_Segment_Display #(.active("false")) u_7_segment_display_8 (
    .g(\输入输出接口_1_hex0 [6]), .f(\输入输出接口_1_hex0 [5]), .a(\输入输出接口_1_hex0 [0]), .b(\输入输出接口_1_hex0 [1]),
    .e(\输入输出接口_1_hex0 [4]), .d(\输入输出接口_1_hex0 [3]), .c(\输入输出接口_1_hex0 [2]), .dp(1'b1));
  LED #(.active("true")) led_25 (.in(\输入输出接口_1_ledg [0]));
  LED #(.active("true")) led_26 (.in(\输入输出接口_1_ledg [2]));
  LED #(.active("true")) led_27 (.in(\输入输出接口_1_ledg [1]));

  // Notes on the sheet:
  //   PC
  //   bitaddr
  //   nextPC
  //   target
  //   wordaddr
  //   shamt
  //   imm/offset
  //   时钟及复位信号
  //   op
  //   contents of rom_1 (hex, n*v repeats v):
  //   20080100 20010007 20020006 20030005 20040004 20050003 20060002 20070001 ad000000 ad010004 ad020008
  //   ad03000c ad040010 ad050014 ad060018 ad07001c c
  //   func
  //   rs
  //   rt
  //   rd
  //   regwdata
  //   regwaddr
  //   SW[17:0]
  //   简单外围设备及接口
  //   x
  //   y
  //   x aluop y
  //   aluop
  //   KEY[3:1]
  //   ram bitaddr
  //   Din
  //   Dout
  //   LEDR[18:0]
  //   HEX[7:0]
  //   主机：CPU及内存
  //   LEDG[8:0]
endmodule

module \输入输出接口  (
  input  nWE,
  input  [8:0] addr,
  input  [31:0] KEY,
  input  [31:0] din,
  input  [31:0] SW,
  input  clk,
  input  nrst,
  output [31:0] dout,
  output [8:0] LEDG,
  output [17:0] LEDR,
  output [7:0] LCD_DATA,
  output LCD_EN,
  output LCD_RS,
  output LCD_RW,
  output LCD_ON,
  output LCD_ON_2,
  output [6:0] HEX0,
  output [6:0] HEX1,
  output [6:0] HEX2,
  output [6:0] HEX3,
  output [6:0] HEX4,
  output [6:0] HEX5,
  output [6:0] HEX6,
  output [6:0] HEX7
);

  wire and_1_out, and_2_out, and_3_out, HEX0_E, HEX1_E, HEX2_E, HEX3_E, HEX4_E, HEX5_E, HEX6_E, HEX7_E,
       KEY_E, LCD_Command_E, LCD_Data_E, LEDG_E, LEDR_E, not_1_out, not_2_out, not_3_out, not_4_out,
       not_5_out, SW_E;
  wire [6:0] \数码管显示译码器_1_s0 ;

  and and_1 (and_1_out, LCD_Command_E, ~nWE);  // AND_Gate
  and and_2 (and_2_out, LCD_Data_E, ~nWE);  // AND_Gate
  \I_O地址译码器  \i_o地址译码器_1  (
    .nWE(nWE), .addr(addr), .SW_E(SW_E), .HEX0_E(HEX0_E), .KEY_E(KEY_E), .HEX1_E(HEX1_E), .LEDG_E(LEDG_E),
    .HEX2_E(HEX2_E), .LEDR_E(LEDR_E), .HEX3_E(HEX3_E), .HEX4_E(HEX4_E), .LCD_Command_E(LCD_Command_E),
    .HEX5_E(HEX5_E), .LCD_Data_E(LCD_Data_E), .HEX6_E(HEX6_E), .HEX7_E(HEX7_E));
  Register #(.width(3), .trigger("rising"), .Select("low")) register_1 (
    .D(din[2:0]), .en(and_1_out), .Q({LCD_EN, LCD_RS, LCD_RW}), .clk(clk), .clr(not_1_out));
  not not_1 (not_1_out, nrst);
  assign dout = and_3_out ? {{24{1'b0}}, LCD_DATA} : 32'bz;  // Controlled_Buffer controlled_buffer_1
  Register #(.width(8), .trigger("rising"), .Select("low")) register_2 (
    .D(din[7:0]), .en(and_2_out), .Q(LCD_DATA), .clk(clk), .clr(not_2_out));
  not not_2 (not_2_out, nrst);
  // Probe on {LCD_EN, LCD_RS, LCD_RW}
  and and_3 (and_3_out, LCD_RW, LCD_Data_E);
  // Probe on LCD_DATA
  // Probe on SW
  assign dout = SW_E ? SW : 32'bz;  // Controlled_Buffer controlled_buffer_2
  // Probe on KEY
  assign dout = KEY_E ? KEY : 32'bz;  // Controlled_Buffer controlled_buffer_3
  // Probe on din
  // Probe on din
  Register #(.width(9), .trigger("rising"), .Select("low")) register_3 (
    .D(din[8:0]), .en(LEDG_E), .Q(LEDG), .clk(clk), .clr(not_3_out));
  not not_3 (not_3_out, nrst);
  Register #(.width(18), .trigger("rising"), .Select("low")) register_4 (
    .D(din[17:0]), .en(LEDR_E), .Q(LEDR), .clk(clk), .clr(not_4_out));
  not not_4 (not_4_out, nrst);
  \数码管显示译码器  \u_数码管显示译码器_1  (
    .d3(din[3]), .d2(din[2]), .d1(din[1]), .s0(\数码管显示译码器_1_s0 [0]), .d0(din[0]), .s1(\数码管显示译码器_1_s0 [1]),
    .s2(\数码管显示译码器_1_s0 [2]), .s3(\数码管显示译码器_1_s0 [3]), .s4(\数码管显示译码器_1_s0 [4]), .s5(\数码管显示译码器_1_s0 [5]),
    .s6(\数码管显示译码器_1_s0 [6]));
  Register #(.width(7), .trigger("rising"), .Select("low")) register_5 (
    .D(\数码管显示译码器_1_s0 ), .en(HEX0_E), .Q(HEX0), .clk(clk), .preset(not_5_out));  // open: clr, cs
  Register #(.width(7), .trigger("rising"), .Select("low")) register_6 (
    .D(\数码管显示译码器_1_s0 ), .en(HEX1_E), .Q(HEX1), .clk(clk), .preset(not_5_out));  // open: clr, cs
  Register #(.width(7), .trigger("rising"), .Select("low")) register_7 (
    .D(\数码管显示译码器_1_s0 ), .en(HEX2_E), .Q(HEX2), .clk(clk), .preset(not_5_out));  // open: clr, cs
  Register #(.width(7), .trigger("rising"), .Select("low")) register_8 (
    .D(\数码管显示译码器_1_s0 ), .en(HEX3_E), .Q(HEX3), .clk(clk), .preset(not_5_out));  // open: clr, cs
  Register #(.width(7), .trigger("rising"), .Select("low")) register_9 (
    .D(\数码管显示译码器_1_s0 ), .en(HEX4_E), .Q(HEX4), .clk(clk), .preset(not_5_out));  // open: clr, cs
  Register #(.width(7), .trigger("rising"), .Select("low")) register_10 (
    .D(\数码管显示译码器_1_s0 ), .en(HEX5_E), .Q(HEX5), .clk(clk), .preset(not_5_out));  // open: clr, cs
  Register #(.width(7), .trigger("rising"), .Select("low")) register_11 (
    .D(\数码管显示译码器_1_s0 ), .en(HEX6_E), .Q(HEX6), .clk(clk), .preset(not_5_out));  // open: clr, cs
  Register #(.width(7), .trigger("rising"), .Select("low")) register_12 (
    .D(\数码管显示译码器_1_s0 ), .en(HEX7_E), .Q(HEX7), .clk(clk), .preset(not_5_out));  // open: clr, cs
  not not_5 (not_5_out, nrst);

  assign LCD_ON = 1'b1;
  assign LCD_ON_2 = 1'b0;

  // Notes on the sheet:
  //   I/O地址译码
  //   输入管脚
  //   LCD液晶显示器接口（输入、输出）
  //   逻辑功能：用画电路图的方式设计简单外围设备（拨动开关、按键开关、发光二极管、LCD液晶显示器等）的接口电路
  //   以上管脚名称及位置均不要移动，利用下方的隧道信号用画电路图方式设计IO接口控制逻辑
  //   拨动开关接口（输入）
  //   按键开关接口（输入）
  //   绿色LED接口（输出）
  //   红色LED接口（输出）
  //   输出管脚
  //   数码管接口（输出）
endmodule

module \I_O地址译码器  (
  input  nWE,
  input  [8:0] addr,
  output SW_E,
  output KEY_E,
  output LEDG_E,
  output LEDR_E,
  output LCD_Command_E,
  output LCD_Data_E,
  output HEX0_E,
  output HEX1_E,
  output HEX2_E,
  output HEX3_E,
  output HEX4_E,
  output HEX5_E,
  output HEX6_E,
  output HEX7_E
);

  wire and_3_out, and_4_out, and_5_out, and_6_out, and_7_out, and_8_out, and_9_out, and_10_out, and_11_out,
       and_12_out, not_1_out, not_2_out, not_3_out, not_4_out, not_5_out, not_6_out, not_7_out, not_8_out,
       not_9_out, not_10_out;

  not not_1 (not_1_out, addr[6]);
  not not_2 (not_2_out, addr[5]);
  not not_3 (not_3_out, addr[8]);
  not not_4 (not_4_out, addr[7]);
  not not_5 (not_5_out, addr[3]);
  not not_6 (not_6_out, addr[2]);
  not not_7 (not_7_out, addr[1]);
  not not_8 (not_8_out, addr[4]);
  not not_9 (not_9_out, addr[0]);
  not not_10 (not_10_out, nWE);
  and and_1 (SW_E, not_9_out, not_7_out, addr[2], not_5_out, not_8_out, addr[5], not_1_out, not_4_out, addr[8]);
  and and_2 (KEY_E, not_9_out, not_7_out, not_6_out, not_5_out, addr[4], addr[5], not_1_out, not_4_out, addr[8]);
  and and_3 (and_3_out, not_9_out, not_7_out, addr[2], addr[3], not_8_out, addr[5], not_1_out, not_4_out, addr[8]);
  and and_4 (and_4_out, not_9_out, not_7_out, not_6_out, addr[3], not_8_out, addr[5], not_1_out, not_4_out, addr[8]);
  and and_5 (and_5_out, not_9_out, not_7_out, not_6_out, not_5_out, not_8_out, not_2_out, not_1_out, not_4_out, addr[8]);
  and and_6 (and_6_out, not_9_out, not_7_out, addr[2], not_5_out, not_8_out, not_2_out, not_1_out, not_4_out, addr[8]);
  and and_7 (and_7_out, not_9_out, not_7_out, not_6_out, addr[3], not_8_out, not_2_out, not_1_out, not_4_out, addr[8]);
  and and_8 (and_8_out, not_9_out, not_7_out, addr[2], addr[3], not_8_out, not_2_out, not_1_out, not_4_out, addr[8]);
  and and_9 (and_9_out, not_9_out, not_7_out, not_6_out, not_5_out, addr[4], not_2_out, not_1_out, not_4_out, addr[8]);
  and and_10 (and_10_out, not_9_out, not_7_out, addr[2], not_5_out, addr[4], not_2_out, not_1_out, not_4_out, addr[8]);
  and and_11 (and_11_out, not_9_out, not_7_out, not_6_out, addr[3], addr[4], not_2_out, not_1_out, not_4_out, addr[8]);
  and and_12 (and_12_out, not_9_out, not_7_out, addr[2], addr[3], addr[4], not_2_out, not_1_out, not_4_out, addr[8]);
  and and_13 (LCD_Command_E, not_9_out, not_7_out, not_6_out, not_5_out, not_8_out, not_2_out, addr[6], not_4_out, addr[8]);
  and and_14 (LCD_Data_E, addr[0], not_7_out, not_6_out, not_5_out, not_8_out, not_2_out, addr[6], not_4_out, addr[8]);
  and and_15 (LEDG_E, not_10_out, and_3_out);
  and and_16 (LEDR_E, not_10_out, and_4_out);
  and and_17 (HEX0_E, not_10_out, and_5_out);
  and and_18 (HEX1_E, not_10_out, and_6_out);
  and and_19 (HEX2_E, not_10_out, and_7_out);
  and and_20 (HEX3_E, not_10_out, and_8_out);
  and and_21 (HEX4_E, not_10_out, and_9_out);
  and and_22 (HEX5_E, not_10_out, and_10_out);
  and and_23 (HEX6_E, not_10_out, and_11_out);
  and and_24 (HEX7_E, not_10_out, and_12_out);

  // Notes on the sheet:
  //   设备名称
  //   拨动开关
  //   红色LED
  //   绿色LED
  //   按键开关
  //   数码管0
  //   数码管1
  //   数码管2
  //   数码管3
  //   数码管4
  //   数码管5
  //   数码管6
  //   数码管7
  //   液晶显示器
  //   液晶显示器
  //   输入管脚
  //   使能信号名称
  //   SW_E
  //   LEDR_E
  //   LEDG_E
  //   KEY_E
  //   HEX0_E
  //   HEX1_E
  //   HEX2_E
  //   HEX3_E
  //   HEX4_E
  //   HEX5_E
  //   HEX6_E
  //   HEX7_E
  //   LCD_Command_E
  //   LCD_Data_E
  //   设备地址
  //   124H(1 0010 0100)
  //   128H(1 0010 1000)
  //   12CH(1 0010 1100)
  //   130H(1 0011 0000)
  //   100H(1 0000 0000)
  //   104H(1 0000 0100)
  //   108H(1 0000 1000)
  //   10CH(1 0000 1100)
  //   110H(1 0001 0000)
  //   114H(1 0001 0100)
  //   118H(1 0001 1000)
  //   11CH(1 0001 1100)
  //   140H(1 0100 0000)
  //   141H(1 0100 0001)
  //   逻辑功能：根据输入的IO地址码，生成IO设备的使能控制信号
  //   备注
  //   以上管脚名称及位置均不要移动，利用下方的隧道信号按左下表中的信息设计I/O地址译码电路
  //   输出管脚
  //   外围设备地址译码器
endmodule

module \数码管显示译码器  (
  input  d3,
  input  d2,
  input  d1,
  input  d0,
  output s0,
  output s1,
  output s2,
  output s3,
  output s4,
  output s5,
  output s6
);

  wire and_1_out, and_2_out, and_3_out, and_4_out, and_5_out, and_6_out, and_7_out, and_8_out, and_9_out,
       and_10_out, and_11_out, and_12_out, and_13_out, and_14_out, and_15_out, and_16_out, and_17_out,
       and_18_out, and_19_out, and_20_out, and_21_out, and_22_out, and_23_out, and_24_out, and_25_out,
       and_26_out, and_27_out, and_28_out, and_29_out, and_30_out, and_31_out, and_32_out, and_33_out,
       and_34_out, and_35_out, not_1_out, not_2_out, not_3_out, not_4_out, not_5_out, not_6_out, not_7_out,
       not_8_out, not_9_out, not_10_out, not_11_out, not_12_out, not_13_out, not_14_out, not_15_out,
       not_16_out, not_17_out, not_18_out, not_19_out, not_20_out, not_21_out, not_22_out, not_23_out,
       not_24_out, not_25_out, not_26_out, not_27_out, not_28_out, not_29_out, not_30_out, not_31_out,
       not_32_out, not_33_out, not_34_out, not_35_out, not_36_out, not_37_out, not_38_out, not_39_out,
       not_40_out, not_41_out, not_42_out, not_43_out;

  not not_1 (not_1_out, d2);
  and and_1 (and_1_out, not_1_out, not_2_out);
  not not_2 (not_2_out, d0);
  not not_3 (not_3_out, d3);
  and and_2 (and_2_out, not_3_out, d1);
  not not_4 (not_4_out, d3);
  and and_3 (and_3_out, not_4_out, d2, d0);
  and and_4 (and_4_out, d2, d1);
  and and_5 (and_5_out, d3, not_5_out, not_6_out);
  not not_5 (not_5_out, d2);
  not not_6 (not_6_out, d1);
  and and_6 (and_6_out, d3, not_7_out);
  not not_7 (not_7_out, d0);
  not not_8 (not_8_out, d3);
  and and_7 (and_7_out, not_8_out, not_9_out);
  not not_9 (not_9_out, d2);
  not not_10 (not_10_out, d3);
  not not_11 (not_11_out, d1);
  and and_8 (and_8_out, not_10_out, not_11_out, not_12_out);
  not not_12 (not_12_out, d0);
  not not_13 (not_13_out, d2);
  and and_9 (and_9_out, not_13_out, not_14_out);
  not not_14 (not_14_out, d0);
  not not_15 (not_15_out, d3);
  and and_10 (and_10_out, not_15_out, d1, d0);
  and and_11 (and_11_out, d3, not_16_out, d0);
  not not_16 (not_16_out, d1);
  not not_17 (not_17_out, d3);
  and and_12 (and_12_out, not_17_out, not_18_out);
  not not_18 (not_18_out, d1);
  not not_19 (not_19_out, d3);
  and and_13 (and_13_out, not_19_out, d0);
  not not_20 (not_20_out, d1);
  and and_14 (and_14_out, not_20_out, d0);
  not not_21 (not_21_out, d3);
  and and_15 (and_15_out, not_21_out, d2);
  and and_16 (and_16_out, d3, not_22_out);
  not not_22 (not_22_out, d2);
  not not_23 (not_23_out, d3);
  not not_24 (not_24_out, d2);
  and and_17 (and_17_out, not_23_out, not_24_out, not_25_out);
  not not_25 (not_25_out, d0);
  not not_26 (not_26_out, d2);
  and and_18 (and_18_out, not_26_out, d1, d0);
  not not_27 (not_27_out, d1);
  and and_19 (and_19_out, d2, not_27_out, d0);
  and and_20 (and_20_out, d2, d1, not_28_out);
  not not_28 (not_28_out, d0);
  and and_21 (and_21_out, d3, not_29_out);
  not not_29 (not_29_out, d1);
  not not_30 (not_30_out, d2);
  and and_22 (and_22_out, not_30_out, not_31_out);
  not not_31 (not_31_out, d0);
  and and_23 (and_23_out, d1, not_32_out);
  not not_32 (not_32_out, d0);
  and and_24 (and_24_out, d3, d1);
  and and_25 (and_25_out, d3, d2);
  not not_33 (not_33_out, d1);
  and and_26 (and_26_out, not_33_out, not_34_out);
  not not_34 (not_34_out, d0);
  not not_35 (not_35_out, d3);
  and and_27 (and_27_out, not_35_out, d2, not_36_out);
  not not_36 (not_36_out, d1);
  and and_28 (and_28_out, d2, not_37_out);
  not not_37 (not_37_out, d0);
  and and_29 (and_29_out, d3, not_38_out);
  not not_38 (not_38_out, d2);
  and and_30 (and_30_out, d3, d1);
  not not_39 (not_39_out, d2);
  and and_31 (and_31_out, not_39_out, d1);
  and and_32 (and_32_out, d1, not_40_out);
  not not_40 (not_40_out, d0);
  not not_41 (not_41_out, d3);
  and and_33 (and_33_out, not_41_out, d2, not_42_out);
  not not_42 (not_42_out, d1);
  and and_34 (and_34_out, d3, not_43_out);
  not not_43 (not_43_out, d2);
  and and_35 (and_35_out, d3, d0);
  or or_1 (s1, and_7_out, and_8_out, and_9_out, and_10_out, and_11_out);
  or or_2 (s2, and_12_out, and_13_out, and_14_out, and_15_out, and_16_out);
  or or_3 (s3, and_17_out, and_18_out, and_19_out, and_20_out, and_21_out);
  or or_4 (s4, and_22_out, and_23_out, and_24_out, and_25_out);
  or or_5 (s5, and_26_out, and_27_out, and_28_out, and_29_out, and_30_out);
  or or_6 (s6, and_31_out, and_32_out, and_33_out, and_34_out, and_35_out);
  or or_7 (s0, and_1_out, and_2_out, and_3_out, and_4_out, and_5_out, and_6_out);
endmodule

module \硬布线控制器_CU  (
  input  z,
  input  [5:0] op,
  input  [5:0] func,
  output RStoPC,
  output TargettoPC,
  output MemtoREG,
  output Branch,
  output nWriteMem,
  output [3:0] ALUOP,
  output ShamttoA,
  output Lui,
  output ImmtoB,
  output SignExtend,
  output nWriteReg,
  output PCtoR31,
  output RegDst,
  output Halt,
  output [1:0] Mode
);

  wire \指令译码器_1_iadd , \指令译码器_1_iaddi , \指令译码器_1_iand , \指令译码器_1_iandi , \指令译码器_1_ibeq , \指令译码器_1_ibne ,
       \指令译码器_1_ij , \指令译码器_1_ijal , \指令译码器_1_ijr , \指令译码器_1_ilbu , \指令译码器_1_ilhu , \指令译码器_1_ilui ,
       \指令译码器_1_ilw , \指令译码器_1_ior , \指令译码器_1_iori , \指令译码器_1_isb , \指令译码器_1_ish , \指令译码器_1_isll ,
       \指令译码器_1_islt , \指令译码器_1_isra , \指令译码器_1_isrl , \指令译码器_1_isub , \指令译码器_1_isw , \指令译码器_1_ixor ,
       \指令译码器_1_r_type , \指令译码器_1_syscall ;

  \指令译码器  \u_指令译码器_1  (
    .op(op), .func(func), .iADD(\指令译码器_1_iadd ), .iSUB(\指令译码器_1_isub ), .iAND(\指令译码器_1_iand ),
    .iOR(\指令译码器_1_ior ), .iXOR(\指令译码器_1_ixor ), .iSLT(\指令译码器_1_islt ), .iSLL(\指令译码器_1_isll ),
    .iSRL(\指令译码器_1_isrl ), .iJR(\指令译码器_1_ijr ), .SYSCALL(\指令译码器_1_syscall ), .R_Type(\指令译码器_1_r_type ),
    .iLW(\指令译码器_1_ilw ), .iLHU(\指令译码器_1_ilhu ), .iLBU(\指令译码器_1_ilbu ), .iSW(\指令译码器_1_isw ),
    .iSH(\指令译码器_1_ish ), .iSB(\指令译码器_1_isb ), .iADDi(\指令译码器_1_iaddi ), .iANDi(\指令译码器_1_iandi ),
    .iORi(\指令译码器_1_iori ), .iLUi(\指令译码器_1_ilui ), .iBEQ(\指令译码器_1_ibeq ), .iBNE(\指令译码器_1_ibne ),
    .iJ(\指令译码器_1_ij ), .iJAL(\指令译码器_1_ijal ), .iSRA(\指令译码器_1_isra ));
  \微命令产生电路  \u_微命令产生电路_1  (
    .Z(z), .iADD(\指令译码器_1_iadd ), .iSUB(\指令译码器_1_isub ), .iAND(\指令译码器_1_iand ), .iOR(\指令译码器_1_ior ),
    .iXOR(\指令译码器_1_ixor ), .iSLT(\指令译码器_1_islt ), .iSLL(\指令译码器_1_isll ), .iSRL(\指令译码器_1_isrl ),
    .iSRA(\指令译码器_1_isra ), .iJR(\指令译码器_1_ijr ), .SYSCALL(\指令译码器_1_syscall ), .R_Type(\指令译码器_1_r_type ),
    .iLW(\指令译码器_1_ilw ), .iLHU(\指令译码器_1_ilhu ), .iLBU(\指令译码器_1_ilbu ), .iSW(\指令译码器_1_isw ),
    .iSH(\指令译码器_1_ish ), .iSB(\指令译码器_1_isb ), .iADDi(\指令译码器_1_iaddi ), .iANDi(\指令译码器_1_iandi ),
    .iORi(\指令译码器_1_iori ), .iLUi(\指令译码器_1_ilui ), .iBEQ(\指令译码器_1_ibeq ), .iBNE(\指令译码器_1_ibne ),
    .iJ(\指令译码器_1_ij ), .iJAL(\指令译码器_1_ijal ), .RStoPC(RStoPC), .TargettoPC(TargettoPC), .MemtoReg(MemtoREG),
    .Branch(Branch), .nWriteMem(nWriteMem), .ALUOP(ALUOP), .ShamttoA(ShamttoA), .Lui(Lui), .ImmtoB(ImmtoB),
    .Signextend(SignExtend), .nWriteReg(nWriteReg), .PCtoR31(PCtoR31), .RegDst(RegDst), .Halt(Halt),
    .Mode(Mode));

  // Other names for the same wires on the sheet: nWritMem = nWriteMem; TargertoPC = TargettoPC

  // Notes on the sheet:
  //   输入管脚
  //   输出管脚
  //   以上管脚名称及位置均不要移动，利用下方的隧道信号用画电路图方式设计MIPS32控制器指令译码器逻辑
  //   逻辑功能：调用指令译码器和微命令产生电路设计支持10条指令的MIPS32CPU控制器
  //   10条指令：add、sll、syscall、lw、sw、sb、addi、beq、j、jal
endmodule

module \微命令产生电路  (
  input  Z,
  input  iADD,
  input  iSUB,
  input  iAND,
  input  iOR,
  input  iXOR,
  input  iSLT,
  input  iSLL,
  input  iSRL,
  input  iSRA,
  input  iJR,
  input  SYSCALL,
  input  R_Type,
  input  iLW,
  input  iLHU,
  input  iLBU,
  input  iSW,
  input  iSH,
  input  iSB,
  input  iADDi,
  input  iANDi,
  input  iORi,
  input  iLUi,
  input  iBEQ,
  input  iBNE,
  input  iJ,
  input  iJAL,
  output RStoPC,
  output TargettoPC,
  output MemtoReg,
  output Branch,
  output nWriteMem,
  output [3:0] ALUOP,
  output ShamttoA,
  output Lui,
  output ImmtoB,
  output Signextend,
  output nWriteReg,
  output PCtoR31,
  output RegDst,
  output Halt,
  output [1:0] Mode
);

  wire and_1_out, and_2_out, and_3_out, not_1_out, not_2_out, not_3_out;

  not not_1 (not_1_out, iJR);
  and and_1 (and_1_out, Z, iBEQ);
  not not_2 (not_2_out, Z);
  and and_2 (and_2_out, not_2_out, iBNE);
  and and_3 (and_3_out, R_Type, not_3_out);
  not not_3 (not_3_out, iJR);
  or or_1 (TargettoPC, iJ, iJAL);
  or or_2 (MemtoReg, iLBU, iLW);
  or or_3 (Branch, and_1_out, and_2_out);
  and and_4 (nWriteMem, ~iSB, ~iSW);  // AND_Gate
  or or_4 (ALUOP[3], iSLT, iXOR, iOR, iORi);
  or or_5 (ALUOP[2], iAND, iSUB, iADD, iSB, iLBU, iANDi, iADDi, iSW, iLW);
  or or_6 (ALUOP[1], iSRL, iSLT, iAND, iSUB, iANDi);
  or or_7 (ALUOP[0], iSLT, iXOR, iAND, iADD, iSB, iLBU, iANDi, iADDi, iSW, iLW);
  or or_8 (ShamttoA, iSRL, iSLL);
  or or_9 (ImmtoB, iSB, iLBU, iLW, iSW, iADDi, iANDi, iORi, iLUi);
  or or_10 (Signextend, iSB, iLBU, iLW, iSW, iADDi, iBEQ, iBNE);
  nor nor_1 (nWriteReg, and_3_out, iLBU, iLW, iADDi, iSLL, iANDi, iORi, iLUi, iJAL);
  and and_5 (RegDst, not_1_out, R_Type);
  or or_11 (Mode[0], iSB, iLBU);

  assign Halt = SYSCALL;
  assign Lui = iLUi;
  assign Mode[1] = 1'b0;
  assign PCtoR31 = iJAL;
  assign RStoPC = iJR;

  // Other names for the same wires on the sheet: ALUOP_0 = ALUOP[0]; ALUOP_1 = ALUOP[1]; ALUOP_2 = ALUOP[2];
  //   ALUOP_3 = ALUOP[3]; Mode_0 = Mode[0]; TargertoPC = TargettoPC

  // Notes on the sheet:
  //   0标志位
  //   I、J类指令
  //   逻辑功能：根据指令译码器的译码结果，采用硬布线方式生成指令系统10条指令中的4条指令（sll、lw、sb、jal）所需的微命令
  //   输入管脚
  //   6条指令：add、sw、addi、beq、j、syscall已实现
  //   以上管脚名称及位置均不要移动，利用下方的隧道信号用画电路图方式设计MIPS32控制器微命令逻辑
  //   输出管脚
  //   R类指令
endmodule

module \指令译码器  (
  input  [5:0] op,
  input  [5:0] func,
  output iADD,
  output iSUB,
  output iAND,
  output iOR,
  output iXOR,
  output iSLT,
  output iSLL,
  output iSRL,
  output iSRA,
  output iJR,
  output SYSCALL,
  output R_Type,
  output iLW,
  output iLHU,
  output iLBU,
  output iSW,
  output iSH,
  output iSB,
  output iADDi,
  output iANDi,
  output iORi,
  output iLUi,
  output iBEQ,
  output iBNE,
  output iJ,
  output iJAL
);

  wire not_1_out, not_2_out, not_3_out, not_4_out, not_5_out, not_6_out, not_7_out, not_8_out, not_9_out,
       not_10_out, not_11_out, not_12_out;

  not not_1 (not_1_out, op[5]);
  not not_2 (not_2_out, op[4]);
  not not_3 (not_3_out, op[3]);
  not not_4 (not_4_out, op[2]);
  not not_5 (not_5_out, op[1]);
  not not_6 (not_6_out, op[0]);
  and and_1 (R_Type, not_1_out, not_2_out, not_3_out, not_4_out, not_5_out, not_6_out);
  not not_7 (not_7_out, func[5]);
  not not_8 (not_8_out, func[4]);
  not not_9 (not_9_out, func[3]);
  not not_10 (not_10_out, func[2]);
  not not_11 (not_11_out, func[1]);
  not not_12 (not_12_out, func[0]);
  and and_2 (iLW, op[5], not_2_out, not_3_out, not_4_out, op[1], op[0]);
  and and_3 (iADD, func[5], not_8_out, not_9_out, R_Type, not_10_out, not_11_out, not_12_out);
  and and_4 (iSW, op[5], not_2_out, op[3], not_4_out, op[1], op[0]);
  and and_5 (iSUB, func[5], not_8_out, not_9_out, R_Type, not_10_out, func[1], not_12_out);
  and and_6 (iADDi, not_1_out, not_2_out, op[3], not_4_out, not_5_out, not_6_out);
  and and_7 (iAND, func[5], not_8_out, not_9_out, R_Type, func[2], not_11_out, not_12_out);
  and and_8 (iANDi, not_1_out, not_2_out, op[3], op[2], not_5_out, not_6_out);
  and and_9 (iOR, func[5], not_8_out, not_9_out, R_Type, func[2], not_11_out, func[0]);
  and and_10 (iORi, not_1_out, not_2_out, op[3], op[2], not_5_out, op[0]);
  and and_11 (iXOR, func[5], not_8_out, not_9_out, R_Type, func[2], func[1], not_12_out);
  and and_12 (iLUi, not_1_out, not_2_out, op[3], op[2], op[1], op[0]);
  and and_13 (iSLT, func[5], not_8_out, func[3], R_Type, not_10_out, func[1], not_12_out);
  and and_14 (iBEQ, not_1_out, not_2_out, not_3_out, op[2], not_5_out, not_6_out);
  and and_15 (iSLL, not_7_out, not_8_out, not_9_out, R_Type, not_10_out, not_11_out, not_12_out);
  and and_16 (iBNE, not_1_out, not_2_out, not_3_out, op[2], not_5_out, op[0]);
  and and_17 (iSRL, not_7_out, not_8_out, not_9_out, R_Type, not_10_out, func[1], not_12_out);
  and and_18 (iJ, not_1_out, not_2_out, not_3_out, not_4_out, op[1], not_6_out);
  and and_19 (iSRA, not_7_out, not_8_out, not_9_out, R_Type, not_10_out, func[1], func[0]);
  and and_20 (iJAL, not_1_out, not_2_out, not_3_out, not_4_out, op[1], op[0]);
  and and_21 (iJR, not_7_out, not_8_out, func[3], R_Type, not_10_out, not_11_out, not_12_out);
  and and_22 (iLBU, op[5], not_2_out, not_3_out, op[2], not_5_out, not_6_out);
  and and_23 (SYSCALL, R_Type, not_7_out, not_8_out, func[3], func[2], not_11_out, not_12_out);
  and and_24 (iSB, op[5], not_2_out, op[3], not_4_out, not_5_out, not_6_out);
  and and_25 (iLHU, op[5], not_2_out, not_3_out, op[2], not_5_out, op[0]);
  and and_26 (iSH, op[5], not_2_out, op[3], not_4_out, not_5_out, op[0]);

  // Notes on the sheet:
  //   指令操作码输入管脚
  //   R类指令
  //   以上管脚名称及位置均不要移动，利用下方的隧道信号用画电路图方式设计MIPS32控制器指令译码器逻辑
  //   I、J类指令译码器
  //   R类指令译码器
  //   逻辑功能：根据输入指令的OP码及Function码，采用硬布线方式生成指令系统11条指令中的4条指令（sll、lw、sb、jal）所需的指令译码器
  //   6条指令：add、syscall、sw、addi、beq、j已实现
  //   译码输出管脚
  //   I类指令
  //   J类指令
endmodule
