// Logisim project Memory.circ as structural Verilog: 4 circuits, main circuit BitExtension256K×8bit
// 256K×8bit
module BitExtension256K_8bit (
  input  [17:0] Addr,
  input  [7:0] Din,
  input  CSn,
  input  RWn,
  input  CLK,
  output [7:0] Dout
);

  wire not_1_out;

  not not_1 (not_1_out, RWn);
  RAM #(.addrWidth(18), .dataWidth(1), .bus("separate"), .Select("low")) ram_1 (
    .addr(Addr), .din(Din[0]), .data(Dout[0]), .str(not_1_out), .sel(CSn), .clk(CLK));  // open: ld, clr
  RAM #(.addrWidth(18), .dataWidth(1), .bus("separate"), .Select("low")) ram_2 (
    .addr(Addr), .din(Din[1]), .data(Dout[1]), .str(not_1_out), .sel(CSn), .clk(CLK));  // open: ld, clr
  RAM #(.addrWidth(18), .dataWidth(1), .bus("separate"), .Select("low")) ram_3 (
    .addr(Addr), .din(Din[2]), .data(Dout[2]), .str(not_1_out), .sel(CSn), .clk(CLK));  // open: ld, clr
  RAM #(.addrWidth(18), .dataWidth(1), .bus("separate"), .Select("low")) ram_4 (
    .addr(Addr), .din(Din[3]), .data(Dout[3]), .str(not_1_out), .sel(CSn), .clk(CLK));  // open: ld, clr
  RAM #(.addrWidth(18), .dataWidth(1), .bus("separate"), .Select("low")) ram_5 (
    .addr(Addr), .din(Din[4]), .data(Dout[4]), .str(not_1_out), .sel(CSn), .clk(CLK));  // open: ld, clr
  RAM #(.addrWidth(18), .dataWidth(1), .bus("separate"), .Select("low")) ram_6 (
    .addr(Addr), .din(Din[5]), .data(Dout[5]), .str(not_1_out), .sel(CSn), .clk(CLK));  // open: ld, clr
  RAM #(.addrWidth(18), .dataWidth(1), .bus("separate"), .Select("low")) ram_7 (
    .addr(Addr), .din(Din[6]), .data(Dout[6]), .str(not_1_out), .sel(CSn), .clk(CLK));  // open: ld, clr
  RAM #(.addrWidth(18), .dataWidth(1), .bus("separate"), .Select("low")) ram_8 (
    .addr(Addr), .din(Din[7]), .data(Dout[7]), .str(not_1_out), .sel(CSn), .clk(CLK));  // open: ld, clr

  // Notes on the sheet:
  //   输入管脚
  //   功能说明：利用256K×1bit的RAM存储器，通过位扩展构成256K×8bit的存储器
  //   以上管脚名称及位置均不要移动，利用下方的隧道信号用画电路图的方式设计256K×8bit的存储器
  //   输出管脚
endmodule

// 2M×8bit
module WordExtension2M_8bit (
  input  [20:0] Addr,
  input  [7:0] Din,
  input  MREQn,
  input  RWn,
  input  CLK,
  output [7:0] Dout
);

  wire decoder_1_out0, decoder_1_out1, decoder_1_out2, decoder_1_out3, decoder_1_out4, decoder_1_out5,
       decoder_1_out6, decoder_1_out7, not_1_out, not_2_out, not_3_out, not_4_out, not_5_out, not_6_out,
       not_7_out, not_8_out, not_9_out;

  Decoder #(.select(3), .tristate("false"), .disabled(0), .enable("true")) decoder_1 (
    .out0(decoder_1_out0), .out1(decoder_1_out1), .out2(decoder_1_out2), .out3(decoder_1_out3),
    .out4(decoder_1_out4), .out5(decoder_1_out5), .out6(decoder_1_out6), .out7(decoder_1_out7),
    .sel(Addr[20:18]), .en(not_1_out));
  not not_1 (not_1_out, MREQn);
  not not_2 (not_2_out, decoder_1_out0);
  not not_3 (not_3_out, decoder_1_out1);
  not not_4 (not_4_out, decoder_1_out2);
  not not_5 (not_5_out, decoder_1_out3);
  not not_6 (not_6_out, decoder_1_out4);
  not not_7 (not_7_out, decoder_1_out5);
  not not_8 (not_8_out, decoder_1_out6);
  not not_9 (not_9_out, decoder_1_out7);
  BitExtension256K_8bit bitextension256k_8bit_1 (
    .Addr(Addr[17:0]), .Din(Din), .CSn(not_2_out), .RWn(RWn), .CLK(CLK), .Dout(Dout));
  BitExtension256K_8bit bitextension256k_8bit_2 (
    .Addr(Addr[17:0]), .Din(Din), .CSn(not_3_out), .RWn(RWn), .CLK(CLK), .Dout(Dout));
  BitExtension256K_8bit bitextension256k_8bit_3 (
    .Addr(Addr[17:0]), .Din(Din), .CSn(not_4_out), .RWn(RWn), .CLK(CLK), .Dout(Dout));
  BitExtension256K_8bit bitextension256k_8bit_4 (
    .Addr(Addr[17:0]), .Din(Din), .CSn(not_5_out), .RWn(RWn), .CLK(CLK), .Dout(Dout));
  BitExtension256K_8bit bitextension256k_8bit_5 (
    .Addr(Addr[17:0]), .Din(Din), .CSn(not_6_out), .RWn(RWn), .CLK(CLK), .Dout(Dout));
  BitExtension256K_8bit bitextension256k_8bit_6 (
    .Addr(Addr[17:0]), .Din(Din), .CSn(not_7_out), .RWn(RWn), .CLK(CLK), .Dout(Dout));
  BitExtension256K_8bit bitextension256k_8bit_7 (
    .Addr(Addr[17:0]), .Din(Din), .CSn(not_8_out), .RWn(RWn), .CLK(CLK), .Dout(Dout));
  BitExtension256K_8bit bitextension256k_8bit_8 (
    .Addr(Addr[17:0]), .Din(Din), .CSn(not_9_out), .RWn(RWn), .CLK(CLK), .Dout(Dout));

  // Notes on the sheet:
  //   输入管脚
  //   功能说明：利用256K×8bit的RAM存储器，通过字扩展构成2M×8bit的存储器
  //   以上管脚名称及位置均不要移动，利用下方的隧道信号用画电路图的方式设计2M×8bit的存储器
  //   输出管脚
endmodule

// 2M×32bit
module WordBitExtension2M_32bit (
  input  [20:0] Addr,
  input  [31:0] Din,
  input  MREQn,
  input  RWn,
  input  CLK,
  output [31:0] Dout
);

  wire decoder_1_out0, decoder_1_out1, decoder_1_out2, decoder_1_out3, decoder_1_out4, decoder_1_out5,
       decoder_1_out6, decoder_1_out7, not_1_out, not_2_out, not_3_out, not_4_out, not_5_out, not_6_out,
       not_7_out, not_8_out, not_9_out;

  not not_1 (not_1_out, MREQn);
  not not_2 (not_2_out, decoder_1_out0);
  not not_3 (not_3_out, decoder_1_out1);
  not not_4 (not_4_out, decoder_1_out2);
  not not_5 (not_5_out, decoder_1_out3);
  not not_6 (not_6_out, decoder_1_out4);
  not not_7 (not_7_out, decoder_1_out5);
  not not_8 (not_8_out, decoder_1_out6);
  not not_9 (not_9_out, decoder_1_out7);
  Decoder #(.select(3), .tristate("false"), .disabled(0), .enable("true")) decoder_1 (
    .out0(decoder_1_out0), .out1(decoder_1_out1), .out2(decoder_1_out2), .out3(decoder_1_out3),
    .out4(decoder_1_out4), .out5(decoder_1_out5), .out6(decoder_1_out6), .out7(decoder_1_out7),
    .sel(Addr[20:18]), .en(not_1_out));
  BitExtension256K_8bit bitextension256k_8bit_1 (
    .Addr(Addr[17:0]), .Din(Din[7:0]), .CSn(not_2_out), .RWn(RWn), .CLK(CLK), .Dout(Dout[7:0]));
  BitExtension256K_8bit bitextension256k_8bit_2 (
    .Addr(Addr[17:0]), .Din(Din[15:8]), .CSn(not_2_out), .RWn(RWn), .CLK(CLK), .Dout(Dout[15:8]));
  BitExtension256K_8bit bitextension256k_8bit_3 (
    .Addr(Addr[17:0]), .Din(Din[23:16]), .CSn(not_2_out), .RWn(RWn), .CLK(CLK), .Dout(Dout[23:16]));
  BitExtension256K_8bit bitextension256k_8bit_4 (
    .Addr(Addr[17:0]), .Din(Din[31:24]), .CSn(not_2_out), .RWn(RWn), .CLK(CLK), .Dout(Dout[31:24]));
  BitExtension256K_8bit bitextension256k_8bit_5 (
    .Addr(Addr[17:0]), .Din(Din[7:0]), .CSn(not_3_out), .RWn(RWn), .CLK(CLK), .Dout(Dout[7:0]));
  BitExtension256K_8bit bitextension256k_8bit_6 (
    .Addr(Addr[17:0]), .Din(Din[15:8]), .CSn(not_3_out), .RWn(RWn), .CLK(CLK), .Dout(Dout[15:8]));
  BitExtension256K_8bit bitextension256k_8bit_7 (
    .Addr(Addr[17:0]), .Din(Din[23:16]), .CSn(not_3_out), .RWn(RWn), .CLK(CLK), .Dout(Dout[23:16]));
  BitExtension256K_8bit bitextension256k_8bit_8 (
    .Addr(Addr[17:0]), .Din(Din[31:24]), .CSn(not_3_out), .RWn(RWn), .CLK(CLK), .Dout(Dout[31:24]));
  BitExtension256K_8bit bitextension256k_8bit_9 (
    .Addr(Addr[17:0]), .Din(Din[7:0]), .CSn(not_4_out), .RWn(RWn), .CLK(CLK), .Dout(Dout[7:0]));
  BitExtension256K_8bit bitextension256k_8bit_10 (
    .Addr(Addr[17:0]), .Din(Din[15:8]), .CSn(not_4_out), .RWn(RWn), .CLK(CLK), .Dout(Dout[15:8]));
  BitExtension256K_8bit bitextension256k_8bit_11 (
    .Addr(Addr[17:0]), .Din(Din[23:16]), .CSn(not_4_out), .RWn(RWn), .CLK(CLK), .Dout(Dout[23:16]));
  BitExtension256K_8bit bitextension256k_8bit_12 (
    .Addr(Addr[17:0]), .Din(Din[31:24]), .CSn(not_4_out), .RWn(RWn), .CLK(CLK), .Dout(Dout[31:24]));
  BitExtension256K_8bit bitextension256k_8bit_13 (
    .Addr(Addr[17:0]), .Din(Din[7:0]), .CSn(not_5_out), .RWn(RWn), .CLK(CLK), .Dout(Dout[7:0]));
  BitExtension256K_8bit bitextension256k_8bit_14 (
    .Addr(Addr[17:0]), .Din(Din[15:8]), .CSn(not_5_out), .RWn(RWn), .CLK(CLK), .Dout(Dout[15:8]));
  BitExtension256K_8bit bitextension256k_8bit_15 (
    .Addr(Addr[17:0]), .Din(Din[23:16]), .CSn(not_5_out), .RWn(RWn), .CLK(CLK), .Dout(Dout[23:16]));
  BitExtension256K_8bit bitextension256k_8bit_16 (
    .Addr(Addr[17:0]), .Din(Din[31:24]), .CSn(not_5_out), .RWn(RWn), .CLK(CLK), .Dout(Dout[31:24]));
  BitExtension256K_8bit bitextension256k_8bit_17 (
    .Addr(Addr[17:0]), .Din(Din[7:0]), .CSn(not_6_out), .RWn(RWn), .CLK(CLK), .Dout(Dout[7:0]));
  BitExtension256K_8bit bitextension256k_8bit_18 (
    .Addr(Addr[17:0]), .Din(Din[15:8]), .CSn(not_6_out), .RWn(RWn), .CLK(CLK), .Dout(Dout[15:8]));
  BitExtension256K_8bit bitextension256k_8bit_19 (
    .Addr(Addr[17:0]), .Din(Din[23:16]), .CSn(not_6_out), .RWn(RWn), .CLK(CLK), .Dout(Dout[23:16]));
  BitExtension256K_8bit bitextension256k_8bit_20 (
    .Addr(Addr[17:0]), .Din(Din[31:24]), .CSn(not_6_out), .RWn(RWn), .CLK(CLK), .Dout(Dout[31:24]));
  BitExtension256K_8bit bitextension256k_8bit_21 (
    .Addr(Addr[17:0]), .Din(Din[7:0]), .CSn(not_7_out), .RWn(RWn), .CLK(CLK), .Dout(Dout[7:0]));
  BitExtension256K_8bit bitextension256k_8bit_22 (
    .Addr(Addr[17:0]), .Din(Din[15:8]), .CSn(not_7_out), .RWn(RWn), .CLK(CLK), .Dout(Dout[15:8]));
  BitExtension256K_8bit bitextension256k_8bit_23 (
    .Addr(Addr[17:0]), .Din(Din[23:16]), .CSn(not_7_out), .RWn(RWn), .CLK(CLK), .Dout(Dout[23:16]));
  BitExtension256K_8bit bitextension256k_8bit_24 (
    .Addr(Addr[17:0]), .Din(Din[31:24]), .CSn(not_7_out), .RWn(RWn), .CLK(CLK), .Dout(Dout[31:24]));
  BitExtension256K_8bit bitextension256k_8bit_25 (
    .Addr(Addr[17:0]), .Din(Din[7:0]), .CSn(not_8_out), .RWn(RWn), .CLK(CLK), .Dout(Dout[7:0]));
  BitExtension256K_8bit bitextension256k_8bit_26 (
    .Addr(Addr[17:0]), .Din(Din[15:8]), .CSn(not_8_out), .RWn(RWn), .CLK(CLK), .Dout(Dout[15:8]));
  BitExtension256K_8bit bitextension256k_8bit_27 (
    .Addr(Addr[17:0]), .Din(Din[23:16]), .CSn(not_8_out), .RWn(RWn), .CLK(CLK), .Dout(Dout[23:16]));
  BitExtension256K_8bit bitextension256k_8bit_28 (
    .Addr(Addr[17:0]), .Din(Din[31:24]), .CSn(not_8_out), .RWn(RWn), .CLK(CLK), .Dout(Dout[31:24]));
  BitExtension256K_8bit bitextension256k_8bit_29 (
    .Addr(Addr[17:0]), .Din(Din[7:0]), .CSn(not_9_out), .RWn(RWn), .CLK(CLK), .Dout(Dout[7:0]));
  BitExtension256K_8bit bitextension256k_8bit_30 (
    .Addr(Addr[17:0]), .Din(Din[15:8]), .CSn(not_9_out), .RWn(RWn), .CLK(CLK), .Dout(Dout[15:8]));
  BitExtension256K_8bit bitextension256k_8bit_31 (
    .Addr(Addr[17:0]), .Din(Din[23:16]), .CSn(not_9_out), .RWn(RWn), .CLK(CLK), .Dout(Dout[23:16]));
  BitExtension256K_8bit bitextension256k_8bit_32 (
    .Addr(Addr[17:0]), .Din(Din[31:24]), .CSn(not_9_out), .RWn(RWn), .CLK(CLK), .Dout(Dout[31:24]));

  // Notes on the sheet:
  //   输入管脚
  //   功能说明：利用256K×8bit的RAM存储器，通过字位扩展构成2M×32bit的存储器
  //   以上管脚名称及位置均不要移动，利用下方的隧道信号用画电路图的方式设计2M×32bit的存储器
  //   输出管脚
endmodule

// RISC-RAM
module RISC_RAM2M_32bit (
  input  [1:0] Mode,
  input  [22:0] Addr,
  input  [31:0] Din,
  input  RWn,
  input  CLK,
  output [31:0] Dout
);

  wire and_1_out, and_2_out, CS0n, CS1n, CS2n, CS3n, decoder_2_out0, decoder_2_out1, decoder_2_out2,
       decoder_2_out3, \半字访问 , \字节访问 , \字访问 ;
  wire [7:0] Dout0, Dout1, Dout2, Dout3, multiplexer_2_out;
  wire [15:0] multiplexer_3_out;
  wire [31:0] Data;

  WordExtension2M_8bit wordextension2m_8bit_1 (
    .Dout(Dout0), .Addr(Addr[22:2]), .Din(Data[7:0]), .MREQn(CS0n), .RWn(RWn), .CLK(CLK));
  WordExtension2M_8bit wordextension2m_8bit_2 (
    .Dout(Dout1), .Addr(Addr[22:2]), .Din(Data[15:8]), .MREQn(CS1n), .RWn(RWn), .CLK(CLK));
  WordExtension2M_8bit wordextension2m_8bit_3 (
    .Dout(Dout2), .Addr(Addr[22:2]), .Din(Data[23:16]), .MREQn(CS2n), .RWn(RWn), .CLK(CLK));
  WordExtension2M_8bit wordextension2m_8bit_4 (
    .Dout(Dout3), .Addr(Addr[22:2]), .Din(Data[31:24]), .MREQn(CS3n), .RWn(RWn), .CLK(CLK));
  // Probe on Dout0
  // Probe on Dout1
  // Probe on Dout2
  // Probe on Dout3
  Multiplexer #(.select(2), .width(32), .disabled("Z"), .enable("false")) multiplexer_1 (
    .in0(Din), .in1({Din[7:0], Din[7:0], Din[7:0], Din[7:0]}), .in2({Din[15:0], Din[15:0]}), .in3(Din),
    .out(Data), .sel(Mode));
  Decoder #(.select(2), .tristate("false"), .disabled("Z"), .enable("false")) decoder_1 (
    .out0(\字访问 ), .out1(\字节访问 ), .out2(\半字访问 ), .sel(Mode));  // open: out3
  Decoder #(.select(2), .tristate("false"), .disabled("Z"), .enable("false")) decoder_2 (
    .out0(decoder_2_out0), .out1(decoder_2_out1), .out2(decoder_2_out2), .out3(decoder_2_out3),
    .sel(Addr[1:0]));
  and and_1 (and_1_out, \半字访问 , ~Addr[1]);  // AND_Gate
  and and_2 (and_2_out, \半字访问 , Addr[1]);
  Multiplexer #(.select(2), .width(8), .disabled("Z"), .enable("false")) multiplexer_2 (
    .in0(Dout0), .in1(Dout1), .in2(Dout2), .in3(Dout3), .out(multiplexer_2_out), .sel(Addr[1:0]));
  Multiplexer #(.select(1), .width(16), .disabled("Z"), .enable("false")) multiplexer_3 (
    .in0({Dout1, Dout0}), .in1({Dout3, Dout2}), .out(multiplexer_3_out), .sel(Addr[1]));
  nor nor_1 (CS0n, \字访问 , and_1_out, decoder_2_out0);
  nor nor_2 (CS1n, \字访问 , and_1_out, decoder_2_out1);
  nor nor_3 (CS2n, \字访问 , and_2_out, decoder_2_out2);
  nor nor_4 (CS3n, \字访问 , and_2_out, decoder_2_out3);
  Multiplexer #(.select(2), .width(32), .disabled("Z"), .enable("false")) multiplexer_4 (
    .in0({Dout3, Dout2, Dout1, Dout0}), .in1({{24{1'b0}}, multiplexer_2_out}),
    .in2({{16{1'b0}}, multiplexer_3_out}), .in3({Dout3, Dout2, Dout1, Dout0}), .out(Dout), .sel(Mode));

  // Other names for the same wires on the sheet: Din0[7:0] = Din[7:0]; Din1[7:0] = Din[15:8]; Din2[7:0] = Din[23:16];
  //   Din3[7:0] = Din[31:24]; 字节地址[22:0] = Addr; 字节选择[1:0] = Addr[1:0]; 半节选择 = Addr[1]; 字地址[20:0] = Addr[22:2]

  // Notes on the sheet:
  //   存储体
  //   输入数据
  //   输入管脚
  //   功能说明：利用2M×8bit的RAM存储器，通过位扩展构成2M×32bit (8MByte)的RISC-RAM存储器
  //   以上管脚名称及位置均不要移动，利用下方的隧道信号用画电路图的方式设计2M×32bit的RISC-RAM存储器
  //   片选逻辑（低电平有效）
  //   Mode=00为字访问，CS0n,CS1n,CS2n,CS3n均有效（低电平有效）
  //   Mode=01为字节访问，Addr的低2位字节选择为00时CS0n有效（低电平有效），访问0号字节
  //   Mode=01为字节访问，Addr的低2位字节选择为01时CS1n有效（低电平有效），访问1号字节
  //   Mode=01为字节访问，Addr的低2位字节选择为10时CS2n有效（低电平有效），访问2号字节
  //   Mode=01为字节访问，Addr的低2位字节选择为11时CS3n有效（低电平有效），访问3号字节
  //   输出数据
  //   Mode=10为半字访问，Addr的次低位半字选择为0时CS1n,CS0n有效（低电平有效），访问低半字
  //   Mode=10为半字访问，Addr的次低位半字选择为1时CS3n,CS2n有效（低电平有效），访问高半字
  //   输出管脚
endmodule
