// Logisim project RISCREG.circ as structural Verilog: 1 circuit, main circuit RISCRegfile
module RISCRegfile (
  input  [4:0] RAddr1,
  input  [4:0] RAddr2,
  input  [31:0] WData,
  input  [4:0] WAddr,
  input  nWE,
  input  CLK,
  input  nrst,
  output [31:0] RData1,
  output [31:0] RData2
);

  wire D0A, D0B, D0C, D0D, D0E, D0F, D01, D1A, D1B, D1C, D1D, D1E, D1F, D02, D03, D04, D05, D06, D07, D08,
       D09, D10, D11, D12, D13, D14, D15, D16, D17, D18, D19, not_1_out, not_2_out;
  wire [31:0] Dout0A, Dout0B, Dout0C, Dout0D, Dout0E, Dout0F, Dout01, Dout1A, Dout1B, Dout1C, Dout1D, Dout1E,
       Dout1F, Dout02, Dout03, Dout04, Dout05, Dout06, Dout07, Dout08, Dout09, Dout10, Dout11, Dout12,
       Dout13, Dout14, Dout15, Dout16, Dout17, Dout18, Dout19;

  not not_1 (not_1_out, nWE);
  Decoder #(.select(5), .tristate("false"), .disabled(0), .enable("true")) decoder_1 (
    .out1(D01), .out2(D02), .out3(D03), .out4(D04), .out5(D05), .out6(D06), .out7(D07), .out8(D08),
    .out9(D09), .out10(D0A), .out11(D0B), .out12(D0C), .out13(D0D), .out14(D0E), .out15(D0F), .out16(D10),
    .out17(D11), .out18(D12), .out19(D13), .out20(D14), .out21(D15), .out22(D16), .out23(D17), .out24(D18),
    .out25(D19), .out26(D1A), .out27(D1B), .out28(D1C), .out29(D1D), .out30(D1E), .out31(D1F), .sel(WAddr),
    .en(not_1_out));  // open: out0
  not not_2 (not_2_out, nrst);
  Register #(.width(32), .trigger("rising"), .Select("low")) register_1 (
    .D(WData), .en(D01), .Q(Dout01), .clk(CLK), .clr(not_2_out));
  Register #(.width(32), .trigger("rising"), .Select("low")) register_2 (
    .D(WData), .en(D02), .Q(Dout02), .clk(CLK), .clr(not_2_out));
  Register #(.width(32), .trigger("rising"), .Select("low")) register_3 (
    .D(WData), .en(D03), .Q(Dout03), .clk(CLK), .clr(not_2_out));
  Register #(.width(32), .trigger("rising"), .Select("low")) register_4 (
    .D(WData), .en(D04), .Q(Dout04), .clk(CLK), .clr(not_2_out));
  Register #(.width(32), .trigger("rising"), .Select("low")) register_5 (
    .D(WData), .en(D05), .Q(Dout05), .clk(CLK), .clr(not_2_out));
  Register #(.width(32), .trigger("rising"), .Select("low")) register_6 (
    .D(WData), .en(D06), .Q(Dout06), .clk(CLK), .clr(not_2_out));
  Register #(.width(32), .trigger("rising"), .Select("low")) register_7 (
    .D(WData), .en(D07), .Q(Dout07), .clk(CLK), .clr(not_2_out));
  Register #(.width(32), .trigger("rising"), .Select("low")) register_8 (
    .D(WData), .en(D08), .Q(Dout08), .clk(CLK), .clr(not_2_out));
  Register #(.width(32), .trigger("rising"), .Select("low")) register_9 (
    .D(WData), .en(D09), .Q(Dout09), .clk(CLK), .clr(not_2_out));
  Register #(.width(32), .trigger("rising"), .Select("low")) register_10 (
    .D(WData), .en(D0A), .Q(Dout0A), .clk(CLK), .clr(not_2_out));
  Register #(.width(32), .trigger("rising"), .Select("low")) register_11 (
    .D(WData), .en(D0B), .Q(Dout0B), .clk(CLK), .clr(not_2_out));
  Register #(.width(32), .trigger("rising"), .Select("low")) register_12 (
    .D(WData), .en(D0C), .Q(Dout0C), .clk(CLK), .clr(not_2_out));
  Register #(.width(32), .trigger("rising"), .Select("low")) register_13 (
    .D(WData), .en(D0D), .Q(Dout0D), .clk(CLK), .clr(not_2_out));
  Register #(.width(32), .trigger("rising"), .Select("low")) register_14 (
    .D(WData), .en(D0E), .Q(Dout0E), .clk(CLK), .clr(not_2_out));
  Register #(.width(32), .trigger("rising"), .Select("low")) register_15 (
    .D(WData), .en(D0F), .Q(Dout0F), .clk(CLK), .clr(not_2_out));
  Register #(.width(32), .trigger("rising"), .Select("low")) register_16 (
    .D(WData), .en(D10), .Q(Dout10), .clk(CLK), .clr(not_2_out));
  Register #(.width(32), .trigger("rising"), .Select("low")) register_17 (
    .D(WData), .en(D11), .Q(Dout11), .clk(CLK), .clr(not_2_out));
  Register #(.width(32), .trigger("rising"), .Select("low")) register_18 (
    .D(WData), .en(D12), .Q(Dout12), .clk(CLK), .clr(not_2_out));
  Register #(.width(32), .trigger("rising"), .Select("low")) register_19 (
    .D(WData), .en(D13), .Q(Dout13), .clk(CLK), .clr(not_2_out));
  Register #(.width(32), .trigger("rising"), .Select("low")) register_20 (
    .D(WData), .en(D14), .Q(Dout14), .clk(CLK), .clr(not_2_out));
  Register #(.width(32), .trigger("rising"), .Select("low")) register_21 (
    .D(WData), .en(D15), .Q(Dout15), .clk(CLK), .clr(not_2_out));
  Register #(.width(32), .trigger("rising"), .Select("low")) register_22 (
    .D(WData), .en(D16), .Q(Dout16), .clk(CLK), .clr(not_2_out));
  Register #(.width(32), .trigger("rising"), .Select("low")) register_23 (
    .D(WData), .en(D17), .Q(Dout17), .clk(CLK), .clr(not_2_out));
  Register #(.width(32), .trigger("rising"), .Select("low")) register_24 (
    .D(WData), .en(D18), .Q(Dout18), .clk(CLK), .clr(not_2_out));
  Register #(.width(32), .trigger("rising"), .Select("low")) register_25 (
    .D(WData), .en(D19), .Q(Dout19), .clk(CLK), .clr(not_2_out));
  Register #(.width(32), .trigger("rising"), .Select("low")) register_26 (
    .D(WData), .en(D1A), .Q(Dout1A), .clk(CLK), .clr(not_2_out));
  Register #(.width(32), .trigger("rising"), .Select("low")) register_27 (
    .D(WData), .en(D1B), .Q(Dout1B), .clk(CLK), .clr(not_2_out));
  Register #(.width(32), .trigger("rising"), .Select("low")) register_28 (
    .D(WData), .en(D1C), .Q(Dout1C), .clk(CLK), .clr(not_2_out));
  Register #(.width(32), .trigger("rising"), .Select("low")) register_29 (
    .D(WData), .en(D1D), .Q(Dout1D), .clk(CLK), .clr(not_2_out));
  Register #(.width(32), .trigger("rising"), .Select("low")) register_30 (
    .D(WData), .en(D1E), .Q(Dout1E), .clk(CLK), .clr(not_2_out));
  Register #(.width(32), .trigger("rising"), .Select("low")) register_31 (
    .D(WData), .en(D1F), .Q(Dout1F), .clk(CLK), .clr(not_2_out));
  Multiplexer #(.select(5), .width(32), .disabled("Z"), .enable("false")) multiplexer_1 (
    .in0({32{1'b0}}), .in1(Dout01), .in2(Dout02), .in3(Dout03), .in4(Dout04), .in5(Dout05), .in6(Dout06),
    .in7(Dout07), .in8(Dout08), .in9(Dout09), .in10(Dout0A), .in11(Dout0B), .in12(Dout0C), .in13(Dout0D),
    .in14(Dout0E), .in15(Dout0F), .in16(Dout10), .in17(Dout11), .in18(Dout12), .in19(Dout13), .in20(Dout14),
    .in21(Dout15), .in22(Dout16), .in23(Dout17), .in24(Dout18), .in25(Dout19), .in26(Dout1A), .in27(Dout1B),
    .in28(Dout1C), .in29(Dout1D), .in30(Dout1E), .in31(Dout1F), .out(RData1), .sel(RAddr1));
  Multiplexer #(.select(5), .width(32), .disabled("Z"), .enable("false")) multiplexer_2 (
    .in0({32{1'b0}}), .in1(Dout01), .in2(Dout02), .in3(Dout03), .in4(Dout04), .in5(Dout05), .in6(Dout06),
    .in7(Dout07), .in8(Dout08), .in9(Dout09), .in10(Dout0A), .in11(Dout0B), .in12(Dout0C), .in13(Dout0D),
    .in14(Dout0E), .in15(Dout0F), .in16(Dout10), .in17(Dout11), .in18(Dout12), .in19(Dout13), .in20(Dout14),
    .in21(Dout15), .in22(Dout16), .in23(Dout17), .in24(Dout18), .in25(Dout19), .in26(Dout1A), .in27(Dout1B),
    .in28(Dout1C), .in29(Dout1D), .in30(Dout1E), .in31(Dout1F), .out(RData2), .sel(RAddr2));

  // Notes on the sheet:
  //   输入引脚
  //   请补齐下面寄存器文件电路，仔细测试电路，核对功能无误后提交EDUCoder平台进行自动检测评分
  //   输出引脚
endmodule
